// Logisim project console.circ as structural Verilog: 2 circuits, main circuit main
module main (
);

  wire clock_1_out, L, M, R, S, tunnel, tunnel_t;
  wire [31:0] menu_1_out_8, menu_1_out_9, menu_1_out_10, menu_1_out_11, menu_1_out_12, menu_1_out_13,
       menu_1_out_14, menu_1_out_15, menu_1_out_16, menu_1_out_17, menu_1_out_18, menu_1_out_19,
       menu_1_out_20, menu_1_out_21, menu_1_out_22, menu_1_out_23, menu_1_out_24, menu_1_out_25,
       menu_1_out_26, menu_1_out_27, menu_1_out_28, menu_1_out_29, menu_1_out_30, menu_1_out_31,
       menu_1_out_32, menu_1_out_33, menu_1_out_34, menu_1_out_35, menu_1_out_36, menu_1_out_37,
       menu_1_out_38, menu_1_out_39, menu_1_out_40, menu_1_out_41, menu_1_out_42, menu_1_out_43,
       menu_1_out_44, menu_1_out_45, menu_1_out_46, menu_1_out_47, menu_1_out_48, menu_1_out_49,
       menu_1_out_50, menu_1_out_51, menu_1_out_52, menu_1_out_53, menu_1_out_54, menu_1_out_55;

  Clock clock_1 (.out(clock_1_out));
  DotMatrix #(.inputtype("row"), .matrixcols(32), .matrixrows(24)) dotmatrix_1 (
    .row0(menu_1_out_8), .row1(menu_1_out_9), .row2(menu_1_out_10), .row3(menu_1_out_11),
    .row4(menu_1_out_12), .row5(menu_1_out_13), .row6(menu_1_out_14), .row7(menu_1_out_15),
    .row8(menu_1_out_16), .row9(menu_1_out_17), .row10(menu_1_out_18), .row11(menu_1_out_19),
    .row12(menu_1_out_20), .row13(menu_1_out_21), .row14(menu_1_out_22), .row15(menu_1_out_23),
    .row16(menu_1_out_24), .row17(menu_1_out_25), .row18(menu_1_out_26), .row19(menu_1_out_27),
    .row20(menu_1_out_28), .row21(menu_1_out_29), .row22(menu_1_out_30), .row23(menu_1_out_31));
  menu menu_1 (
    .tick(clock_1_out), .start(S), .menu(M), .left(tunnel), .right(tunnel_t), .lup(L), .rup(R),
    .out_8(menu_1_out_8), .out_9(menu_1_out_9), .out_10(menu_1_out_10), .out_11(menu_1_out_11),
    .out_12(menu_1_out_12), .out_13(menu_1_out_13), .out_14(menu_1_out_14), .out_15(menu_1_out_15),
    .out_16(menu_1_out_16), .out_17(menu_1_out_17), .out_18(menu_1_out_18), .out_19(menu_1_out_19),
    .out_20(menu_1_out_20), .out_21(menu_1_out_21), .out_22(menu_1_out_22), .out_23(menu_1_out_23),
    .out_24(menu_1_out_24), .out_25(menu_1_out_25), .out_26(menu_1_out_26), .out_27(menu_1_out_27),
    .out_28(menu_1_out_28), .out_29(menu_1_out_29), .out_30(menu_1_out_30), .out_31(menu_1_out_31),
    .out_32(menu_1_out_32), .out_33(menu_1_out_33), .out_34(menu_1_out_34), .out_35(menu_1_out_35),
    .out_36(menu_1_out_36), .out_37(menu_1_out_37), .out_38(menu_1_out_38), .out_39(menu_1_out_39),
    .out_40(menu_1_out_40), .out_41(menu_1_out_41), .out_42(menu_1_out_42), .out_43(menu_1_out_43),
    .out_44(menu_1_out_44), .out_45(menu_1_out_45), .out_46(menu_1_out_46), .out_47(menu_1_out_47),
    .out_48(menu_1_out_48), .out_49(menu_1_out_49), .out_50(menu_1_out_50), .out_51(menu_1_out_51),
    .out_52(menu_1_out_52), .out_53(menu_1_out_53), .out_54(menu_1_out_54), .out_55(menu_1_out_55));
  DotMatrix #(.inputtype("row"), .matrixcols(32), .matrixrows(24)) dotmatrix_2 (
    .row0(menu_1_out_32), .row1(menu_1_out_33), .row2(menu_1_out_34), .row3(menu_1_out_35),
    .row4(menu_1_out_36), .row5(menu_1_out_37), .row6(menu_1_out_38), .row7(menu_1_out_39),
    .row8(menu_1_out_40), .row9(menu_1_out_41), .row10(menu_1_out_42), .row11(menu_1_out_43),
    .row12(menu_1_out_44), .row13(menu_1_out_45), .row14(menu_1_out_46), .row15(menu_1_out_47),
    .row16(menu_1_out_48), .row17(menu_1_out_49), .row18(menu_1_out_50), .row19(menu_1_out_51),
    .row20(menu_1_out_52), .row21(menu_1_out_53), .row22(menu_1_out_54), .row23(menu_1_out_55));
  Button u_M (.out(M));
  Button u_L (.out(L));
  Button button (.out(tunnel));
  Button u_S (.out(S));
  Button u_R (.out(R));
  Button button_2 (.out(tunnel_t));
endmodule

module menu (
  input  tick,
  input  start,
  input  menu,
  input  left,
  input  right,
  input  lup,
  input  rup,
  output [31:0] out_8,
  output [31:0] out_9,
  output [31:0] out_10,
  output [31:0] out_11,
  output [31:0] out_12,
  output [31:0] out_13,
  output [31:0] out_14,
  output [31:0] out_15,
  output [31:0] out_16,
  output [31:0] out_17,
  output [31:0] out_18,
  output [31:0] out_19,
  output [31:0] out_20,
  output [31:0] out_21,
  output [31:0] out_22,
  output [31:0] out_23,
  output [31:0] out_24,
  output [31:0] out_25,
  output [31:0] out_26,
  output [31:0] out_27,
  output [31:0] out_28,
  output [31:0] out_29,
  output [31:0] out_30,
  output [31:0] out_31,
  output [31:0] out_32,
  output [31:0] out_33,
  output [31:0] out_34,
  output [31:0] out_35,
  output [31:0] out_36,
  output [31:0] out_37,
  output [31:0] out_38,
  output [31:0] out_39,
  output [31:0] out_40,
  output [31:0] out_41,
  output [31:0] out_42,
  output [31:0] out_43,
  output [31:0] out_44,
  output [31:0] out_45,
  output [31:0] out_46,
  output [31:0] out_47,
  output [31:0] out_48,
  output [31:0] out_49,
  output [31:0] out_50,
  output [31:0] out_51,
  output [31:0] out_52,
  output [31:0] out_53,
  output [31:0] out_54,
  output [31:0] out_55
);

  wire and_1_out, and_2_out, and_3_out, and_4_out, and_5_out, comparator_1_eq, comparator_2_eq,
       comparator_3_eq, comparator_4_eq, or_1_out, or_2_out;
  wire [1:0] multiplexer_1_out, multiplexer_2_out, multiplexer_3_out, multiplexer_4_out, state;
  wire [31:0] screen_united_1_out_4, screen_united_1_out_5, screen_united_1_out_6, screen_united_1_out_7,
       screen_united_1_out_8, screen_united_1_out_9, screen_united_1_out_10, screen_united_1_out_11,
       screen_united_1_out_12, screen_united_1_out_13, screen_united_1_out_14, screen_united_1_out_15,
       screen_united_1_out_16, screen_united_1_out_17, screen_united_1_out_18, screen_united_1_out_19,
       screen_united_1_out_20, screen_united_1_out_21, screen_united_1_out_22, screen_united_1_out_23,
       screen_united_1_out_24, screen_united_1_out_25, screen_united_1_out_26, screen_united_1_out_27,
       screen_united_1_out_28, screen_united_1_out_29, screen_united_1_out_30, screen_united_1_out_31,
       screen_united_1_out_32, screen_united_1_out_33, screen_united_1_out_34, screen_united_1_out_35,
       screen_united_1_out_36, screen_united_1_out_37, screen_united_1_out_38, screen_united_1_out_39,
       screen_united_1_out_40, screen_united_1_out_41, screen_united_1_out_42, screen_united_1_out_43,
       screen_united_1_out_44, screen_united_1_out_45, screen_united_1_out_46, screen_united_1_out_47,
       screen_united_1_out_48, screen_united_1_out_49, screen_united_1_out_50, screen_united_1_out_51,
       tetris_1_r1, tetris_1_r2, tetris_1_r3, tetris_1_r4, tetris_1_r5, tetris_1_r6, tetris_1_r7,
       tetris_1_r8, tetris_1_r9, tetris_1_r10, tetris_1_r11, tetris_1_r12, tetris_1_r13, tetris_1_r14,
       tetris_1_r15, tetris_1_r16, tetris_1_r17, tetris_1_r18, tetris_1_r19, tetris_1_r20, tetris_1_r21,
       tetris_1_r22, tetris_1_r23, tetris_1_r24, tetris_1_r25, tetris_1_r26, tetris_1_r27, tetris_1_r28,
       tetris_1_r29, tetris_1_r30, tetris_1_r31, tetris_1_r32, tetris_1_r33, tetris_1_r34, tetris_1_r35,
       tetris_1_r36, tetris_1_r37, tetris_1_r38, tetris_1_r39, tetris_1_r40, tetris_1_r41, tetris_1_r42,
       tetris_1_r43, tetris_1_r44, tetris_1_r45, tetris_1_r46, tetris_1_r47, tetris_1_r48;

  Comparator #(.width(2)) comparator_1 (.a(2'b00), .b(state), .eq(comparator_1_eq));  // open: gt, lt
  Comparator #(.width(2)) comparator_2 (.a(2'b01), .b(state), .eq(comparator_2_eq));  // open: gt, lt
  Comparator #(.width(2)) comparator_3 (.a(2'b00), .b(state), .eq(comparator_3_eq));  // open: gt, lt
  Comparator #(.width(2)) comparator_4 (.a(2'b01), .b(state), .eq(comparator_4_eq));  // open: gt, lt
  or or_1 (or_1_out, right, left, start);
  and and_1 (and_1_out, comparator_1_eq, right);
  and and_2 (and_2_out, comparator_2_eq, left);
  Multiplexer #(.width(2), .enable("false")) multiplexer_1 (
    .in0(multiplexer_2_out), .in1(2'b10), .out(multiplexer_1_out), .sel(and_3_out));
  and and_3 (and_3_out, comparator_3_eq, start);
  Multiplexer #(.width(2), .enable("false")) multiplexer_2 (
    .in1(2'b11), .out(multiplexer_2_out), .sel(and_4_out));  // open: in0
  and and_4 (and_4_out, comparator_4_eq, start);
  Register #(.width(2)) register_1 (.D(multiplexer_3_out), .Q(state), .clk(and_5_out), .clr(menu));  // open: en
  and and_5 (and_5_out, or_1_out, tick);
  Multiplexer #(.width(2), .enable("false")) multiplexer_3 (
    .in0(multiplexer_4_out), .in1(2'b01), .out(multiplexer_3_out), .sel(and_1_out));
  Multiplexer #(.width(2), .enable("false")) multiplexer_4 (
    .in0(multiplexer_1_out), .in1(2'b00), .out(multiplexer_4_out), .sel(and_2_out));
  or or_2 (or_2_out, left, right, lup, rup);
  tetris tetris_1 (
    .Start(start), .ML(left), .MR(right), .TL(lup), .TR(rup), .R1(tetris_1_r1), .R2(tetris_1_r2),
    .R3(tetris_1_r3), .R4(tetris_1_r4), .R5(tetris_1_r5), .R6(tetris_1_r6), .R7(tetris_1_r7),
    .R8(tetris_1_r8), .R9(tetris_1_r9), .R10(tetris_1_r10), .R11(tetris_1_r11), .R12(tetris_1_r12),
    .R13(tetris_1_r13), .R14(tetris_1_r14), .R15(tetris_1_r15), .R16(tetris_1_r16), .R17(tetris_1_r17),
    .R18(tetris_1_r18), .R19(tetris_1_r19), .R20(tetris_1_r20), .R21(tetris_1_r21), .R22(tetris_1_r22),
    .R23(tetris_1_r23), .R24(tetris_1_r24), .R25(tetris_1_r25), .R26(tetris_1_r26), .R27(tetris_1_r27),
    .R28(tetris_1_r28), .R29(tetris_1_r29), .R30(tetris_1_r30), .R31(tetris_1_r31), .R32(tetris_1_r32),
    .R33(tetris_1_r33), .R34(tetris_1_r34), .R35(tetris_1_r35), .R36(tetris_1_r36), .R37(tetris_1_r37),
    .R38(tetris_1_r38), .R39(tetris_1_r39), .R40(tetris_1_r40), .R41(tetris_1_r41), .R42(tetris_1_r42),
    .R43(tetris_1_r43), .R44(tetris_1_r44), .R45(tetris_1_r45), .R46(tetris_1_r46), .R47(tetris_1_r47),
    .R48(tetris_1_r48), .Clock(tick));
  Screen_United screen_united_1 (
    .jump(or_2_out), .reset(start), .clock(tick), .out_4(screen_united_1_out_4),
    .out_5(screen_united_1_out_5), .out_6(screen_united_1_out_6), .out_7(screen_united_1_out_7),
    .out_8(screen_united_1_out_8), .out_9(screen_united_1_out_9), .out_10(screen_united_1_out_10),
    .out_11(screen_united_1_out_11), .out_12(screen_united_1_out_12), .out_13(screen_united_1_out_13),
    .out_14(screen_united_1_out_14), .out_15(screen_united_1_out_15), .out_16(screen_united_1_out_16),
    .out_17(screen_united_1_out_17), .out_18(screen_united_1_out_18), .out_19(screen_united_1_out_19),
    .out_20(screen_united_1_out_20), .out_21(screen_united_1_out_21), .out_22(screen_united_1_out_22),
    .out_23(screen_united_1_out_23), .out_24(screen_united_1_out_24), .out_25(screen_united_1_out_25),
    .out_26(screen_united_1_out_26), .out_27(screen_united_1_out_27), .out_28(screen_united_1_out_28),
    .out_29(screen_united_1_out_29), .out_30(screen_united_1_out_30), .out_31(screen_united_1_out_31),
    .out_32(screen_united_1_out_32), .out_33(screen_united_1_out_33), .out_34(screen_united_1_out_34),
    .out_35(screen_united_1_out_35), .out_36(screen_united_1_out_36), .out_37(screen_united_1_out_37),
    .out_38(screen_united_1_out_38), .out_39(screen_united_1_out_39), .out_40(screen_united_1_out_40),
    .out_41(screen_united_1_out_41), .out_42(screen_united_1_out_42), .out_43(screen_united_1_out_43),
    .out_44(screen_united_1_out_44), .out_45(screen_united_1_out_45), .out_46(screen_united_1_out_46),
    .out_47(screen_united_1_out_47), .out_48(screen_united_1_out_48), .out_49(screen_united_1_out_49),
    .out_50(screen_united_1_out_50), .out_51(screen_united_1_out_51));
  Multiplexer #(.select(2), .width(32), .enable("false")) multiplexer_5 (
    .in0({32{1'b1}}), .in1({32{1'b0}}), .in2(tetris_1_r1), .in3(screen_united_1_out_4), .out(out_8),
    .sel(state));
  Multiplexer #(.select(2), .width(32), .enable("false")) multiplexer_6 (
    .in0({32{1'b1}}), .in1({32{1'b0}}), .in2(tetris_1_r2), .in3(screen_united_1_out_5), .out(out_9),
    .sel(state));
  Multiplexer #(.select(2), .width(32), .enable("false")) multiplexer_7 (
    .in0({32{1'b1}}), .in1({32{1'b0}}), .in2(tetris_1_r3), .in3(screen_united_1_out_6), .out(out_10),
    .sel(state));
  Multiplexer #(.select(2), .width(32), .enable("false")) multiplexer_8 (
    .in0(32'hfffe0fff), .in1(32'h1f000), .in2(tetris_1_r4), .in3(screen_united_1_out_7), .out(out_11),
    .sel(state));
  Multiplexer #(.select(2), .width(32), .enable("false")) multiplexer_9 (
    .in0(32'hffffbfff), .in1(32'h10000), .in2(tetris_1_r5), .in3(screen_united_1_out_8), .out(out_12),
    .sel(state));
  Multiplexer #(.select(2), .width(32), .enable("false")) multiplexer_10 (
    .in0(32'hffffbfff), .in1(32'h1c000), .in2(tetris_1_r6), .in3(screen_united_1_out_9), .out(out_13),
    .sel(state));
  Multiplexer #(.select(2), .width(32), .enable("false")) multiplexer_11 (
    .in0(32'hffffbfff), .in1(32'h10000), .in2(tetris_1_r7), .in3(screen_united_1_out_10), .out(out_14),
    .sel(state));
  Multiplexer #(.select(2), .width(32), .enable("false")) multiplexer_12 (
    .in0(32'hffffbfff), .in1(32'h10000), .in2(tetris_1_r8), .in3(screen_united_1_out_11), .out(out_15),
    .sel(state));
  Multiplexer #(.select(2), .width(32), .enable("false")) multiplexer_13 (
    .in0({32{1'b1}}), .in1({32{1'b0}}), .in2(tetris_1_r9), .in3(screen_united_1_out_12), .out(out_16),
    .sel(state));
  Multiplexer #(.select(2), .width(32), .enable("false")) multiplexer_14 (
    .in0({32{1'b1}}), .in1({32{1'b0}}), .in2(tetris_1_r10), .in3(screen_united_1_out_13), .out(out_17),
    .sel(state));
  Multiplexer #(.select(2), .width(32), .enable("false")) multiplexer_15 (
    .in0({32{1'b1}}), .in1({32{1'b0}}), .in2(tetris_1_r11), .in3(screen_united_1_out_14), .out(out_18),
    .sel(state));
  Multiplexer #(.select(2), .width(32), .enable("false")) multiplexer_16 (
    .in0({32{1'b1}}), .in1({32{1'b0}}), .in2(tetris_1_r12), .in3(screen_united_1_out_15), .out(out_19),
    .sel(state));
  Multiplexer #(.select(2), .width(32), .enable("false")) multiplexer_17 (
    .in0({32{1'b1}}), .in1({32{1'b0}}), .in2(tetris_1_r13), .in3(screen_united_1_out_16), .out(out_20),
    .sel(state));
  Multiplexer #(.select(2), .width(32), .enable("false")) multiplexer_18 (
    .in0({32{1'b1}}), .in1({32{1'b0}}), .in2(tetris_1_r14), .in3(screen_united_1_out_17), .out(out_21),
    .sel(state));
  Multiplexer #(.select(2), .width(32), .enable("false")) multiplexer_19 (
    .in0({32{1'b1}}), .in1({32{1'b0}}), .in2(tetris_1_r15), .in3(screen_united_1_out_18), .out(out_22),
    .sel(state));
  Multiplexer #(.select(2), .width(32), .enable("false")) multiplexer_20 (
    .in0({32{1'b1}}), .in1({32{1'b0}}), .in2(tetris_1_r16), .in3(screen_united_1_out_19), .out(out_23),
    .sel(state));
  Multiplexer #(.select(2), .width(32), .enable("false")) multiplexer_21 (
    .in0({32{1'b1}}), .in1({32{1'b0}}), .in2(tetris_1_r17), .in3(screen_united_1_out_20), .out(out_24),
    .sel(state));
  Multiplexer #(.select(2), .width(32), .enable("false")) multiplexer_22 (
    .in0({32{1'b1}}), .in1({32{1'b0}}), .in2(tetris_1_r18), .in3(screen_united_1_out_21), .out(out_25),
    .sel(state));
  Multiplexer #(.select(2), .width(32), .enable("false")) multiplexer_23 (
    .in0({32{1'b1}}), .in1({32{1'b0}}), .in2(tetris_1_r19), .in3(screen_united_1_out_22), .out(out_26),
    .sel(state));
  Multiplexer #(.select(2), .width(32), .enable("false")) multiplexer_24 (
    .in0({32{1'b1}}), .in1({32{1'b0}}), .in2(tetris_1_r20), .in3(screen_united_1_out_23), .out(out_27),
    .sel(state));
  Multiplexer #(.select(2), .width(32), .enable("false")) multiplexer_25 (
    .in0({32{1'b1}}), .in1({32{1'b0}}), .in2(tetris_1_r21), .in3(screen_united_1_out_24), .out(out_28),
    .sel(state));
  Multiplexer #(.select(2), .width(32), .enable("false")) multiplexer_26 (
    .in0({32{1'b1}}), .in1({32{1'b0}}), .in2(tetris_1_r22), .in3(screen_united_1_out_25), .out(out_29),
    .sel(state));
  Multiplexer #(.select(2), .width(32), .enable("false")) multiplexer_27 (
    .in0({32{1'b1}}), .in1({32{1'b0}}), .in2(tetris_1_r23), .in3(screen_united_1_out_26), .out(out_30),
    .sel(state));
  Multiplexer #(.select(2), .width(32), .enable("false")) multiplexer_28 (
    .in0({32{1'b1}}), .in1({32{1'b0}}), .in2(tetris_1_r24), .in3(screen_united_1_out_27), .out(out_31),
    .sel(state));
  Multiplexer #(.select(2), .width(32), .enable("false")) multiplexer_29 (
    .in0({32{1'b1}}), .in1({32{1'b0}}), .in2(tetris_1_r25), .in3(screen_united_1_out_28), .out(out_32),
    .sel(state));
  Multiplexer #(.select(2), .width(32), .enable("false")) multiplexer_30 (
    .in0({32{1'b1}}), .in1({32{1'b0}}), .in2(tetris_1_r26), .in3(screen_united_1_out_29), .out(out_33),
    .sel(state));
  Multiplexer #(.select(2), .width(32), .enable("false")) multiplexer_31 (
    .in0({32{1'b1}}), .in1({32{1'b0}}), .in2(tetris_1_r27), .in3(screen_united_1_out_30), .out(out_34),
    .sel(state));
  Multiplexer #(.select(2), .width(32), .enable("false")) multiplexer_32 (
    .in0({32{1'b1}}), .in1({32{1'b0}}), .in2(tetris_1_r28), .in3(screen_united_1_out_31), .out(out_35),
    .sel(state));
  Multiplexer #(.select(2), .width(32), .enable("false")) multiplexer_33 (
    .in0({32{1'b1}}), .in1({32{1'b0}}), .in2(tetris_1_r29), .in3(screen_united_1_out_32), .out(out_36),
    .sel(state));
  Multiplexer #(.select(2), .width(32), .enable("false")) multiplexer_34 (
    .in0({32{1'b1}}), .in1({32{1'b0}}), .in2(tetris_1_r30), .in3(screen_united_1_out_33), .out(out_37),
    .sel(state));
  Multiplexer #(.select(2), .width(32), .enable("false")) multiplexer_35 (
    .in0({32{1'b1}}), .in1({32{1'b0}}), .in2(tetris_1_r31), .in3(screen_united_1_out_34), .out(out_38),
    .sel(state));
  Multiplexer #(.select(2), .width(32), .enable("false")) multiplexer_36 (
    .in0({32{1'b1}}), .in1({32{1'b0}}), .in2(tetris_1_r32), .in3(screen_united_1_out_35), .out(out_39),
    .sel(state));
  Multiplexer #(.select(2), .width(32), .enable("false")) multiplexer_37 (
    .in0({32{1'b1}}), .in1({32{1'b0}}), .in2(tetris_1_r33), .in3(screen_united_1_out_36), .out(out_40),
    .sel(state));
  Multiplexer #(.select(2), .width(32), .enable("false")) multiplexer_38 (
    .in0({32{1'b1}}), .in1({32{1'b0}}), .in2(tetris_1_r34), .in3(screen_united_1_out_37), .out(out_41),
    .sel(state));
  Multiplexer #(.select(2), .width(32), .enable("false")) multiplexer_39 (
    .in0({32{1'b1}}), .in1({32{1'b0}}), .in2(tetris_1_r35), .in3(screen_united_1_out_38), .out(out_42),
    .sel(state));
  Multiplexer #(.select(2), .width(32), .enable("false")) multiplexer_40 (
    .in0({32{1'b1}}), .in1({32{1'b0}}), .in2(tetris_1_r36), .in3(screen_united_1_out_39), .out(out_43),
    .sel(state));
  Multiplexer #(.select(2), .width(32), .enable("false")) multiplexer_41 (
    .in0({32{1'b1}}), .in1({32{1'b0}}), .in2(tetris_1_r37), .in3(screen_united_1_out_40), .out(out_44),
    .sel(state));
  Multiplexer #(.select(2), .width(32), .enable("false")) multiplexer_42 (
    .in0({32{1'b1}}), .in1({32{1'b0}}), .in2(tetris_1_r38), .in3(screen_united_1_out_41), .out(out_45),
    .sel(state));
  Multiplexer #(.select(2), .width(32), .enable("false")) multiplexer_43 (
    .in0({32{1'b1}}), .in1({32{1'b0}}), .in2(tetris_1_r39), .in3(screen_united_1_out_42), .out(out_46),
    .sel(state));
  Multiplexer #(.select(2), .width(32), .enable("false")) multiplexer_44 (
    .in0({32{1'b1}}), .in1({32{1'b0}}), .in2(tetris_1_r40), .in3(screen_united_1_out_43), .out(out_47),
    .sel(state));
  Multiplexer #(.select(2), .width(32), .enable("false")) multiplexer_45 (
    .in0({32{1'b1}}), .in1({32{1'b0}}), .in2(tetris_1_r41), .in3(screen_united_1_out_44), .out(out_48),
    .sel(state));
  Multiplexer #(.select(2), .width(32), .enable("false")) multiplexer_46 (
    .in0({32{1'b1}}), .in1({32{1'b0}}), .in2(tetris_1_r42), .in3(screen_united_1_out_45), .out(out_49),
    .sel(state));
  Multiplexer #(.select(2), .width(32), .enable("false")) multiplexer_47 (
    .in0({32{1'b1}}), .in1({32{1'b0}}), .in2(tetris_1_r43), .in3(screen_united_1_out_46), .out(out_50),
    .sel(state));
  Multiplexer #(.select(2), .width(32), .enable("false")) multiplexer_48 (
    .in0({32{1'b1}}), .in1({32{1'b0}}), .in2(tetris_1_r44), .in3(screen_united_1_out_47), .out(out_51),
    .sel(state));
  Multiplexer #(.select(2), .width(32), .enable("false")) multiplexer_49 (
    .in0({32{1'b1}}), .in1({32{1'b0}}), .in2(tetris_1_r45), .in3(screen_united_1_out_48), .out(out_52),
    .sel(state));
  Multiplexer #(.select(2), .width(32), .enable("false")) multiplexer_50 (
    .in0({32{1'b1}}), .in1({32{1'b0}}), .in2(tetris_1_r46), .in3(screen_united_1_out_49), .out(out_53),
    .sel(state));
  Multiplexer #(.select(2), .width(32), .enable("false")) multiplexer_51 (
    .in0({32{1'b1}}), .in1({32{1'b0}}), .in2(tetris_1_r47), .in3(screen_united_1_out_50), .out(out_54),
    .sel(state));
  Multiplexer #(.select(2), .width(32), .enable("false")) multiplexer_52 (
    .in0({32{1'b1}}), .in1({32{1'b0}}), .in2(tetris_1_r48), .in3(screen_united_1_out_51), .out(out_55),
    .sel(state));
endmodule
