// Logisim project flappy_module.circ as structural Verilog: 6 circuits, main circuit Main_Module
module Main_Module (
);

  wire clock_1_out, jump_out, reset_out;
  wire [31:0] screen_united_1_out_4, screen_united_1_out_5, screen_united_1_out_6, screen_united_1_out_7,
       screen_united_1_out_8, screen_united_1_out_9, screen_united_1_out_10, screen_united_1_out_11,
       screen_united_1_out_12, screen_united_1_out_13, screen_united_1_out_14, screen_united_1_out_15,
       screen_united_1_out_16, screen_united_1_out_17, screen_united_1_out_18, screen_united_1_out_19,
       screen_united_1_out_20, screen_united_1_out_21, screen_united_1_out_22, screen_united_1_out_23,
       screen_united_1_out_24, screen_united_1_out_25, screen_united_1_out_26, screen_united_1_out_27,
       screen_united_1_out_28, screen_united_1_out_29, screen_united_1_out_30, screen_united_1_out_31,
       screen_united_1_out_32, screen_united_1_out_33, screen_united_1_out_34, screen_united_1_out_35,
       screen_united_1_out_36, screen_united_1_out_37, screen_united_1_out_38, screen_united_1_out_39,
       screen_united_1_out_40, screen_united_1_out_41, screen_united_1_out_42, screen_united_1_out_43,
       screen_united_1_out_44, screen_united_1_out_45, screen_united_1_out_46, screen_united_1_out_47,
       screen_united_1_out_48, screen_united_1_out_49, screen_united_1_out_50, screen_united_1_out_51;

  Button jump (.out(jump_out));
  Button reset (.out(reset_out));
  Clock clock_1 (.out(clock_1_out));
  Screen_United screen_united_1 (
    .jump(jump_out), .reset(reset_out), .clock(clock_1_out), .out_4(screen_united_1_out_4),
    .out_5(screen_united_1_out_5), .out_6(screen_united_1_out_6), .out_7(screen_united_1_out_7),
    .out_8(screen_united_1_out_8), .out_9(screen_united_1_out_9), .out_10(screen_united_1_out_10),
    .out_11(screen_united_1_out_11), .out_12(screen_united_1_out_12), .out_13(screen_united_1_out_13),
    .out_14(screen_united_1_out_14), .out_15(screen_united_1_out_15), .out_16(screen_united_1_out_16),
    .out_17(screen_united_1_out_17), .out_18(screen_united_1_out_18), .out_19(screen_united_1_out_19),
    .out_20(screen_united_1_out_20), .out_21(screen_united_1_out_21), .out_22(screen_united_1_out_22),
    .out_23(screen_united_1_out_23), .out_24(screen_united_1_out_24), .out_25(screen_united_1_out_25),
    .out_26(screen_united_1_out_26), .out_27(screen_united_1_out_27), .out_28(screen_united_1_out_28),
    .out_29(screen_united_1_out_29), .out_30(screen_united_1_out_30), .out_31(screen_united_1_out_31),
    .out_32(screen_united_1_out_32), .out_33(screen_united_1_out_33), .out_34(screen_united_1_out_34),
    .out_35(screen_united_1_out_35), .out_36(screen_united_1_out_36), .out_37(screen_united_1_out_37),
    .out_38(screen_united_1_out_38), .out_39(screen_united_1_out_39), .out_40(screen_united_1_out_40),
    .out_41(screen_united_1_out_41), .out_42(screen_united_1_out_42), .out_43(screen_united_1_out_43),
    .out_44(screen_united_1_out_44), .out_45(screen_united_1_out_45), .out_46(screen_united_1_out_46),
    .out_47(screen_united_1_out_47), .out_48(screen_united_1_out_48), .out_49(screen_united_1_out_49),
    .out_50(screen_united_1_out_50), .out_51(screen_united_1_out_51));
  DotMatrix #(.inputtype("row"), .matrixcols(32), .matrixrows(24)) dotmatrix_1 (
    .row0(screen_united_1_out_4), .row1(screen_united_1_out_5), .row2(screen_united_1_out_6),
    .row3(screen_united_1_out_7), .row4(screen_united_1_out_8), .row5(screen_united_1_out_9),
    .row6(screen_united_1_out_10), .row7(screen_united_1_out_11), .row8(screen_united_1_out_12),
    .row9(screen_united_1_out_13), .row10(screen_united_1_out_14), .row11(screen_united_1_out_15),
    .row12(screen_united_1_out_16), .row13(screen_united_1_out_17), .row14(screen_united_1_out_18),
    .row15(screen_united_1_out_19), .row16(screen_united_1_out_20), .row17(screen_united_1_out_21),
    .row18(screen_united_1_out_22), .row19(screen_united_1_out_23), .row20(screen_united_1_out_24),
    .row21(screen_united_1_out_25), .row22(screen_united_1_out_26), .row23(screen_united_1_out_27));
  DotMatrix #(.inputtype("row"), .matrixcols(32), .matrixrows(24)) dotmatrix_2 (
    .row0(screen_united_1_out_28), .row1(screen_united_1_out_29), .row2(screen_united_1_out_30),
    .row3(screen_united_1_out_31), .row4(screen_united_1_out_32), .row5(screen_united_1_out_33),
    .row6(screen_united_1_out_34), .row7(screen_united_1_out_35), .row8(screen_united_1_out_36),
    .row9(screen_united_1_out_37), .row10(screen_united_1_out_38), .row11(screen_united_1_out_39),
    .row12(screen_united_1_out_40), .row13(screen_united_1_out_41), .row14(screen_united_1_out_42),
    .row15(screen_united_1_out_43), .row16(screen_united_1_out_44), .row17(screen_united_1_out_45),
    .row18(screen_united_1_out_46), .row19(screen_united_1_out_47), .row20(screen_united_1_out_48),
    .row21(screen_united_1_out_49), .row22(screen_united_1_out_50), .row23(screen_united_1_out_51));

  // Notes on the sheet:
  //   Вывод процесса игры на матрицу 
endmodule

module Screen_United (
  input  jump,
  input  reset,
  input  clock,
  output [31:0] out_4,
  output [31:0] out_5,
  output [31:0] out_6,
  output [31:0] out_7,
  output [31:0] out_8,
  output [31:0] out_9,
  output [31:0] out_10,
  output [31:0] out_11,
  output [31:0] out_12,
  output [31:0] out_13,
  output [31:0] out_14,
  output [31:0] out_15,
  output [31:0] out_16,
  output [31:0] out_17,
  output [31:0] out_18,
  output [31:0] out_19,
  output [31:0] out_20,
  output [31:0] out_21,
  output [31:0] out_22,
  output [31:0] out_23,
  output [31:0] out_24,
  output [31:0] out_25,
  output [31:0] out_26,
  output [31:0] out_27,
  output [31:0] out_28,
  output [31:0] out_29,
  output [31:0] out_30,
  output [31:0] out_31,
  output [31:0] out_32,
  output [31:0] out_33,
  output [31:0] out_34,
  output [31:0] out_35,
  output [31:0] out_36,
  output [31:0] out_37,
  output [31:0] out_38,
  output [31:0] out_39,
  output [31:0] out_40,
  output [31:0] out_41,
  output [31:0] out_42,
  output [31:0] out_43,
  output [31:0] out_44,
  output [31:0] out_45,
  output [31:0] out_46,
  output [31:0] out_47,
  output [31:0] out_48,
  output [31:0] out_49,
  output [31:0] out_50,
  output [31:0] out_51
);

  wire loser, or_18_out;
  wire [31:0] a1, a2, a3, a4, a5, a6, a7, a8, a9, a10, a11, a12, a13, a14, a15, a16, a17, a18, a19, a20, a21,
       a22, a23, a24, and_1_out, and_2_out, and_3_out, and_4_out, and_5_out, and_6_out, and_7_out, and_8_out,
       and_9_out, and_10_out, and_11_out, and_12_out, and_13_out, and_14_out, and_15_out, and_16_out,
       and_17_out, and_18_out, and_19_out, and_20_out, and_21_out, and_22_out, and_23_out, and_24_out,
       or_13_out, \с1 , \с2 , \с3 , \с4 , \с5 , \с6 , \с7 , \с8 , \с9 , \с10 , \с11 , \с12 , \с13 , \с14 ,
       \с15 , \с16 , \с17 , \с18 , \с19 , \с20 , \с21 , \с22 , \с23 , \с24 ;

  assign out_28 = \с1  | a1;  // OR_Gate or_1, 32 bits wide
  assign out_29 = \с2  | a2;  // OR_Gate or_2, 32 bits wide
  assign out_30 = \с3  | a3;  // OR_Gate or_3, 32 bits wide
  assign out_31 = \с4  | a4;  // OR_Gate or_4, 32 bits wide
  assign and_1_out = \с1  & a1;  // AND_Gate and_1, 32 bits wide
  assign and_2_out = \с2  & a2;  // AND_Gate and_2, 32 bits wide
  assign and_3_out = \с3  & a3;  // AND_Gate and_3, 32 bits wide
  assign and_4_out = \с4  & a4;  // AND_Gate and_4, 32 bits wide
  assign and_5_out = \с5  & a5;  // AND_Gate and_5, 32 bits wide
  assign and_6_out = \с6  & a6;  // AND_Gate and_6, 32 bits wide
  assign and_7_out = \с7  & a7;  // AND_Gate and_7, 32 bits wide
  assign and_8_out = \с8  & a8;  // AND_Gate and_8, 32 bits wide
  assign and_9_out = \с9  & a9;  // AND_Gate and_9, 32 bits wide
  assign and_10_out = \с10  & a10;  // AND_Gate and_10, 32 bits wide
  assign and_11_out = \с11  & a11;  // AND_Gate and_11, 32 bits wide
  assign and_12_out = \с12  & a12;  // AND_Gate and_12, 32 bits wide
  assign and_13_out = \с13  & a13;  // AND_Gate and_13, 32 bits wide
  assign and_14_out = \с14  & a14;  // AND_Gate and_14, 32 bits wide
  assign and_15_out = \с15  & a15;  // AND_Gate and_15, 32 bits wide
  assign and_16_out = \с16  & a16;  // AND_Gate and_16, 32 bits wide
  assign and_17_out = \с17  & a17;  // AND_Gate and_17, 32 bits wide
  assign and_18_out = \с18  & a18;  // AND_Gate and_18, 32 bits wide
  assign and_19_out = \с19  & a19;  // AND_Gate and_19, 32 bits wide
  assign and_20_out = \с20  & a20;  // AND_Gate and_20, 32 bits wide
  assign and_21_out = \с21  & a21;  // AND_Gate and_21, 32 bits wide
  assign and_22_out = \с22  & a22;  // AND_Gate and_22, 32 bits wide
  assign and_23_out = \с23  & a23;  // AND_Gate and_23, 32 bits wide
  assign and_24_out = \с24  & a24;  // AND_Gate and_24, 32 bits wide
  assign out_32 = \с5  | a5;  // OR_Gate or_5, 32 bits wide
  assign out_33 = \с6  | a6;  // OR_Gate or_6, 32 bits wide
  assign out_34 = \с7  | a7;  // OR_Gate or_7, 32 bits wide
  assign out_35 = \с8  | a8;  // OR_Gate or_8, 32 bits wide
  assign out_36 = \с9  | a9;  // OR_Gate or_9, 32 bits wide
  assign out_37 = \с10  | a10;  // OR_Gate or_10, 32 bits wide
  assign out_38 = \с11  | a11;  // OR_Gate or_11, 32 bits wide
  assign out_39 = \с12  | a12;  // OR_Gate or_12, 32 bits wide
  assign or_13_out = and_1_out | and_2_out | and_3_out | and_4_out | and_5_out | and_6_out | and_7_out | and_8_out | and_9_out | and_10_out | and_11_out | and_12_out | and_13_out | and_14_out | and_15_out | and_16_out | and_17_out | and_18_out | and_19_out | and_20_out | and_21_out | and_22_out | and_23_out | and_24_out;  // OR_Gate or_13, 32 bits wide
  assign out_40 = \с13  | a13;  // OR_Gate or_14, 32 bits wide
  assign out_41 = \с14  | a14;  // OR_Gate or_15, 32 bits wide
  assign out_42 = \с15  | a15;  // OR_Gate or_16, 32 bits wide
  assign out_43 = \с16  | a16;  // OR_Gate or_17, 32 bits wide
  or or_18 (or_18_out, or_13_out[0], or_13_out[1], or_13_out[2], or_13_out[3], or_13_out[4], or_13_out[5], or_13_out[6], or_13_out[7], or_13_out[8], or_13_out[9], or_13_out[10], or_13_out[11], or_13_out[12], or_13_out[13], or_13_out[14], or_13_out[15], or_13_out[16], or_13_out[17], or_13_out[18], or_13_out[19], or_13_out[20], or_13_out[21], or_13_out[22], or_13_out[23], or_13_out[24], or_13_out[25], or_13_out[26], or_13_out[27], or_13_out[28], or_13_out[29], or_13_out[30], or_13_out[31]);
  assign out_44 = \с17  | a17;  // OR_Gate or_19, 32 bits wide
  assign out_45 = \с18  | a18;  // OR_Gate or_20, 32 bits wide
  assign out_46 = \с19  | a19;  // OR_Gate or_21, 32 bits wide
  assign out_47 = \с20  | a20;  // OR_Gate or_22, 32 bits wide
  S_R_Flip_Flop s_r_ff_1 (.S(or_18_out), .clk(clock), .R(reset), .Q(loser));  // open: Qn, preset, reset, en
  assign out_48 = \с21  | a21;  // OR_Gate or_23, 32 bits wide
  assign out_49 = \с22  | a22;  // OR_Gate or_24, 32 bits wide
  assign out_50 = \с23  | a23;  // OR_Gate or_25, 32 bits wide
  assign out_51 = \с24  | a24;  // OR_Gate or_26, 32 bits wide
  Over_or_Play over_or_play_1 (
    .out_3(out_4), .out_4(out_5), .out_5(out_6), .out_6(out_7), .out_7(out_8), .out_8(out_9), .out_9(out_10),
    .out_10(out_11), .out_11(out_12), .out_12(out_13), .out_13(out_14), .out_14(out_15), .out_15(out_16),
    .out_16(out_17), .out_17(out_18), .out_18(out_19), .out_19(out_20), .out_20(out_21), .out_21(out_22),
    .out_22(out_23), .out_23(out_24), .out_24(out_25), .out_25(out_26), .out_26(out_27), .out_27(\с1 ),
    .out_28(\с2 ), .out_29(\с3 ), .out_30(\с4 ), .out_31(\с5 ), .out_32(\с6 ), .out_33(\с7 ), .out_34(\с8 ),
    .out_35(\с9 ), .out_36(\с10 ), .out_37(\с11 ), .out_38(\с12 ), .out_39(\с13 ), .out_40(\с14 ),
    .out_41(\с15 ), .out_42(\с16 ), .out_43(\с17 ), .out_44(\с18 ), .out_45(\с19 ), .out_46(\с20 ),
    .out_47(\с21 ), .out_48(\с22 ), .out_49(\с23 ), .out_50(\с24 ), .loser(loser), .clock(clock));
  Fluppy fluppy_1 (
    .keyboard(jump), .clock(clock), .loser(loser), .out_5(a1), .out_6(a7), .out_7(a13), .out_8(a19),
    .out_9(a2), .out_10(a8), .out_11(a14), .out_12(a20), .out_13(a3), .out_14(a9), .out_15(a15),
    .out_16(a21), .out_17(a4), .out_18(a10), .out_19(a16), .out_20(a22), .out_21(a5), .out_22(a11),
    .out_23(a17), .out_24(a23), .out_25(a6), .out_26(a12), .out_27(a18), .out_28(a24), .reset(reset));

  // Other names for the same wires on the sheet: key = jump; res1[31:0] = out_28; res2[31:0] = out_29;
  //   res3[31:0] = out_30; res4[31:0] = out_31; res5[31:0] = out_32; res6[31:0] = out_33; res7[31:0] = out_34;
  //   res8[31:0] = out_35; res9[31:0] = out_36; res10[31:0] = out_37; res11[31:0] = out_38; res12[31:0] = out_39;
  //   res13[31:0] = out_40; res14[31:0] = out_41; res15[31:0] = out_42; res16[31:0] = out_43; res17[31:0] = out_44;
  //   res18[31:0] = out_45; res19[31:0] = out_46; res20[31:0] = out_47; res21[31:0] = out_48; res22[31:0] = out_49;
  //   res23[31:0] = out_50; res24[31:0] = out_51

  // Notes on the sheet:
  //   Объединение моделей (Птица & Столбы)
  //   Обработка коллизий
  //   Вывод на матрицу 
  //   Объединение экранов & Обработка коллизий
endmodule

module Fluppy (
  input  keyboard,
  input  clock,
  input  loser,
  input  reset,
  output [31:0] out_5,
  output [31:0] out_6,
  output [31:0] out_7,
  output [31:0] out_8,
  output [31:0] out_9,
  output [31:0] out_10,
  output [31:0] out_11,
  output [31:0] out_12,
  output [31:0] out_13,
  output [31:0] out_14,
  output [31:0] out_15,
  output [31:0] out_16,
  output [31:0] out_17,
  output [31:0] out_18,
  output [31:0] out_19,
  output [31:0] out_20,
  output [31:0] out_21,
  output [31:0] out_22,
  output [31:0] out_23,
  output [31:0] out_24,
  output [31:0] out_25,
  output [31:0] out_26,
  output [31:0] out_27,
  output [31:0] out_28
);

  wire _1, _1lol, _2, _3, _4, _5, _6, _7, _8, _9, _10, _11, _12, _13, _14, _15, _16, _17, _18, _19, _20, _21,
       _22, _23, _24, not_1_out, s_r_ff_1_q;
  wire [4:0] adder_1_out, and_17_out, bit_extender_17_out, multiplexer_1_out, register_1_q;
  wire [31:0] bit_extender_1_out, bit_extender_2_out, bit_extender_3_out, bit_extender_4_out,
       bit_extender_5_out, bit_extender_6_out, bit_extender_7_out, bit_extender_8_out, bit_extender_9_out,
       bit_extender_10_out, bit_extender_11_out, bit_extender_12_out, bit_extender_13_out,
       bit_extender_14_out, bit_extender_15_out, bit_extender_16_out, bit_extender_18_out,
       bit_extender_19_out, bit_extender_20_out, bit_extender_21_out, bit_extender_22_out,
       bit_extender_23_out, bit_extender_24_out, bit_extender_25_out;

  assign out_5 = 32'h10000000 & bit_extender_1_out;  // AND_Gate and_1, 32 bits wide
  assign bit_extender_1_out = {{31{_1lol}}, _1lol};  // Bit_Extender bit_extender_1
  assign out_9 = 32'h10000000 & bit_extender_2_out;  // AND_Gate and_2, 32 bits wide
  assign bit_extender_2_out = {{31{_2}}, _2};  // Bit_Extender bit_extender_2
  assign out_13 = 32'h10000000 & bit_extender_3_out;  // AND_Gate and_3, 32 bits wide
  assign bit_extender_3_out = {{31{_3}}, _3};  // Bit_Extender bit_extender_3
  assign out_17 = 32'h10000000 & bit_extender_4_out;  // AND_Gate and_4, 32 bits wide
  assign bit_extender_4_out = {{31{_4}}, _4};  // Bit_Extender bit_extender_4
  assign out_21 = 32'h10000000 & bit_extender_5_out;  // AND_Gate and_5, 32 bits wide
  assign bit_extender_5_out = {{31{_5}}, _5};  // Bit_Extender bit_extender_5
  assign out_25 = 32'h10000000 & bit_extender_6_out;  // AND_Gate and_6, 32 bits wide
  assign bit_extender_6_out = {{31{_6}}, _6};  // Bit_Extender bit_extender_6
  assign out_6 = 32'h10000000 & bit_extender_7_out;  // AND_Gate and_7, 32 bits wide
  assign bit_extender_7_out = {{31{_7}}, _7};  // Bit_Extender bit_extender_7
  assign out_10 = 32'h10000000 & bit_extender_8_out;  // AND_Gate and_8, 32 bits wide
  assign bit_extender_8_out = {{31{_8}}, _8};  // Bit_Extender bit_extender_8
  assign bit_extender_9_out = {{31{_9}}, _9};  // Bit_Extender bit_extender_9
  assign bit_extender_10_out = {{31{_10}}, _10};  // Bit_Extender bit_extender_10
  assign bit_extender_11_out = {{31{_11}}, _11};  // Bit_Extender bit_extender_11
  assign bit_extender_12_out = {{31{_12}}, _12};  // Bit_Extender bit_extender_12
  assign bit_extender_13_out = {{31{_13}}, _13};  // Bit_Extender bit_extender_13
  assign bit_extender_14_out = {{31{_14}}, _14};  // Bit_Extender bit_extender_14
  assign bit_extender_15_out = {{31{_15}}, _15};  // Bit_Extender bit_extender_15
  assign bit_extender_16_out = {{31{_16}}, _16};  // Bit_Extender bit_extender_16
  S_R_Flip_Flop s_r_ff_1 (.S(keyboard), .clk(clock), .R(s_r_ff_1_q), .Q(s_r_ff_1_q));  // open: Qn, preset, reset, en
  Register #(.width(5)) register_1 (.D(adder_1_out), .Q(register_1_q), .clk(clock), .clr(reset));  // open: en
  assign out_14 = 32'h10000000 & bit_extender_9_out;  // AND_Gate and_9, 32 bits wide
  assign out_18 = 32'h10000000 & bit_extender_10_out;  // AND_Gate and_10, 32 bits wide
  assign out_22 = 32'h10000000 & bit_extender_11_out;  // AND_Gate and_11, 32 bits wide
  assign out_26 = 32'h10000000 & bit_extender_12_out;  // AND_Gate and_12, 32 bits wide
  assign out_7 = 32'h10000000 & bit_extender_13_out;  // AND_Gate and_13, 32 bits wide
  assign out_11 = 32'h10000000 & bit_extender_14_out;  // AND_Gate and_14, 32 bits wide
  assign out_15 = 32'h10000000 & bit_extender_15_out;  // AND_Gate and_15, 32 bits wide
  assign out_19 = 32'h10000000 & bit_extender_16_out;  // AND_Gate and_16, 32 bits wide
  Multiplexer #(.width(5)) multiplexer_1 (
    .in0(5'b00001), .in1(5'b11110), .out(multiplexer_1_out), .sel(s_r_ff_1_q), .en(not_1_out));
  not not_1 (not_1_out, loser);
  Adder #(.width(5)) adder_1 (.a(multiplexer_1_out), .b(register_1_q), .out(adder_1_out));  // open: cin, cout
  assign bit_extender_17_out = {{4{not_1_out}}, not_1_out};  // Bit_Extender bit_extender_17
  assign bit_extender_18_out = {{31{_17}}, _17};  // Bit_Extender bit_extender_18
  assign bit_extender_19_out = {{31{_18}}, _18};  // Bit_Extender bit_extender_19
  assign bit_extender_20_out = {{31{_19}}, _19};  // Bit_Extender bit_extender_20
  assign bit_extender_21_out = {{31{_20}}, _20};  // Bit_Extender bit_extender_21
  assign bit_extender_22_out = {{31{_21}}, _21};  // Bit_Extender bit_extender_22
  assign bit_extender_23_out = {{31{_22}}, _22};  // Bit_Extender bit_extender_23
  assign bit_extender_24_out = {{31{_23}}, _23};  // Bit_Extender bit_extender_24
  assign bit_extender_25_out = {{31{_24}}, _24};  // Bit_Extender bit_extender_25
  Decoder #(.select(5), .enable("false")) decoder_1 (
    .out0(_1), .out1(_2), .out2(_3), .out3(_4), .out4(_5), .out5(_6), .out6(_7), .out7(_8), .out8(_9),
    .out9(_10), .out10(_11), .out11(_12), .out12(_13), .out13(_14), .out14(_15), .out15(_16), .out16(_17),
    .out17(_18), .out18(_19), .out19(_20), .out20(_21), .out21(_22), .out22(_23), .out23(_24),
    .sel(and_17_out));  // open: out24, out25, out26, out27, out28, out29, out30, out31
  assign and_17_out = adder_1_out & bit_extender_17_out;  // AND_Gate and_17, 5 bits wide
  and and_18 (_1lol, _1, not_1_out);
  assign out_23 = 32'h10000000 & bit_extender_18_out;  // AND_Gate and_19, 32 bits wide
  assign out_27 = 32'h10000000 & bit_extender_19_out;  // AND_Gate and_20, 32 bits wide
  assign out_8 = 32'h10000000 & bit_extender_20_out;  // AND_Gate and_21, 32 bits wide
  assign out_12 = 32'h10000000 & bit_extender_21_out;  // AND_Gate and_22, 32 bits wide
  assign out_16 = 32'h10000000 & bit_extender_22_out;  // AND_Gate and_23, 32 bits wide
  assign out_20 = 32'h10000000 & bit_extender_23_out;  // AND_Gate and_24, 32 bits wide
  assign out_24 = 32'h10000000 & bit_extender_24_out;  // AND_Gate and_25, 32 bits wide
  assign out_28 = 32'h10000000 & bit_extender_25_out;  // AND_Gate and_26, 32 bits wide
  DotMatrix #(.inputtype("row"), .matrixcols(32), .matrixrows(24)) dotmatrix_1 (
    .row0(out_5), .row1(out_9), .row2(out_13), .row3(out_17), .row4(out_21), .row5(out_25), .row6(out_6),
    .row7(out_10), .row8(out_14), .row9(out_18), .row10(out_22), .row11(out_26), .row12(out_7),
    .row13(out_11), .row14(out_15), .row15(out_19), .row16(out_23), .row17(out_27), .row18(out_8),
    .row19(out_12), .row20(out_16), .row21(out_20), .row22(out_24), .row23(out_28));

  // Other names for the same wires on the sheet: a[31:0] = out_5; b[31:0] = out_9; c[31:0] = out_13; d[31:0] = out_17;
  //   e[31:0] = out_21; f[31:0] = out_25; g[31:0] = out_6; h[31:0] = out_10; h1[31:0] = out_7; h2[31:0] = out_11;
  //   h3[31:0] = out_15; h4[31:0] = out_19; h5[31:0] = out_23; h6[31:0] = out_27; h7[31:0] = out_8; h8[31:0] = out_12;
  //   h9[31:0] = out_16; h10[31:0] = out_20; h11[31:0] = out_24; h12[31:0] = out_28; k[31:0] = out_26;
  //   o[31:0] = out_22; p[31:0] = out_14; q[31:0] = out_18

  // Notes on the sheet:
  //   Размещение птицы по 4 столбцу
  //   Рассчёт высоты полёта (Гравитация&Прыжки)
  //   Реализация движения птицы
  //   Вывод на матрицу
endmodule

module Column (
  input  clock,
  output [31:0] out_2,
  output [31:0] out_3,
  output [31:0] out_4,
  output [31:0] out_5,
  output [31:0] out_6,
  output [31:0] out_7,
  output [31:0] out_8,
  output [31:0] out_9,
  output [31:0] out_10,
  output [31:0] out_11,
  output [31:0] out_12,
  output [31:0] out_13,
  output [31:0] out_14,
  output [31:0] out_15,
  output [31:0] out_16,
  output [31:0] out_17,
  output [31:0] out_18,
  output [31:0] out_19,
  output [31:0] out_20,
  output [31:0] out_21,
  output [31:0] out_22,
  output [31:0] out_23,
  output [31:0] out_24,
  output [31:0] out_25,
  output [31:0] out_26,
  output [31:0] out_27,
  output [31:0] out_28,
  output [31:0] out_29,
  output [31:0] out_30,
  output [31:0] out_31,
  output [31:0] out_32,
  output [31:0] out_33,
  output [31:0] out_34,
  output [31:0] out_35,
  output [31:0] out_36,
  output [31:0] out_37,
  output [31:0] out_38,
  output [31:0] out_39,
  output [31:0] out_40,
  output [31:0] out_41,
  output [31:0] out_42,
  output [31:0] out_43,
  output [31:0] out_44,
  output [31:0] out_45,
  output [31:0] out_46,
  output [31:0] out_47,
  output [31:0] out_48,
  output [31:0] out_49
);

  wire comparator_1_eq;
  wire [5:0] counter_1_q;
  wire [31:0] register_1_q, shifter_1_out;

  Register #(.width(32)) register_1 (.D(out_4), .Q(register_1_q), .clk(clock));  // open: en, clr
  Counter #(.width(6), .max('h6)) counter_1 (.Q(counter_1_q), .clk(clock));  // open: load, D, count, carry, clr
  Shifter #(.width(32)) shifter_1 (.in(register_1_q), .\dist (5'b00001), .out(shifter_1_out));
  Comparator #(.width(6)) comparator_1 (.a(6'b000110), .b(counter_1_q), .eq(comparator_1_eq));  // open: gt, lt
  Multiplexer #(.width(32)) multiplexer_1 (
    .in0(shifter_1_out), .in1(32'hc0c0c0c), .out(out_4), .sel(comparator_1_eq));  // open: en
  DotMatrix #(.inputtype("row"), .matrixcols(32), .matrixrows(24)) dotmatrix_1 (
    .row0({32{1'b0}}), .row1({32{1'b0}}), .row2({32{1'b0}}), .row3({32{1'b0}}), .row4({32{1'b0}}),
    .row5({32{1'b0}}), .row6({32{1'b0}}), .row7({32{1'b0}}), .row8({32{1'b0}}), .row9({32{1'b0}}),
    .row10({32{1'b0}}), .row11({32{1'b0}}), .row12({32{1'b0}}), .row13({32{1'b0}}), .row14({32{1'b0}}),
    .row15({32{1'b0}}), .row16({32{1'b0}}), .row17({32{1'b0}}), .row18({32{1'b0}}), .row19({32{1'b0}}),
    .row20({32{1'b0}}), .row21({32{1'b0}}), .row22({32{1'b0}}), .row23({32{1'b0}}));
  DotMatrix #(.inputtype("row"), .matrixcols(32), .matrixrows(24)) dotmatrix_2 (
    .row0({32{1'b0}}), .row1({32{1'b0}}), .row2({32{1'b0}}), .row3({32{1'b0}}), .row4({32{1'b0}}),
    .row5({32{1'b0}}), .row6({32{1'b0}}), .row7({32{1'b0}}), .row8({32{1'b0}}), .row9({32{1'b0}}),
    .row10({32{1'b0}}), .row11({32{1'b0}}), .row12(out_4), .row13(out_4), .row14(out_4), .row15(out_4),
    .row16(out_4), .row17(out_4), .row18(out_4), .row19(out_4), .row20(out_4), .row21(out_4), .row22(out_4),
    .row23(out_4));

  assign out_2 = {32{1'b0}};
  assign out_3 = {32{1'b0}};
  assign out_5 = out_4;
  assign out_6 = {32{1'b0}};
  assign out_7 = {32{1'b0}};
  assign out_8 = {32{1'b0}};
  assign out_9 = {32{1'b0}};
  assign out_10 = {32{1'b0}};
  assign out_11 = {32{1'b0}};
  assign out_12 = out_4;
  assign out_13 = out_4;
  assign out_14 = {32{1'b0}};
  assign out_15 = {32{1'b0}};
  assign out_16 = {32{1'b0}};
  assign out_17 = {32{1'b0}};
  assign out_18 = {32{1'b0}};
  assign out_19 = {32{1'b0}};
  assign out_20 = out_4;
  assign out_21 = out_4;
  assign out_22 = {32{1'b0}};
  assign out_23 = {32{1'b0}};
  assign out_24 = {32{1'b0}};
  assign out_25 = {32{1'b0}};
  assign out_26 = {32{1'b0}};
  assign out_27 = {32{1'b0}};
  assign out_28 = out_4;
  assign out_29 = out_4;
  assign out_30 = {32{1'b0}};
  assign out_31 = {32{1'b0}};
  assign out_32 = {32{1'b0}};
  assign out_33 = {32{1'b0}};
  assign out_34 = {32{1'b0}};
  assign out_35 = {32{1'b0}};
  assign out_36 = out_4;
  assign out_37 = out_4;
  assign out_38 = {32{1'b0}};
  assign out_39 = {32{1'b0}};
  assign out_40 = {32{1'b0}};
  assign out_41 = {32{1'b0}};
  assign out_42 = {32{1'b0}};
  assign out_43 = {32{1'b0}};
  assign out_44 = out_4;
  assign out_45 = out_4;
  assign out_46 = {32{1'b0}};
  assign out_47 = {32{1'b0}};
  assign out_48 = {32{1'b0}};
  assign out_49 = {32{1'b0}};

  // Other names for the same wires on the sheet: vec_adr[31:0] = out_4

  // Notes on the sheet:
  //   Генератор препятствий (ход игры)
endmodule

module Over_or_Play (
  input  loser,
  input  clock,
  output [31:0] out_3,
  output [31:0] out_4,
  output [31:0] out_5,
  output [31:0] out_6,
  output [31:0] out_7,
  output [31:0] out_8,
  output [31:0] out_9,
  output [31:0] out_10,
  output [31:0] out_11,
  output [31:0] out_12,
  output [31:0] out_13,
  output [31:0] out_14,
  output [31:0] out_15,
  output [31:0] out_16,
  output [31:0] out_17,
  output [31:0] out_18,
  output [31:0] out_19,
  output [31:0] out_20,
  output [31:0] out_21,
  output [31:0] out_22,
  output [31:0] out_23,
  output [31:0] out_24,
  output [31:0] out_25,
  output [31:0] out_26,
  output [31:0] out_27,
  output [31:0] out_28,
  output [31:0] out_29,
  output [31:0] out_30,
  output [31:0] out_31,
  output [31:0] out_32,
  output [31:0] out_33,
  output [31:0] out_34,
  output [31:0] out_35,
  output [31:0] out_36,
  output [31:0] out_37,
  output [31:0] out_38,
  output [31:0] out_39,
  output [31:0] out_40,
  output [31:0] out_41,
  output [31:0] out_42,
  output [31:0] out_43,
  output [31:0] out_44,
  output [31:0] out_45,
  output [31:0] out_46,
  output [31:0] out_47,
  output [31:0] out_48,
  output [31:0] out_49,
  output [31:0] out_50
);

  wire [31:0] column_1_out_2, column_1_out_3, column_1_out_4, column_1_out_5, column_1_out_6, column_1_out_7,
       column_1_out_8, column_1_out_9, column_1_out_10, column_1_out_11, column_1_out_12, column_1_out_13,
       column_1_out_14, column_1_out_15, column_1_out_16, column_1_out_17, column_1_out_18, column_1_out_19,
       column_1_out_20, column_1_out_21, column_1_out_22, column_1_out_23, column_1_out_24, column_1_out_25,
       column_1_out_26, column_1_out_27, column_1_out_28, column_1_out_29, column_1_out_30, column_1_out_31,
       column_1_out_32, column_1_out_33, column_1_out_34, column_1_out_35, column_1_out_36, column_1_out_37,
       column_1_out_38, column_1_out_39, column_1_out_40, column_1_out_41, column_1_out_42, column_1_out_43,
       column_1_out_44, column_1_out_45, column_1_out_46, column_1_out_47, column_1_out_48, column_1_out_49,
       final_screen_1_out_1, final_screen_1_out_2, final_screen_1_out_3, final_screen_1_out_4,
       final_screen_1_out_5, final_screen_1_out_6, final_screen_1_out_7, final_screen_1_out_8,
       final_screen_1_out_9, final_screen_1_out_10, final_screen_1_out_11, final_screen_1_out_12,
       final_screen_1_out_13, final_screen_1_out_14, final_screen_1_out_15, final_screen_1_out_16,
       final_screen_1_out_17, final_screen_1_out_18, final_screen_1_out_19, final_screen_1_out_20,
       final_screen_1_out_21, final_screen_1_out_22, final_screen_1_out_23, final_screen_1_out_24,
       final_screen_1_out_25, final_screen_1_out_26, final_screen_1_out_27, final_screen_1_out_28,
       final_screen_1_out_29, final_screen_1_out_30, final_screen_1_out_31, final_screen_1_out_32,
       final_screen_1_out_33, final_screen_1_out_34, final_screen_1_out_35, final_screen_1_out_36,
       final_screen_1_out_37, final_screen_1_out_38, final_screen_1_out_39, final_screen_1_out_40,
       final_screen_1_out_41, final_screen_1_out_42, final_screen_1_out_43, final_screen_1_out_44,
       final_screen_1_out_45, final_screen_1_out_46, final_screen_1_out_47, final_screen_1_out_48;

  Multiplexer #(.width(32)) multiplexer_1 (
    .in0(column_1_out_6), .in1(final_screen_1_out_1), .out(out_3), .sel(loser));  // open: en
  Multiplexer #(.width(32)) multiplexer_2 (
    .in0(column_1_out_14), .in1(final_screen_1_out_9), .out(out_4), .sel(loser));  // open: en
  Multiplexer #(.width(32)) multiplexer_3 (
    .in0(column_1_out_22), .in1(final_screen_1_out_17), .out(out_5), .sel(loser));  // open: en
  Multiplexer #(.width(32)) multiplexer_4 (
    .in0(column_1_out_30), .in1(final_screen_1_out_25), .out(out_6), .sel(loser));  // open: en
  Multiplexer #(.width(32)) multiplexer_5 (
    .in0(column_1_out_38), .in1(final_screen_1_out_33), .out(out_7), .sel(loser));  // open: en
  Multiplexer #(.width(32)) multiplexer_6 (
    .in0(column_1_out_46), .in1(final_screen_1_out_41), .out(out_8), .sel(loser));  // open: en
  Multiplexer #(.width(32)) multiplexer_7 (
    .in0(column_1_out_7), .in1(final_screen_1_out_2), .out(out_9), .sel(loser));  // open: en
  Multiplexer #(.width(32)) multiplexer_8 (
    .in0(column_1_out_15), .in1(final_screen_1_out_10), .out(out_10), .sel(loser));  // open: en
  Multiplexer #(.width(32)) multiplexer_9 (
    .in0(column_1_out_23), .in1(final_screen_1_out_18), .out(out_11), .sel(loser));  // open: en
  Multiplexer #(.width(32)) multiplexer_10 (
    .in0(column_1_out_31), .in1(final_screen_1_out_26), .out(out_12), .sel(loser));  // open: en
  Multiplexer #(.width(32)) multiplexer_11 (
    .in0(column_1_out_39), .in1(final_screen_1_out_34), .out(out_13), .sel(loser));  // open: en
  Multiplexer #(.width(32)) multiplexer_12 (
    .in0(column_1_out_47), .in1(final_screen_1_out_42), .out(out_14), .sel(loser));  // open: en
  Multiplexer #(.width(32)) multiplexer_13 (
    .in0(column_1_out_8), .in1(final_screen_1_out_3), .out(out_15), .sel(loser));  // open: en
  Multiplexer #(.width(32)) multiplexer_14 (
    .in0(column_1_out_16), .in1(final_screen_1_out_11), .out(out_16), .sel(loser));  // open: en
  Multiplexer #(.width(32)) multiplexer_15 (
    .in0(column_1_out_24), .in1(final_screen_1_out_19), .out(out_17), .sel(loser));  // open: en
  Multiplexer #(.width(32)) multiplexer_16 (
    .in0(column_1_out_32), .in1(final_screen_1_out_27), .out(out_18), .sel(loser));  // open: en
  Multiplexer #(.width(32)) multiplexer_17 (
    .in0(column_1_out_40), .in1(final_screen_1_out_35), .out(out_19), .sel(loser));  // open: en
  Multiplexer #(.width(32)) multiplexer_18 (
    .in0(column_1_out_48), .in1(final_screen_1_out_43), .out(out_20), .sel(loser));  // open: en
  Multiplexer #(.width(32)) multiplexer_19 (
    .in0(column_1_out_9), .in1(final_screen_1_out_4), .out(out_21), .sel(loser));  // open: en
  Multiplexer #(.width(32)) multiplexer_20 (
    .in0(column_1_out_17), .in1(final_screen_1_out_12), .out(out_22), .sel(loser));  // open: en
  Multiplexer #(.width(32)) multiplexer_21 (
    .in0(column_1_out_25), .in1(final_screen_1_out_20), .out(out_23), .sel(loser));  // open: en
  Multiplexer #(.width(32)) multiplexer_22 (
    .in0(column_1_out_33), .in1(final_screen_1_out_28), .out(out_24), .sel(loser));  // open: en
  Final_Screen final_screen_1 (
    .out_1(final_screen_1_out_1), .out_2(final_screen_1_out_2), .out_3(final_screen_1_out_3),
    .out_4(final_screen_1_out_4), .out_5(final_screen_1_out_5), .out_6(final_screen_1_out_6),
    .out_7(final_screen_1_out_7), .out_8(final_screen_1_out_8), .out_9(final_screen_1_out_9),
    .out_10(final_screen_1_out_10), .out_11(final_screen_1_out_11), .out_12(final_screen_1_out_12),
    .out_13(final_screen_1_out_13), .out_14(final_screen_1_out_14), .out_15(final_screen_1_out_15),
    .out_16(final_screen_1_out_16), .out_17(final_screen_1_out_17), .out_18(final_screen_1_out_18),
    .out_19(final_screen_1_out_19), .out_20(final_screen_1_out_20), .out_21(final_screen_1_out_21),
    .out_22(final_screen_1_out_22), .out_23(final_screen_1_out_23), .out_24(final_screen_1_out_24),
    .out_25(final_screen_1_out_25), .out_26(final_screen_1_out_26), .out_27(final_screen_1_out_27),
    .out_28(final_screen_1_out_28), .out_29(final_screen_1_out_29), .out_30(final_screen_1_out_30),
    .out_31(final_screen_1_out_31), .out_32(final_screen_1_out_32), .out_33(final_screen_1_out_33),
    .out_34(final_screen_1_out_34), .out_35(final_screen_1_out_35), .out_36(final_screen_1_out_36),
    .out_37(final_screen_1_out_37), .out_38(final_screen_1_out_38), .out_39(final_screen_1_out_39),
    .out_40(final_screen_1_out_40), .out_41(final_screen_1_out_41), .out_42(final_screen_1_out_42),
    .out_43(final_screen_1_out_43), .out_44(final_screen_1_out_44), .out_45(final_screen_1_out_45),
    .out_46(final_screen_1_out_46), .out_47(final_screen_1_out_47), .out_48(final_screen_1_out_48));
  Column column_1 (
    .out_2(column_1_out_2), .out_3(column_1_out_3), .out_4(column_1_out_4), .out_5(column_1_out_5),
    .out_6(column_1_out_6), .out_7(column_1_out_7), .out_8(column_1_out_8), .out_9(column_1_out_9),
    .out_10(column_1_out_10), .out_11(column_1_out_11), .out_12(column_1_out_12), .out_13(column_1_out_13),
    .out_14(column_1_out_14), .out_15(column_1_out_15), .out_16(column_1_out_16), .out_17(column_1_out_17),
    .out_18(column_1_out_18), .out_19(column_1_out_19), .out_20(column_1_out_20), .out_21(column_1_out_21),
    .out_22(column_1_out_22), .out_23(column_1_out_23), .out_24(column_1_out_24), .out_25(column_1_out_25),
    .out_26(column_1_out_26), .out_27(column_1_out_27), .out_28(column_1_out_28), .out_29(column_1_out_29),
    .out_30(column_1_out_30), .out_31(column_1_out_31), .out_32(column_1_out_32), .out_33(column_1_out_33),
    .out_34(column_1_out_34), .out_35(column_1_out_35), .out_36(column_1_out_36), .out_37(column_1_out_37),
    .out_38(column_1_out_38), .out_39(column_1_out_39), .out_40(column_1_out_40), .out_41(column_1_out_41),
    .out_42(column_1_out_42), .out_43(column_1_out_43), .out_44(column_1_out_44), .out_45(column_1_out_45),
    .out_46(column_1_out_46), .out_47(column_1_out_47), .out_48(column_1_out_48), .out_49(column_1_out_49),
    .clock(clock));
  Multiplexer #(.width(32)) multiplexer_23 (
    .in0(column_1_out_41), .in1(final_screen_1_out_36), .out(out_25), .sel(loser));  // open: en
  Multiplexer #(.width(32)) multiplexer_24 (
    .in0(column_1_out_49), .in1(final_screen_1_out_44), .out(out_26), .sel(loser));  // open: en
  Multiplexer #(.width(32)) multiplexer_25 (
    .in0(column_1_out_2), .in1(final_screen_1_out_5), .out(out_27), .sel(loser));  // open: en
  Multiplexer #(.width(32)) multiplexer_26 (
    .in0(column_1_out_10), .in1(final_screen_1_out_13), .out(out_28), .sel(loser));  // open: en
  Multiplexer #(.width(32)) multiplexer_27 (
    .in0(column_1_out_18), .in1(final_screen_1_out_21), .out(out_29), .sel(loser));  // open: en
  Multiplexer #(.width(32)) multiplexer_28 (
    .in0(column_1_out_26), .in1(final_screen_1_out_29), .out(out_30), .sel(loser));  // open: en
  Multiplexer #(.width(32)) multiplexer_29 (
    .in0(column_1_out_34), .in1(final_screen_1_out_37), .out(out_31), .sel(loser));  // open: en
  Multiplexer #(.width(32)) multiplexer_30 (
    .in0(column_1_out_42), .in1(final_screen_1_out_45), .out(out_32), .sel(loser));  // open: en
  Multiplexer #(.width(32)) multiplexer_31 (
    .in0(column_1_out_3), .in1(final_screen_1_out_6), .out(out_33), .sel(loser));  // open: en
  Multiplexer #(.width(32)) multiplexer_32 (
    .in0(column_1_out_11), .in1(final_screen_1_out_14), .out(out_34), .sel(loser));  // open: en
  Multiplexer #(.width(32)) multiplexer_33 (
    .in0(column_1_out_19), .in1(final_screen_1_out_22), .out(out_35), .sel(loser));  // open: en
  Multiplexer #(.width(32)) multiplexer_34 (
    .in0(column_1_out_27), .in1(final_screen_1_out_30), .out(out_36), .sel(loser));  // open: en
  Multiplexer #(.width(32)) multiplexer_35 (
    .in0(column_1_out_35), .in1(final_screen_1_out_38), .out(out_37), .sel(loser));  // open: en
  Multiplexer #(.width(32)) multiplexer_36 (
    .in0(column_1_out_43), .in1(final_screen_1_out_46), .out(out_38), .sel(loser));  // open: en
  Multiplexer #(.width(32)) multiplexer_37 (
    .in0(column_1_out_4), .in1(final_screen_1_out_7), .out(out_39), .sel(loser));  // open: en
  Multiplexer #(.width(32)) multiplexer_38 (
    .in0(column_1_out_12), .in1(final_screen_1_out_15), .out(out_40), .sel(loser));  // open: en
  Multiplexer #(.width(32)) multiplexer_39 (
    .in0(column_1_out_20), .in1(final_screen_1_out_23), .out(out_41), .sel(loser));  // open: en
  Multiplexer #(.width(32)) multiplexer_40 (
    .in0(column_1_out_28), .in1(final_screen_1_out_31), .out(out_42), .sel(loser));  // open: en
  Multiplexer #(.width(32)) multiplexer_41 (
    .in0(column_1_out_36), .in1(final_screen_1_out_39), .out(out_43), .sel(loser));  // open: en
  Multiplexer #(.width(32)) multiplexer_42 (
    .in0(column_1_out_44), .in1(final_screen_1_out_47), .out(out_44), .sel(loser));  // open: en
  Multiplexer #(.width(32)) multiplexer_43 (
    .in0(column_1_out_5), .in1(final_screen_1_out_8), .out(out_45), .sel(loser));  // open: en
  Multiplexer #(.width(32)) multiplexer_44 (
    .in0(column_1_out_13), .in1(final_screen_1_out_16), .out(out_46), .sel(loser));  // open: en
  Multiplexer #(.width(32)) multiplexer_45 (
    .in0(column_1_out_21), .in1(final_screen_1_out_24), .out(out_47), .sel(loser));  // open: en
  Multiplexer #(.width(32)) multiplexer_46 (
    .in0(column_1_out_29), .in1(final_screen_1_out_32), .out(out_48), .sel(loser));  // open: en
  Multiplexer #(.width(32)) multiplexer_47 (
    .in0(column_1_out_37), .in1(final_screen_1_out_40), .out(out_49), .sel(loser));  // open: en
  Multiplexer #(.width(32)) multiplexer_48 (
    .in0(column_1_out_45), .in1(final_screen_1_out_48), .out(out_50), .sel(loser));  // open: en

  // Notes on the sheet:
  //   Вывод на экран (состояние)
endmodule

module Final_Screen (
  output [31:0] out_1,
  output [31:0] out_2,
  output [31:0] out_3,
  output [31:0] out_4,
  output [31:0] out_5,
  output [31:0] out_6,
  output [31:0] out_7,
  output [31:0] out_8,
  output [31:0] out_9,
  output [31:0] out_10,
  output [31:0] out_11,
  output [31:0] out_12,
  output [31:0] out_13,
  output [31:0] out_14,
  output [31:0] out_15,
  output [31:0] out_16,
  output [31:0] out_17,
  output [31:0] out_18,
  output [31:0] out_19,
  output [31:0] out_20,
  output [31:0] out_21,
  output [31:0] out_22,
  output [31:0] out_23,
  output [31:0] out_24,
  output [31:0] out_25,
  output [31:0] out_26,
  output [31:0] out_27,
  output [31:0] out_28,
  output [31:0] out_29,
  output [31:0] out_30,
  output [31:0] out_31,
  output [31:0] out_32,
  output [31:0] out_33,
  output [31:0] out_34,
  output [31:0] out_35,
  output [31:0] out_36,
  output [31:0] out_37,
  output [31:0] out_38,
  output [31:0] out_39,
  output [31:0] out_40,
  output [31:0] out_41,
  output [31:0] out_42,
  output [31:0] out_43,
  output [31:0] out_44,
  output [31:0] out_45,
  output [31:0] out_46,
  output [31:0] out_47,
  output [31:0] out_48
);

  DotMatrix #(.inputtype("row"), .matrixcols(32), .matrixrows(24)) dotmatrix_1 (
    .row0({32{1'b0}}), .row1({32{1'b0}}), .row2({32{1'b0}}), .row3({32{1'b0}}), .row4({32{1'b0}}),
    .row5({32{1'b0}}), .row6({32{1'b0}}), .row7({32{1'b0}}), .row8({32{1'b0}}), .row9(32'h18000),
    .row10(32'h18000), .row11(32'h1c000), .row12(32'h1f000), .row13(32'h1fc00), .row14(32'h1ff80),
    .row15(32'h1fffe), .row16(32'h1fff8), .row17(32'h1fffe), .row18(32'h1ff80), .row19(32'h1fc00),
    .row20(32'h1f000), .row21(32'h1c000), .row22(32'h18000), .row23(32'h18000));
  DotMatrix #(.inputtype("row"), .matrixcols(32), .matrixrows(24)) dotmatrix_2 (
    .row0(32'h18000), .row1(32'h18000), .row2(32'h18000), .row3(32'h18000), .row4(32'h18000),
    .row5(32'h18000), .row6(32'h18000), .row7(32'h18000), .row8(32'h18000), .row9(32'h18000),
    .row10(32'h18000), .row11(32'h18000), .row12(32'h18000), .row13(32'h18000), .row14(32'h18000),
    .row15(32'h18000), .row16(32'h18000), .row17(32'h18000), .row18(32'h18000), .row19(32'hffffff0),
    .row20(32'h1ffffff8), .row21(32'h3ffffffc), .row22(32'h7ffffffe), .row23({32{1'b1}}));

  assign out_1 = {32{1'b0}};
  assign out_2 = {32{1'b0}};
  assign out_3 = 32'h1f000;
  assign out_4 = 32'h1ff80;
  assign out_5 = 32'h18000;
  assign out_6 = 32'h18000;
  assign out_7 = 32'h18000;
  assign out_8 = 32'h18000;
  assign out_9 = {32{1'b0}};
  assign out_10 = {32{1'b0}};
  assign out_11 = 32'h1fc00;
  assign out_12 = 32'h1fc00;
  assign out_13 = 32'h18000;
  assign out_14 = 32'h18000;
  assign out_15 = 32'h18000;
  assign out_16 = 32'hffffff0;
  assign out_17 = {32{1'b0}};
  assign out_18 = {32{1'b0}};
  assign out_19 = 32'h1ff80;
  assign out_20 = 32'h1f000;
  assign out_21 = 32'h18000;
  assign out_22 = 32'h18000;
  assign out_23 = 32'h18000;
  assign out_24 = 32'h1ffffff8;
  assign out_25 = {32{1'b0}};
  assign out_26 = 32'h18000;
  assign out_27 = 32'h1fffe;
  assign out_28 = 32'h1c000;
  assign out_29 = 32'h18000;
  assign out_30 = 32'h18000;
  assign out_31 = 32'h18000;
  assign out_32 = 32'h3ffffffc;
  assign out_33 = {32{1'b0}};
  assign out_34 = 32'h18000;
  assign out_35 = 32'h1fff8;
  assign out_36 = 32'h18000;
  assign out_37 = 32'h18000;
  assign out_38 = 32'h18000;
  assign out_39 = 32'h18000;
  assign out_40 = 32'h7ffffffe;
  assign out_41 = {32{1'b0}};
  assign out_42 = 32'h1c000;
  assign out_43 = 32'h1fffe;
  assign out_44 = 32'h18000;
  assign out_45 = 32'h18000;
  assign out_46 = 32'h18000;
  assign out_47 = 32'h18000;
  assign out_48 = {32{1'b1}};

  // Notes on the sheet:
  //   Экран окончания игры
endmodule
