// Logisim project proiect.circ as structural Verilog: 2 circuits, main circuit main
module main (
);

  wire button_1_out, d_out, l, l_2_out, q, r, r_2_out, s;
  wire [31:0] undriven;

  Button u_l (.out(l));
  Button u_q (.out(q));
  Button u_r (.out(r));
  Button select (.out(s));
  Button l_2 (.out(l_2_out));
  Button up ();  // open: out
  Button r_2 (.out(r_2_out));
  Button d (.out(d_out));
  \схема  \u_схема_1  (.quit(q), .left(l), .right(r), .select(s));
  Button button_1 (.out(button_1_out));
  Clock clock_1 ();  // open: out
  DotMatrix #(.inputtype("row"), .matrixcols(32), .matrixrows(24)) dotmatrix_1 ();  // open: row0, row1, row2, row3, row4, row5, row6, row7, row8, row9, row10, row11, row12, row13, row14, row15, row16, row17, row18, row19, row20, row21, row22, row23
  DotMatrix #(.inputtype("row"), .matrixcols(32), .matrixrows(24)) dotmatrix_2 (
    .row22(undriven), .row23(undriven));  // open: row0, row1, row2, row3, row4, row5, row6, row7, row8, row9, row10, row11, row12, row13, row14, row15, row16, row17, row18, row19, row20, row21
endmodule

module \схема  (
  input  quit,
  input  left,
  input  right,
  input  select
);

  wire and_2_out, cdm_8_mark5_1_p4, cdm_8_mark5_1_p5, cdm_8_mark5_1_p7, cdm_8_mark5_1_p8, cdm_8_mark5_1_p9,
       cdm_8_mark5_1_p10, cdm_8_mark5_1_p11, cdm_8_mark5_1_p12, cdm_8_mark5_1_p13, decoder_1_out0,
       decoder_1_out1, IAck, IO_2_out, IOsel, not_1_out, not_2_out, rd_wr, tic;
  wire [2:0] vec;
  wire [3:0] IOaddr;
  wire [7:0] cdm_8_mark5_1_p17, IOdata, out, register_1_q;
  wire [7:4] cdm_8_mark5_1_p15;

  Clock clock_1 (.out(tic));
  // Probe on cdm_8_mark5_1_p8
  // Probe on cdm_8_mark5_1_p7
  // Probe on cdm_8_mark5_1_p5
  // Probe on cdm_8_mark5_1_p4
  // Probe on cdm_8_mark5_1_p9
  // Probe on cdm_8_mark5_1_p11
  // Probe on cdm_8_mark5_1_p10
  // CdM_8_mark5 cdm_8_mark5_1: pin names not known; wires that end beside it: 1'b0, vec, IAck, cdm_8_mark5_1_p4, cdm_8_mark5_1_p5, tic, cdm_8_mark5_1_p7, cdm_8_mark5_1_p8, cdm_8_mark5_1_p9, cdm_8_mark5_1_p10, cdm_8_mark5_1_p11, cdm_8_mark5_1_p12, cdm_8_mark5_1_p13, rd_wr, {cdm_8_mark5_1_p15, IOaddr}, out, cdm_8_mark5_1_p17
  and and_1 (IOsel, cdm_8_mark5_1_p15[4], cdm_8_mark5_1_p15[5], cdm_8_mark5_1_p15[6], cdm_8_mark5_1_p15[7], decoder_1_out1);
  Decoder decoder_1 (.out0(decoder_1_out0), .out1(decoder_1_out1), .sel(cdm_8_mark5_1_p12), .en(cdm_8_mark5_1_p13));
  not not_1 (not_1_out, rd_wr);
  assign cdm_8_mark5_1_p17 = rd_wr ? IOdata : 8'bz;  // Controlled_Buffer controlled_buffer_1
  and and_2 (and_2_out, decoder_1_out1, ~IOsel);  // AND_Gate
  assign IOdata = not_1_out ? out : 8'bz;  // Controlled_Buffer controlled_buffer_2
  not not_2 (not_2_out, tic);
  ROM rom_1 (.addr({cdm_8_mark5_1_p15, IOaddr}), .data(IOdata), .sel(decoder_1_out0));
  RAM ram_1 (
    .addr({cdm_8_mark5_1_p15, IOaddr}), .data(IOdata), .sel(and_2_out), .clk(not_2_out), .ld(rd_wr));  // open: clr
  and IO_2 (IO_2_out, IOsel, ~IOaddr[0], ~IOaddr[2], ~IOaddr[3]);  // AND_Gate
  DotMatrix #(.matrixcols(1), .matrixrows(8)) dotmatrix_1 (.col0(register_1_q));
  Register #(.trigger("falling")) register_1 (.D(IOdata), .en(IO_2_out), .Q(register_1_q), .clk(tic));  // open: clr
  Controlled_Buffer #(.width(3)) controlled_buffer_3 (.out(vec), .en(IAck));  // open: in

  // Notes on the sheet:
  //   contents of rom_1 (hex, n*v repeats v):
  //   7c 2 7d 0 7e c0 a2 90 82 b1 f6 70 40 0 71 0 72 0 10 40 2 70 50 0 71 0 72 14 10 40 2 70 60 0 71 0 72
  //   1e 10 40 2 70 70 0 71 0 72 28 10 40 2 b0 80 1 40 0 b1 f0 ff 40 1 b1 e0 ff 40 2 b1 d0 ff 40 3 b1 c0
  //   ff f0 c0 ff 7c 0 ad 81 a0 f0 c0 ff 7c 0 ad 80 a0 f0 c0 ff 10 40 2 f0 c0 ff f0 c0 ff 0 4d 45 4e 55 0
  //   3e 20 54 45 54 52 49 53 0 20 42 49 52 44 0 20 53 4f 4f 4e
  //   схема
endmodule
