// Logisim project tetris.circ as structural Verilog: 18 circuits, main circuit get_block
module get_block (
  input  Clock,
  output [7:0] X1,
  output [7:0] X2,
  output [7:0] X3,
  output [7:0] X4,
  output [7:0] XC,
  output [7:0] Y1,
  output [7:0] Y2,
  output [7:0] Y3,
  output [7:0] Y4,
  output [7:0] YC
);

  wire [2:0] id;

  Random #(.width(3)) random_1 (.clk(Clock), .out(id));  // open: next, clr
  Multiplexer #(.select(3), .width(8), .enable("false")) multiplexer_1 (
    .in0(8'h8), .in1(8'h9), .in2(8'h9), .in3(8'h7), .in4(8'h8), .in5(8'ha), .in6(8'h9), .in7(8'h8), .out(X1),
    .sel(id));
  Multiplexer #(.select(3), .width(8), .enable("false")) multiplexer_2 (
    .in0({8{1'b0}}), .in1({8{1'b0}}), .in2({8{1'b0}}), .in3({8{1'b0}}), .in4({8{1'b0}}), .in5({8{1'b0}}),
    .in6({8{1'b0}}), .in7({8{1'b0}}), .out(Y1), .sel(id));
  Multiplexer #(.select(3), .width(8), .enable("false")) multiplexer_3 (
    .in0(8'ha), .in1(8'h9), .in2(8'hb), .in3(8'h9), .in4(8'h8), .in5(8'ha), .in6(8'h7), .in7(8'ha), .out(X2),
    .sel(id));
  Multiplexer #(.select(3), .width(8), .enable("false")) multiplexer_4 (
    .in0({8{1'b0}}), .in1(8'h2), .in2({8{1'b0}}), .in3({8{1'b0}}), .in4(8'h2), .in5(8'h2), .in6(8'h2),
    .in7({8{1'b0}}), .out(Y2), .sel(id));
  Multiplexer #(.select(3), .width(8), .enable("false")) multiplexer_5 (
    .in0(8'h8), .in1(8'h9), .in2(8'h7), .in3(8'h9), .in4(8'h8), .in5(8'h8), .in6(8'h9), .in7(8'h8), .out(X3),
    .sel(id));
  Multiplexer #(.select(3), .width(8), .enable("false")) multiplexer_6 (
    .in0(8'h2), .in1(8'h4), .in2(8'h2), .in3(8'h2), .in4(8'h4), .in5(8'h4), .in6(8'h2), .in7(8'h2), .out(Y3),
    .sel(id));
  Multiplexer #(.select(3), .width(8), .enable("false")) multiplexer_7 (
    .in0(8'ha), .in1(8'h9), .in2(8'h9), .in3(8'hb), .in4(8'ha), .in5(8'ha), .in6(8'hb), .in7(8'ha), .out(X4),
    .sel(id));
  Multiplexer #(.select(3), .width(8), .enable("false")) multiplexer_8 (
    .in0(8'h2), .in1(8'h6), .in2(8'h2), .in3(8'h2), .in4(8'h4), .in5(8'h4), .in6(8'h2), .in7(8'h2), .out(Y4),
    .sel(id));
  Multiplexer #(.select(3), .width(8), .enable("false")) multiplexer_9 (
    .in0(8'ha), .in1(8'ha), .in2(8'ha), .in3(8'ha), .in4(8'ha), .in5(8'ha), .in6(8'ha), .in7(8'ha), .out(XC),
    .sel(id));
  Multiplexer #(.select(3), .width(8), .enable("false")) multiplexer_10 (
    .in0(8'h2), .in1(8'h4), .in2(8'h2), .in3(8'h2), .in4(8'h3), .in5(8'h3), .in6(8'h2), .in7(8'h2), .out(YC),
    .sel(id));

  // Other names for the same wires on the sheet: tick = Clock
endmodule

module block_and_field (
  input  in_1,
  input  ML,
  input  MR,
  input  TL,
  input  TR,
  input  set,
  output [31:0] out_7,
  output [31:0] out_8,
  output [31:0] out_9,
  output [31:0] out_10,
  output [31:0] out_11,
  output [31:0] out_12,
  output [31:0] out_13,
  output [31:0] out_14,
  output [31:0] out_15,
  output [31:0] out_16,
  output [31:0] out_17,
  output [31:0] out_18,
  output [31:0] out_19,
  output [31:0] out_20,
  output [31:0] out_21,
  output [31:0] out_22,
  output [31:0] out_23,
  output [31:0] out_24,
  output [31:0] out_25,
  output [31:0] out_26,
  output [31:0] out_27,
  output [31:0] out_28,
  output [31:0] out_29,
  output [31:0] out_30,
  output [31:0] out_31,
  output [31:0] out_32,
  output [31:0] out_33,
  output [31:0] out_34,
  output [31:0] out_35,
  output [31:0] out_36,
  output [31:0] out_37,
  output [31:0] out_38,
  output [31:0] out_39,
  output [31:0] out_40,
  output [31:0] out_41,
  output [31:0] out_42,
  output [31:0] out_43,
  output [31:0] out_44,
  output [31:0] out_45,
  output [31:0] out_46,
  output [31:0] out_47,
  output [31:0] out_48,
  output [31:0] out_49,
  output [31:0] out_50,
  output [31:0] out_51,
  output [31:0] out_52,
  output [31:0] out_53,
  output [31:0] out_54,
  output fail
);

  wire collision_1_collision, comparator_1_eq, d_ff_1_q, movement_block_1_dropped, or_1_out, or_2_out,
       undriven;
  wire [7:0] get_block_1_x1, get_block_1_x2, get_block_1_x3, get_block_1_x4, get_block_1_xc, get_block_1_y1,
       get_block_1_y2, get_block_1_y3, get_block_1_y4, get_block_1_yc, movement_block_1_x1_2,
       movement_block_1_x2_2, movement_block_1_x3_2, movement_block_1_x4_2, movement_block_1_xc_2,
       movement_block_1_y1_2, movement_block_1_y2_2, movement_block_1_y3_2, movement_block_1_y4_2,
       movement_block_1_yc_2, multiplexer_1_out, multiplexer_2_out, multiplexer_3_out, multiplexer_4_out,
       multiplexer_5_out, multiplexer_6_out, multiplexer_7_out, multiplexer_8_out, multiplexer_9_out,
       multiplexer_10_out, register_9_q, register_10_q, X1, X2, X3, X4, Y1, Y2, Y3, Y4;
  wire [31:0] block_output_1_out_9, block_output_1_out_10, block_output_1_out_11, block_output_1_out_12,
       block_output_1_out_13, block_output_1_out_14, block_output_1_out_15, block_output_1_out_16,
       block_output_1_out_17, block_output_1_out_18, block_output_1_out_19, block_output_1_out_20,
       block_output_1_out_21, block_output_1_out_22, block_output_1_out_23, block_output_1_out_24,
       block_output_1_out_25, block_output_1_out_26, block_output_1_out_27, block_output_1_out_28,
       block_output_1_out_29, block_output_1_out_30, block_output_1_out_31, block_output_1_out_32,
       block_output_1_out_33, block_output_1_out_34, block_output_1_out_35, block_output_1_out_36,
       block_output_1_out_37, block_output_1_out_38, block_output_1_out_39, block_output_1_out_40,
       block_output_1_out_41, block_output_1_out_42, block_output_1_out_43, block_output_1_out_44,
       block_output_1_out_45, block_output_1_out_46, block_output_1_out_47, block_output_1_out_48,
       block_output_1_out_49, block_output_1_out_50, block_output_1_out_51, block_output_1_out_52,
       block_output_1_out_53, block_output_1_out_54, block_output_1_out_55, block_output_1_out_56, R1, R2,
       R3, R4, R5, R6, R7, R8, R9, R10, R11, R12, R13, R14, R15, R16, R17, R18, R19, R20, R21, R22, R23, R24,
       R25, R26, R27, R28, R29, R30, R31, R32, R33, R34, R35, R36, R37, R38, R39, R40, R41, R42, R43, R44,
       R45, R46, R47, R48;

  get_block get_block_1 (
    .Clock(in_1), .X1(get_block_1_x1), .Y1(get_block_1_y1), .X2(get_block_1_x2), .Y2(get_block_1_y2),
    .X3(get_block_1_x3), .X4(get_block_1_x4), .Y4(get_block_1_y4), .XC(get_block_1_xc), .YC(get_block_1_yc),
    .Y3(get_block_1_y3));
  collision collision_1 (
    .X1(X1), .Y1(Y1), .X2(X2), .Y2(Y2), .X3(X3), .Y3(Y3), .X4(X4), .Y4(Y4), .R1(R1), .R2(R2), .R3(R3),
    .R4(R4), .R5(R5), .R6(R6), .R7(R7), .R8(R8), .R9(R9), .R10(R10), .R11(R11), .R12(R12), .R13(R13),
    .R14(R14), .R15(R15), .R16(R16), .R17(R17), .R18(R18), .R19(R19), .R20(R20), .R21(R21), .R22(R22),
    .R23(R23), .R24(R24), .R25(R25), .R26(R26), .R27(R27), .R28(R28), .R29(R29), .R30(R30), .R31(R31),
    .R32(R32), .R33(R33), .R34(R34), .R35(R35), .R36(R36), .R37(R37), .R38(R38), .R39(R39), .R40(R40),
    .R41(R41), .R42(R42), .R43(R43), .R44(R44), .R45(R45), .R46(R46), .R47(R47), .R48(R48),
    .collision(collision_1_collision));
  Multiplexer #(.width(8), .enable("false")) multiplexer_1 (
    .in0(movement_block_1_x1_2), .in1(get_block_1_x1), .out(multiplexer_1_out), .sel(or_1_out));
  Multiplexer #(.width(8), .enable("false")) multiplexer_2 (
    .in0(movement_block_1_y1_2), .in1(get_block_1_y1), .out(multiplexer_2_out), .sel(or_1_out));
  Multiplexer #(.width(8), .enable("false")) multiplexer_3 (
    .in0(movement_block_1_x2_2), .in1(get_block_1_x2), .out(multiplexer_3_out), .sel(or_1_out));
  Multiplexer #(.width(8), .enable("false")) multiplexer_4 (
    .in0(movement_block_1_y2_2), .in1(get_block_1_y2), .out(multiplexer_4_out), .sel(or_1_out));
  Multiplexer #(.width(8), .enable("false")) multiplexer_5 (
    .in0(movement_block_1_x3_2), .in1(get_block_1_x3), .out(multiplexer_5_out), .sel(or_1_out));
  Multiplexer #(.width(8), .enable("false")) multiplexer_6 (
    .in0(movement_block_1_y3_2), .in1(get_block_1_y3), .out(multiplexer_6_out), .sel(or_1_out));
  Multiplexer #(.width(8), .enable("false")) multiplexer_7 (
    .in0(movement_block_1_x4_2), .in1(get_block_1_x4), .out(multiplexer_7_out), .sel(or_1_out));
  Multiplexer #(.width(8), .enable("false")) multiplexer_8 (
    .in0(movement_block_1_y4_2), .in1(get_block_1_y4), .out(multiplexer_8_out), .sel(or_1_out));
  Multiplexer #(.width(8), .enable("false")) multiplexer_9 (
    .in0(movement_block_1_xc_2), .in1(get_block_1_xc), .out(multiplexer_9_out), .sel(or_1_out));
  Multiplexer #(.width(8), .enable("false")) multiplexer_10 (
    .in0(movement_block_1_yc_2), .in1(get_block_1_yc), .out(multiplexer_10_out), .sel(or_1_out));
  or or_1 (or_1_out, set, or_2_out);
  Register register_1 (.D(multiplexer_1_out), .en(undriven), .Q(X1), .clk(in_1));  // open: clr
  Register register_2 (.D(multiplexer_2_out), .en(undriven), .Q(Y1), .clk(in_1));  // open: clr
  Register register_3 (.D(multiplexer_3_out), .en(undriven), .Q(X2), .clk(in_1));  // open: clr
  Register register_4 (.D(multiplexer_4_out), .en(undriven), .Q(Y2), .clk(in_1));  // open: clr
  Register register_5 (.D(multiplexer_5_out), .en(undriven), .Q(X3), .clk(in_1));  // open: clr
  movement_block movement_block_1 (
    .X1(X1), .Y1(Y1), .X2(X2), .Y2(Y2), .X3(X3), .Y3(Y3), .X4(X4), .Y4(Y4), .XC(register_9_q),
    .YC(register_10_q), .move_left(ML), .move_right(MR), .rotate_left(TL), .rotate_right(TR),
    .X1_2(movement_block_1_x1_2), .Y1_2(movement_block_1_y1_2), .X2_2(movement_block_1_x2_2),
    .Y2_2(movement_block_1_y2_2), .X3_2(movement_block_1_x3_2), .Y3_2(movement_block_1_y3_2),
    .X4_2(movement_block_1_x4_2), .Y4_2(movement_block_1_y4_2), .XC_2(movement_block_1_xc_2),
    .YC_2(movement_block_1_yc_2), .Dropped(movement_block_1_dropped));
  Register register_6 (.D(multiplexer_6_out), .en(undriven), .Q(Y3), .clk(in_1));  // open: clr
  Register register_7 (.D(multiplexer_7_out), .en(undriven), .Q(X4), .clk(in_1));  // open: clr
  Register register_8 (.D(multiplexer_8_out), .en(undriven), .Q(Y4), .clk(in_1));  // open: clr
  Register register_9 (.D(multiplexer_9_out), .en(undriven), .Q(register_9_q), .clk(in_1));  // open: clr
  Register register_10 (.D(multiplexer_10_out), .en(undriven), .Q(register_10_q), .clk(in_1));  // open: clr
  block_output block_output_1 (
    .X1(X1), .Y1(Y1), .X2(X2), .Y2(Y2), .X3(X3), .Y3(Y3), .X4(X4), .Y4(Y4), .out_9(block_output_1_out_9),
    .out_11(block_output_1_out_11), .out_12(block_output_1_out_12), .out_13(block_output_1_out_13),
    .out_14(block_output_1_out_14), .out_15(block_output_1_out_15), .out_16(block_output_1_out_16),
    .out_17(block_output_1_out_17), .out_18(block_output_1_out_18), .out_19(block_output_1_out_19),
    .out_20(block_output_1_out_20), .out_21(block_output_1_out_21), .out_22(block_output_1_out_22),
    .out_23(block_output_1_out_23), .out_24(block_output_1_out_24), .out_25(block_output_1_out_25),
    .out_26(block_output_1_out_26), .out_27(block_output_1_out_27), .out_28(block_output_1_out_28),
    .out_29(block_output_1_out_29), .out_30(block_output_1_out_30), .out_31(block_output_1_out_31),
    .out_32(block_output_1_out_32), .out_33(block_output_1_out_33), .out_34(block_output_1_out_34),
    .out_35(block_output_1_out_35), .out_36(block_output_1_out_36), .out_37(block_output_1_out_37),
    .out_38(block_output_1_out_38), .out_39(block_output_1_out_39), .out_40(block_output_1_out_40),
    .out_41(block_output_1_out_41), .out_42(block_output_1_out_42), .out_43(block_output_1_out_43),
    .out_44(block_output_1_out_44), .out_45(block_output_1_out_45), .out_46(block_output_1_out_46),
    .out_47(block_output_1_out_47), .out_48(block_output_1_out_48), .out_49(block_output_1_out_49),
    .out_50(block_output_1_out_50), .out_51(block_output_1_out_51), .out_52(block_output_1_out_52),
    .out_53(block_output_1_out_53), .out_54(block_output_1_out_54), .out_55(block_output_1_out_55),
    .out_56(block_output_1_out_56), .out_10(block_output_1_out_10));
  or or_2 (or_2_out, movement_block_1_dropped, collision_1_collision);
  assign out_7 = block_output_1_out_9 | R1;  // OR_Gate or_3, 32 bits wide
  field field_1 (
    .save(d_ff_1_q), .clr(set), .R1(out_7), .R2(out_31), .R3(out_8), .R4(out_32), .R5(out_9), .R6(out_33),
    .R7(out_10), .R8(out_34), .R9(out_11), .R10(out_35), .R11(out_12), .R12(out_36), .R13(out_13),
    .R14(out_37), .R15(out_14), .R16(out_38), .R17(out_15), .R18(out_39), .R19(out_16), .R20(out_40),
    .R21(out_17), .R22(out_41), .R23(out_18), .R24(out_42), .R25(out_19), .R26(out_43), .R27(out_20),
    .R28(out_44), .R29(out_21), .R30(out_45), .R31(out_22), .R32(out_46), .R33(out_23), .R34(out_47),
    .R35(out_24), .R36(out_48), .R37(out_25), .R38(out_49), .R39(out_26), .R40(out_50), .R41(out_27),
    .R42(out_51), .R43(out_28), .R44(out_52), .R45(out_29), .R46(out_53), .R47(out_30), .R48(out_54),
    .R1_2(R1), .R2_2(R2), .R3_2(R3), .R4_2(R4), .R5_2(R5), .R6_2(R6), .R7_2(R7), .R8_2(R8), .R9_2(R9),
    .R10_2(R10), .R11_2(R11), .R12_2(R12), .R13_2(R13), .R14_2(R14), .R15_2(R15), .R16_2(R16), .R17_2(R17),
    .R18_2(R18), .R19_2(R19), .R20_2(R20), .R21_2(R21), .R22_2(R22), .R23_2(R23), .R24_2(R24), .R25_2(R25),
    .R26_2(R26), .R27_2(R27), .R28_2(R28), .R29_2(R29), .R30_2(R30), .R31_2(R31), .R32_2(R32), .R33_2(R33),
    .R34_2(R34), .R35_2(R35), .R36_2(R36), .R37_2(R37), .R38_2(R38), .R39_2(R39), .R40_2(R40), .R41_2(R41),
    .R42_2(R42), .R43_2(R43), .R44_2(R44), .R45_2(R45), .R46_2(R46), .R47_2(R47), .R48_2(R48));
  D_Flip_Flop d_ff_1 (.clk(in_1), .D(or_2_out), .Q(d_ff_1_q));  // open: Qn, preset, en, reset
  not not_1 (fail, comparator_1_eq);
  Comparator #(.width(32)) comparator_1 (.a(R5), .b({32{1'b0}}), .eq(comparator_1_eq));  // open: gt, lt
  assign out_31 = block_output_1_out_10 | R2;  // OR_Gate or_4, 32 bits wide
  assign out_8 = block_output_1_out_11 | R3;  // OR_Gate or_5, 32 bits wide
  assign out_9 = block_output_1_out_13 | R5;  // OR_Gate or_6, 32 bits wide
  assign out_32 = block_output_1_out_12 | R4;  // OR_Gate or_7, 32 bits wide
  assign out_33 = block_output_1_out_14 | R6;  // OR_Gate or_8, 32 bits wide
  assign out_10 = block_output_1_out_15 | R7;  // OR_Gate or_9, 32 bits wide
  assign out_34 = block_output_1_out_16 | R8;  // OR_Gate or_10, 32 bits wide
  assign out_11 = block_output_1_out_17 | R9;  // OR_Gate or_11, 32 bits wide
  assign out_35 = block_output_1_out_18 | R10;  // OR_Gate or_12, 32 bits wide
  assign out_12 = block_output_1_out_19 | R11;  // OR_Gate or_13, 32 bits wide
  assign out_13 = block_output_1_out_21 | R13;  // OR_Gate or_14, 32 bits wide
  assign out_36 = block_output_1_out_20 | R12;  // OR_Gate or_15, 32 bits wide
  assign out_37 = block_output_1_out_22 | R14;  // OR_Gate or_16, 32 bits wide
  assign out_38 = block_output_1_out_24 | R16;  // OR_Gate or_17, 32 bits wide
  assign out_14 = block_output_1_out_23 | R15;  // OR_Gate or_18, 32 bits wide
  assign out_15 = block_output_1_out_25 | R17;  // OR_Gate or_19, 32 bits wide
  assign out_16 = block_output_1_out_27 | R19;  // OR_Gate or_20, 32 bits wide
  assign out_39 = block_output_1_out_26 | R18;  // OR_Gate or_21, 32 bits wide
  assign out_40 = block_output_1_out_28 | R20;  // OR_Gate or_22, 32 bits wide
  assign out_17 = block_output_1_out_29 | R21;  // OR_Gate or_23, 32 bits wide
  assign out_41 = block_output_1_out_30 | R22;  // OR_Gate or_24, 32 bits wide
  assign out_18 = block_output_1_out_31 | R23;  // OR_Gate or_25, 32 bits wide
  assign out_42 = block_output_1_out_32 | R24;  // OR_Gate or_26, 32 bits wide
  assign out_19 = block_output_1_out_33 | R25;  // OR_Gate or_27, 32 bits wide
  assign out_43 = block_output_1_out_34 | R26;  // OR_Gate or_28, 32 bits wide
  assign out_20 = block_output_1_out_35 | R27;  // OR_Gate or_29, 32 bits wide
  assign out_44 = block_output_1_out_36 | R28;  // OR_Gate or_30, 32 bits wide
  assign out_21 = block_output_1_out_37 | R29;  // OR_Gate or_31, 32 bits wide
  assign out_45 = block_output_1_out_38 | R30;  // OR_Gate or_32, 32 bits wide
  assign out_22 = block_output_1_out_39 | R31;  // OR_Gate or_33, 32 bits wide
  assign out_46 = block_output_1_out_40 | R32;  // OR_Gate or_34, 32 bits wide
  assign out_23 = block_output_1_out_41 | R33;  // OR_Gate or_35, 32 bits wide
  assign out_24 = block_output_1_out_43 | R35;  // OR_Gate or_36, 32 bits wide
  assign out_47 = block_output_1_out_42 | R34;  // OR_Gate or_37, 32 bits wide
  assign out_25 = block_output_1_out_45 | R37;  // OR_Gate or_38, 32 bits wide
  assign out_48 = block_output_1_out_44 | R36;  // OR_Gate or_39, 32 bits wide
  assign out_49 = block_output_1_out_46 | R38;  // OR_Gate or_40, 32 bits wide
  assign out_50 = block_output_1_out_48 | R40;  // OR_Gate or_41, 32 bits wide
  assign out_26 = block_output_1_out_47 | R39;  // OR_Gate or_42, 32 bits wide
  assign out_27 = block_output_1_out_49 | R41;  // OR_Gate or_43, 32 bits wide
  assign out_51 = block_output_1_out_50 | R42;  // OR_Gate or_44, 32 bits wide
  assign out_28 = block_output_1_out_51 | R43;  // OR_Gate or_45, 32 bits wide
  assign out_52 = block_output_1_out_52 | R44;  // OR_Gate or_46, 32 bits wide
  assign out_29 = block_output_1_out_53 | R45;  // OR_Gate or_47, 32 bits wide
  assign out_53 = block_output_1_out_54 | R46;  // OR_Gate or_48, 32 bits wide
  assign out_54 = block_output_1_out_56 | R48;  // OR_Gate or_49, 32 bits wide
  assign out_30 = block_output_1_out_55 | R47;  // OR_Gate or_50, 32 bits wide

  // Other names for the same wires on the sheet: tick = in_1
endmodule

module _8bit_to_32str (
  input  [7:0] in_1,
  output [31:0] out_2
);

  Shifter #(.width(32), .shift("lr")) shifter_1 (.in(32'h80000000), .\dist (in_1[4:0]), .out(out_2));
endmodule

module movement_block (
  input  [7:0] X1,
  input  [7:0] Y1,
  input  [7:0] X2,
  input  [7:0] Y2,
  input  [7:0] X3,
  input  [7:0] Y3,
  input  [7:0] X4,
  input  [7:0] Y4,
  input  [7:0] XC,
  input  [7:0] YC,
  input  move_left,
  input  rotate_left,
  input  move_right,
  input  rotate_right,
  output [7:0] X1_2,
  output [7:0] Y1_2,
  output [7:0] X2_2,
  output [7:0] Y2_2,
  output [7:0] X3_2,
  output [7:0] Y3_2,
  output [7:0] X4_2,
  output [7:0] Y4_2,
  output [7:0] XC_2,
  output [7:0] YC_2,
  output Dropped
);

  wire and_1_out, and_2_out, or_1_out;
  wire [7:0] move_block_1_x1_2, move_block_1_x2_2, move_block_1_x3_2, move_block_1_x4_2, move_block_1_xc_2,
       move_block_1_y1_2, move_block_1_y2_2, move_block_1_y3_2, move_block_1_y4_2, move_block_1_yc_2,
       move_block_2_x1_2, move_block_2_x2_2, move_block_2_x3_2, move_block_2_x4_2, move_block_2_xc_2,
       move_block_2_y1_2, move_block_2_y2_2, move_block_2_y3_2, move_block_2_y4_2, move_block_2_yc_2,
       rotate_block_1_x1_2, rotate_block_1_x2_2, rotate_block_1_x3_2, rotate_block_1_x4_2,
       rotate_block_1_xc_2, rotate_block_1_y1_2, rotate_block_1_y2_2, rotate_block_1_y3_2,
       rotate_block_1_y4_2, rotate_block_1_yc_2;

  move_block move_block_1 (
    .X1(X1), .X3(X3), .Y1(Y1), .Y3(Y3), .XC(XC), .X2(X2), .X4(X4), .YC(YC), .Y2(Y2), .Y4(Y4),
    .move_left(move_left), .move_right(move_right), .X1_2(move_block_1_x1_2), .X3_2(move_block_1_x3_2),
    .Y1_2(move_block_1_y1_2), .Y3_2(move_block_1_y3_2), .XC_2(move_block_1_xc_2), .X2_2(move_block_1_x2_2),
    .X4_2(move_block_1_x4_2), .YC_2(move_block_1_yc_2), .Y2_2(move_block_1_y2_2), .Y4_2(move_block_1_y4_2));
  rotate_block rotate_block_1 (
    .rotate_left(rotate_left), .rotate_right(rotate_right), .XC(move_block_1_xc_2), .YC(move_block_1_yc_2),
    .X1(move_block_1_x1_2), .X3(move_block_1_x3_2), .Y1(move_block_1_y1_2), .Y3(move_block_1_y3_2),
    .X2(move_block_1_x2_2), .X4(move_block_1_x4_2), .Y2(move_block_1_y2_2), .Y4(move_block_1_y4_2),
    .XC_2(rotate_block_1_xc_2), .YC_2(rotate_block_1_yc_2), .X1_2(rotate_block_1_x1_2),
    .X3_2(rotate_block_1_x3_2), .Y1_2(rotate_block_1_y1_2), .Y3_2(rotate_block_1_y3_2),
    .X4_2(rotate_block_1_x4_2), .X2_2(rotate_block_1_x2_2), .Y4_2(rotate_block_1_y4_2),
    .Y2_2(rotate_block_1_y2_2));
  or or_1 (or_1_out, move_left, ~move_right);  // OR_Gate
  move_block move_block_2 (
    .X1(rotate_block_1_x1_2), .X3(rotate_block_1_x3_2), .Y1(rotate_block_1_y1_2), .Y3(rotate_block_1_y3_2),
    .XC(rotate_block_1_xc_2), .X2(rotate_block_1_x2_2), .X4(rotate_block_1_x4_2), .YC(rotate_block_1_yc_2),
    .Y2(rotate_block_1_y2_2), .Y4(rotate_block_1_y4_2), .move_left(and_1_out), .move_right(and_2_out),
    .X1_2(move_block_2_x1_2), .X3_2(move_block_2_x3_2), .Y1_2(move_block_2_y1_2), .Y3_2(move_block_2_y3_2),
    .XC_2(move_block_2_xc_2), .X2_2(move_block_2_x2_2), .X4_2(move_block_2_x4_2), .YC_2(move_block_2_yc_2),
    .Y2_2(move_block_2_y2_2), .Y4_2(move_block_2_y4_2));
  and and_1 (and_1_out, rotate_block_1_x1_2[0], or_1_out);
  and and_2 (and_2_out, rotate_block_1_x1_2[0], move_right);
  drop_block drop_block_1 (
    .X1(move_block_2_x1_2), .Y1(move_block_2_y1_2), .X2(move_block_2_x2_2), .Y2(move_block_2_y2_2),
    .X3(move_block_2_x3_2), .Y3(move_block_2_y3_2), .X4(move_block_2_x4_2), .Y4(move_block_2_y4_2),
    .X1_2(X1_2), .Y1_2(Y1_2), .X2_2(X2_2), .Y2_2(Y2_2), .X3_2(X3_2), .Y3_2(Y3_2), .X4_2(X4_2), .Y4_2(Y4_2),
    .Dropped(Dropped), .XC_2(XC_2), .YC(move_block_2_yc_2), .YC_2(YC_2), .XC(move_block_2_xc_2));
endmodule

module _8bit_inc (
  input  [7:0] in_1,
  output [7:0] out_2
);

  Adder adder_1 (.a(in_1), .b(8'h1), .out(out_2));  // open: cin, cout
endmodule

module _8bit_dec (
  input  [7:0] in_1,
  output [7:0] out_2
);

  Subtractor subtractor_1 (.a(in_1), .b(8'h1), .out(out_2));  // open: bin, bout
endmodule

module move_block (
  input  [7:0] X1,
  input  [7:0] X3,
  input  [7:0] Y1,
  input  [7:0] Y3,
  input  [7:0] X2,
  input  [7:0] X4,
  input  [7:0] Y2,
  input  [7:0] Y4,
  input  move_left,
  input  [7:0] XC,
  input  move_right,
  input  [7:0] YC,
  output [7:0] X1_2,
  output [7:0] X3_2,
  output [7:0] Y1_2,
  output [7:0] Y3_2,
  output [7:0] X2_2,
  output [7:0] X4_2,
  output [7:0] Y2_2,
  output [7:0] Y4_2,
  output [7:0] XC_2,
  output [7:0] YC_2
);

  wire and_1_out, and_2_out, and_3_out, and_4_out, and_5_out, and_6_out, and_7_out, and_8_out, col,
       comparator_1_eq, comparator_2_eq, comparator_3_eq, comparator_4_eq, comparator_5_eq, comparator_6_eq,
       comparator_7_eq, comparator_8_eq;
  wire [7:0] multiplexer_1_out, multiplexer_2_out, multiplexer_6_out, multiplexer_8_out, multiplexer_10_out,
       n8bit_dec_1_out_2, n8bit_dec_2_out_2, n8bit_dec_3_out_2, n8bit_dec_4_out_2, n8bit_dec_5_out_2,
       n8bit_inc_1_out_2, n8bit_inc_2_out_2, n8bit_inc_3_out_2, n8bit_inc_4_out_2, n8bit_inc_5_out_2;

  _8bit_inc u_8bit_inc_1 (.in_1(X1), .out_2(n8bit_inc_1_out_2));
  Multiplexer #(.select(2), .width(8), .enable("false")) multiplexer_1 (
    .in0(X1), .in1(n8bit_inc_1_out_2), .in2(n8bit_dec_1_out_2), .in3(X1), .out(multiplexer_1_out),
    .sel({move_left, move_right}));
  _8bit_dec u_8bit_dec_1 (.in_1(X1), .out_2(n8bit_dec_1_out_2));
  _8bit_inc u_8bit_inc_2 (.in_1(X2), .out_2(n8bit_inc_2_out_2));
  _8bit_dec u_8bit_dec_2 (.in_1(X2), .out_2(n8bit_dec_2_out_2));
  Multiplexer #(.select(2), .width(8), .enable("false")) multiplexer_2 (
    .in0(X2), .in1(n8bit_inc_2_out_2), .in2(n8bit_dec_2_out_2), .in3(X2), .out(multiplexer_2_out),
    .sel({move_left, move_right}));
  Comparator comparator_1 (.a(X1), .b({8{1'b0}}), .eq(comparator_1_eq));  // open: gt, lt
  and and_1 (and_1_out, comparator_1_eq, move_left);
  Comparator comparator_2 (.a(X1), .b(8'h1e), .eq(comparator_2_eq));  // open: gt, lt
  and and_2 (and_2_out, comparator_2_eq, move_right);
  Comparator comparator_3 (.a(X2), .b({8{1'b0}}), .eq(comparator_3_eq));  // open: gt, lt
  and and_3 (and_3_out, comparator_3_eq, move_left);
  Comparator comparator_4 (.a(X2), .b(8'h1e), .eq(comparator_4_eq));  // open: gt, lt
  and and_4 (and_4_out, comparator_4_eq, move_right);
  Comparator comparator_5 (.a(X3), .b({8{1'b0}}), .eq(comparator_5_eq));  // open: gt, lt
  and and_5 (and_5_out, comparator_5_eq, move_left);
  Comparator comparator_6 (.a(X3), .b(8'h1e), .eq(comparator_6_eq));  // open: gt, lt
  and and_6 (and_6_out, comparator_6_eq, move_right);
  Comparator comparator_7 (.a(X4), .b({8{1'b0}}), .eq(comparator_7_eq));  // open: gt, lt
  and and_7 (and_7_out, comparator_7_eq, move_left);
  Comparator comparator_8 (.a(X4), .b(8'h1e), .eq(comparator_8_eq));  // open: gt, lt
  and and_8 (and_8_out, comparator_8_eq, move_right);
  Multiplexer #(.width(8), .enable("false")) multiplexer_3 (.in0(multiplexer_1_out), .in1(X1), .out(X1_2), .sel(col));
  Multiplexer #(.width(8), .enable("false")) multiplexer_4 (.in0(multiplexer_2_out), .in1(X2), .out(X2_2), .sel(col));
  or or_1 (col, and_1_out, and_2_out, and_3_out, and_4_out, and_5_out, and_6_out, and_7_out, and_8_out);
  _8bit_inc u_8bit_inc_3 (.in_1(X3), .out_2(n8bit_inc_3_out_2));
  _8bit_dec u_8bit_dec_3 (.in_1(X3), .out_2(n8bit_dec_3_out_2));
  _8bit_inc u_8bit_inc_4 (.in_1(X4), .out_2(n8bit_inc_4_out_2));
  _8bit_dec u_8bit_dec_4 (.in_1(X4), .out_2(n8bit_dec_4_out_2));
  _8bit_inc u_8bit_inc_5 (.in_1(XC), .out_2(n8bit_inc_5_out_2));
  _8bit_dec u_8bit_dec_5 (.in_1(XC), .out_2(n8bit_dec_5_out_2));
  Multiplexer #(.width(8), .enable("false")) multiplexer_5 (.in0(multiplexer_6_out), .in1(X3), .out(X3_2), .sel(col));
  Multiplexer #(.select(2), .width(8), .enable("false")) multiplexer_6 (
    .in0(X3), .in1(n8bit_inc_3_out_2), .in2(n8bit_dec_3_out_2), .in3(X3), .out(multiplexer_6_out),
    .sel({move_left, move_right}));
  Multiplexer #(.width(8), .enable("false")) multiplexer_7 (.in0(multiplexer_8_out), .in1(X4), .out(X4_2), .sel(col));
  Multiplexer #(.select(2), .width(8), .enable("false")) multiplexer_8 (
    .in0(X4), .in1(n8bit_inc_4_out_2), .in2(n8bit_dec_4_out_2), .in3(X4), .out(multiplexer_8_out),
    .sel({move_left, move_right}));
  Multiplexer #(.width(8), .enable("false")) multiplexer_9 (.in0(multiplexer_10_out), .in1(XC), .out(XC_2), .sel(col));
  Multiplexer #(.select(2), .width(8), .enable("false")) multiplexer_10 (
    .in0(XC), .in1(n8bit_inc_5_out_2), .in2(n8bit_dec_5_out_2), .in3(XC), .out(multiplexer_10_out),
    .sel({move_left, move_right}));

  assign Y1_2 = Y1;
  assign Y2_2 = Y2;
  assign Y3_2 = Y3;
  assign Y4_2 = Y4;
  assign YC_2 = YC;

  // Other names for the same wires on the sheet: side[1:0] = {move_left, move_right}
endmodule

module rotate_block (
  input  rotate_left,
  input  rotate_right,
  input  [7:0] XC,
  input  [7:0] YC,
  input  [7:0] X1,
  input  [7:0] X3,
  input  [7:0] Y1,
  input  [7:0] Y3,
  input  [7:0] X2,
  input  [7:0] X4,
  input  [7:0] Y2,
  input  [7:0] Y4,
  output [7:0] XC_2,
  output [7:0] YC_2,
  output [7:0] X1_2,
  output [7:0] X3_2,
  output [7:0] Y1_2,
  output [7:0] Y3_2,
  output [7:0] X2_2,
  output [7:0] X4_2,
  output [7:0] Y2_2,
  output [7:0] Y4_2
);

  wire col, comparator_1_eq, comparator_1_gt, comparator_2_eq, comparator_2_gt, comparator_3_eq,
       comparator_3_gt, comparator_4_eq, comparator_4_gt, comparator_5_lt, comparator_6_lt, comparator_7_lt,
       comparator_8_lt, comparator_9_eq, comparator_9_gt, comparator_10_eq, comparator_10_gt,
       comparator_11_eq, comparator_11_gt, comparator_12_eq, comparator_12_gt, not_1_out, not_2_out,
       not_3_out, not_4_out, or_1_out, or_2_out, or_4_out;
  wire [7:0] n8bit_rotatel_1_x_2, n8bit_rotatel_1_y_2, n8bit_rotatel_2_x_2, n8bit_rotatel_2_y_2,
       n8bit_rotatel_3_x_2, n8bit_rotatel_3_y_2, n8bit_rotatel_4_x_2, n8bit_rotatel_4_y_2,
       n8bit_rotater_1_x_2, n8bit_rotater_1_y_2, n8bit_rotater_2_x_2, n8bit_rotater_2_y_2,
       n8bit_rotater_3_x_2, n8bit_rotater_3_y_2, n8bit_rotater_4_x_2, n8bit_rotater_4_y_2, X1_t, X2_t, X3_t,
       X4_t, Y1_t, Y2_t, Y3_t, Y4_t;

  _8bit_rotatel u_8bit_rotatel_1 (
    .Y(Y1), .YC(YC), .X(X1), .XC(XC), .X_2(n8bit_rotatel_1_x_2), .Y_2(n8bit_rotatel_1_y_2));
  _8bit_rotater u_8bit_rotater_1 (
    .Y(Y1), .YC(YC), .X(X1), .XC(XC), .X_2(n8bit_rotater_1_x_2), .Y_2(n8bit_rotater_1_y_2));
  _8bit_rotatel u_8bit_rotatel_2 (
    .Y(Y2), .YC(YC), .X(X2), .XC(XC), .X_2(n8bit_rotatel_2_x_2), .Y_2(n8bit_rotatel_2_y_2));
  _8bit_rotater u_8bit_rotater_2 (
    .Y(Y2), .YC(YC), .X(X2), .XC(XC), .X_2(n8bit_rotater_2_x_2), .Y_2(n8bit_rotater_2_y_2));
  Multiplexer #(.select(2), .width(8), .enable("false")) multiplexer_1 (
    .in0(X1), .in1(n8bit_rotatel_1_x_2), .in2(n8bit_rotater_1_x_2), .in3(X1), .out(X1_t),
    .sel({rotate_right, rotate_left}));
  Multiplexer #(.select(2), .width(8), .enable("false")) multiplexer_2 (
    .in0(Y1), .in1(n8bit_rotatel_1_y_2), .in2(n8bit_rotater_1_y_2), .in3(Y1), .out(Y1_t),
    .sel({rotate_right, rotate_left}));
  Multiplexer #(.select(2), .width(8), .enable("false")) multiplexer_3 (
    .in0(X2), .in1(n8bit_rotatel_2_x_2), .in2(n8bit_rotater_2_x_2), .in3(X2), .out(X2_t),
    .sel({rotate_right, rotate_left}));
  Multiplexer #(.select(2), .width(8), .enable("false")) multiplexer_4 (
    .in0(Y2), .in1(n8bit_rotatel_2_y_2), .in2(n8bit_rotater_2_y_2), .in3(Y2), .out(Y2_t),
    .sel({rotate_right, rotate_left}));
  Multiplexer #(.width(8), .enable("false")) multiplexer_5 (.in0(X1), .in1(X1_t), .out(X1_2), .sel(not_1_out));
  not not_1 (not_1_out, col);
  Multiplexer #(.width(8), .enable("false")) multiplexer_6 (.in0(Y1_t), .in1(Y1), .out(Y1_2), .sel(col));
  Multiplexer #(.width(8), .enable("false")) multiplexer_7 (.in0(X2), .in1(X2_t), .out(X2_2), .sel(not_2_out));
  not not_2 (not_2_out, col);
  Multiplexer #(.width(8), .enable("false")) multiplexer_8 (.in0(Y2_t), .in1(Y2), .out(Y2_2), .sel(col));
  _8bit_rotatel u_8bit_rotatel_3 (
    .Y(Y3), .YC(YC), .X(X3), .XC(XC), .X_2(n8bit_rotatel_3_x_2), .Y_2(n8bit_rotatel_3_y_2));
  _8bit_rotater u_8bit_rotater_3 (
    .Y(Y3), .YC(YC), .X(X3), .XC(XC), .X_2(n8bit_rotater_3_x_2), .Y_2(n8bit_rotater_3_y_2));
  _8bit_rotatel u_8bit_rotatel_4 (
    .Y(Y4), .YC(YC), .X(X4), .XC(XC), .X_2(n8bit_rotatel_4_x_2), .Y_2(n8bit_rotatel_4_y_2));
  _8bit_rotater u_8bit_rotater_4 (
    .Y(Y4), .YC(YC), .X(X4), .XC(XC), .X_2(n8bit_rotater_4_x_2), .Y_2(n8bit_rotater_4_y_2));
  Multiplexer #(.width(8), .enable("false")) multiplexer_9 (.in0(X3), .in1(X3_t), .out(X3_2), .sel(not_3_out));
  Multiplexer #(.select(2), .width(8), .enable("false")) multiplexer_10 (
    .in0(X3), .in1(n8bit_rotatel_3_x_2), .in2(n8bit_rotater_3_x_2), .in3(X3), .out(X3_t),
    .sel({rotate_right, rotate_left}));
  not not_3 (not_3_out, col);
  Multiplexer #(.select(2), .width(8), .enable("false")) multiplexer_11 (
    .in0(Y3), .in1(n8bit_rotatel_3_y_2), .in2(n8bit_rotater_3_y_2), .in3(Y3), .out(Y3_t),
    .sel({rotate_right, rotate_left}));
  Multiplexer #(.width(8), .enable("false")) multiplexer_12 (.in0(Y3_t), .in1(Y3), .out(Y3_2), .sel(col));
  Multiplexer #(.width(8), .enable("false")) multiplexer_13 (.in0(X4), .in1(X4_t), .out(X4_2), .sel(not_4_out));
  Multiplexer #(.select(2), .width(8), .enable("false")) multiplexer_14 (
    .in0(X4), .in1(n8bit_rotatel_4_x_2), .in2(n8bit_rotater_4_x_2), .in3(X4), .out(X4_t),
    .sel({rotate_right, rotate_left}));
  not not_4 (not_4_out, col);
  Multiplexer #(.select(2), .width(8), .enable("false")) multiplexer_15 (
    .in0(Y4), .in1(n8bit_rotatel_4_y_2), .in2(n8bit_rotater_4_y_2), .in3(Y4), .out(Y4_t),
    .sel({rotate_right, rotate_left}));
  Multiplexer #(.width(8), .enable("false")) multiplexer_16 (.in0(Y4_t), .in1(Y4), .out(Y4_2), .sel(col));
  Comparator comparator_1 (.a(Y1_t), .b(8'h2e), .gt(comparator_1_gt), .eq(comparator_1_eq));  // open: lt
  Comparator comparator_2 (.a(Y2_t), .b(8'h2e), .gt(comparator_2_gt), .eq(comparator_2_eq));  // open: lt
  Comparator comparator_3 (.a(Y3_t), .b(8'h2e), .gt(comparator_3_gt), .eq(comparator_3_eq));  // open: lt
  Comparator comparator_4 (.a(Y4_t), .b(8'h2e), .gt(comparator_4_gt), .eq(comparator_4_eq));  // open: lt
  Comparator comparator_5 (.a(X1_t), .b({8{1'b0}}), .lt(comparator_5_lt));  // open: gt, eq
  Comparator comparator_6 (.a(X2_t), .b({8{1'b0}}), .lt(comparator_6_lt));  // open: gt, eq
  or or_1 (or_1_out, comparator_5_lt, comparator_6_lt, comparator_7_lt, comparator_8_lt);
  Comparator comparator_7 (.a(X3_t), .b({8{1'b0}}), .lt(comparator_7_lt));  // open: gt, eq
  Comparator comparator_8 (.a(X4_t), .b({8{1'b0}}), .lt(comparator_8_lt));  // open: gt, eq
  Comparator comparator_9 (.a(X1_t), .b(8'h1e), .gt(comparator_9_gt), .eq(comparator_9_eq));  // open: lt
  Comparator comparator_10 (.a(X2_t), .b(8'h1e), .gt(comparator_10_gt), .eq(comparator_10_eq));  // open: lt
  Comparator comparator_11 (.a(X3_t), .b(8'h1e), .gt(comparator_11_gt), .eq(comparator_11_eq));  // open: lt
  Comparator comparator_12 (.a(X4_t), .b(8'h1e), .gt(comparator_12_gt), .eq(comparator_12_eq));  // open: lt
  or or_2 (or_2_out, comparator_1_gt, comparator_1_eq, comparator_2_gt, comparator_2_eq, comparator_3_gt, comparator_3_eq, comparator_4_gt, comparator_4_eq);
  or or_3 (col, or_2_out, or_1_out, or_4_out);
  or or_4 (or_4_out, comparator_9_gt, comparator_9_eq, comparator_10_gt, comparator_10_eq, comparator_11_gt, comparator_11_eq, comparator_12_gt, comparator_12_eq);

  assign XC_2 = XC;
  assign YC_2 = YC;

  // Other names for the same wires on the sheet: side[1:0] = {rotate_right, rotate_left}
endmodule

module drop_block (
  input  [7:0] X1,
  input  [7:0] Y1,
  input  [7:0] X2,
  input  [7:0] Y2,
  input  [7:0] X3,
  input  [7:0] Y3,
  input  [7:0] X4,
  input  [7:0] Y4,
  input  [7:0] XC,
  input  [7:0] YC,
  output [7:0] X1_2,
  output [7:0] Y1_2,
  output [7:0] X2_2,
  output [7:0] Y2_2,
  output [7:0] X3_2,
  output [7:0] Y3_2,
  output [7:0] X4_2,
  output [7:0] Y4_2,
  output [7:0] XC_2,
  output [7:0] YC_2,
  output Dropped
);

  wire comparator_1_eq, comparator_2_eq, comparator_3_eq, comparator_4_eq;
  wire [7:0] n8bit_inc_1_out_2, n8bit_inc_2_out_2, n8bit_inc_3_out_2, n8bit_inc_4_out_2, n8bit_inc_5_out_2;

  _8bit_inc u_8bit_inc_1 (.in_1(Y1), .out_2(n8bit_inc_1_out_2));
  _8bit_inc u_8bit_inc_2 (.in_1(Y2), .out_2(n8bit_inc_2_out_2));
  _8bit_inc u_8bit_inc_3 (.in_1(Y3), .out_2(n8bit_inc_3_out_2));
  _8bit_inc u_8bit_inc_4 (.in_1(Y4), .out_2(n8bit_inc_4_out_2));
  _8bit_inc u_8bit_inc_5 (.in_1(YC), .out_2(n8bit_inc_5_out_2));
  Comparator comparator_1 (.a(Y1), .b(8'h2e), .eq(comparator_1_eq));  // open: gt, lt
  Comparator comparator_2 (.a(Y2), .b(8'h2e), .eq(comparator_2_eq));  // open: gt, lt
  Comparator comparator_3 (.a(Y3), .b(8'h2e), .eq(comparator_3_eq));  // open: gt, lt
  Comparator comparator_4 (.a(Y4), .b(8'h2e), .eq(comparator_4_eq));  // open: gt, lt
  Multiplexer #(.width(8), .enable("false")) multiplexer_1 (
    .in0(n8bit_inc_1_out_2), .in1(Y1), .out(Y1_2), .sel(Dropped));
  Multiplexer #(.width(8), .enable("false")) multiplexer_2 (
    .in0(n8bit_inc_2_out_2), .in1(Y2), .out(Y2_2), .sel(Dropped));
  Multiplexer #(.width(8), .enable("false")) multiplexer_3 (
    .in0(n8bit_inc_3_out_2), .in1(Y3), .out(Y3_2), .sel(Dropped));
  Multiplexer #(.width(8), .enable("false")) multiplexer_4 (
    .in0(n8bit_inc_4_out_2), .in1(Y4), .out(Y4_2), .sel(Dropped));
  Multiplexer #(.width(8), .enable("false")) multiplexer_5 (
    .in0(n8bit_inc_5_out_2), .in1(YC), .out(YC_2), .sel(Dropped));
  or or_1 (Dropped, comparator_1_eq, comparator_2_eq, comparator_3_eq, comparator_4_eq);

  assign X1_2 = X1;
  assign X2_2 = X2;
  assign X3_2 = X3;
  assign X4_2 = X4;
  assign XC_2 = XC;
endmodule

module _8bit_rotatel (
  input  [7:0] Y,
  input  [7:0] XC,
  input  [7:0] YC,
  input  [7:0] X,
  output [7:0] X_2,
  output [7:0] Y_2
);

  wire [7:0] adder_1_out, subtractor_1_out, subtractor_2_out;

  Subtractor subtractor_1 (.a(XC), .b(YC), .out(subtractor_1_out));  // open: bin, bout
  Adder adder_1 (.a(YC), .b(XC), .out(adder_1_out));  // open: cin, cout
  Adder adder_2 (.a(Y), .b(subtractor_1_out), .out(X_2));  // open: cin, cout
  Subtractor subtractor_2 (.a(adder_1_out), .b(X), .out(subtractor_2_out));  // open: bin, bout
  Subtractor subtractor_3 (.a(subtractor_2_out), .b(8'h2), .out(Y_2));  // open: bin, bout

  // Notes on the sheet:
  //   YN = XC + YC - X - 2
  //   XN = Y - YC + XC
endmodule

module _8bit_rotater (
  input  [7:0] Y,
  input  [7:0] YC,
  input  [7:0] XC,
  input  [7:0] X,
  output [7:0] X_2,
  output [7:0] Y_2
);

  wire [7:0] adder_1_out, subtractor_1_out, subtractor_2_out;

  Adder adder_1 (.a(XC), .b(YC), .out(adder_1_out));  // open: cin, cout
  Subtractor subtractor_1 (.a(adder_1_out), .b(Y), .out(subtractor_1_out));  // open: bin, bout
  Subtractor subtractor_2 (.a(YC), .b(XC), .out(subtractor_2_out));  // open: bin, bout
  Adder adder_2 (.a(subtractor_2_out), .b(X), .out(Y_2));  // open: cin, cout
  Subtractor subtractor_3 (.a(subtractor_1_out), .b(8'h2), .out(X_2));  // open: bin, bout

  // Notes on the sheet:
  //   XN = XC + YC - Y - 2
  //   YN = YC + X - XC
endmodule

module test (
);

  wire clock_1_out, tetris_1_p1, tetris_1_p2, tetris_1_p3, tetris_1_p4, tetris_1_p5;
  wire [31:0] tetris_1_p7, tetris_1_p8, tetris_1_p9, tetris_1_p10, tetris_1_p11, tetris_1_p12, tetris_1_p13,
       tetris_1_p14, tetris_1_p15, tetris_1_p16, tetris_1_p17, tetris_1_p18, tetris_1_p19, tetris_1_p20,
       tetris_1_p21, tetris_1_p22, tetris_1_p23, tetris_1_p24, tetris_1_p25, tetris_1_p26, tetris_1_p27,
       tetris_1_p28, tetris_1_p29, tetris_1_p30, tetris_1_p31, tetris_1_p32, tetris_1_p33, tetris_1_p34,
       tetris_1_p35, tetris_1_p36, tetris_1_p37, tetris_1_p38, tetris_1_p39, tetris_1_p40, tetris_1_p41,
       tetris_1_p42, tetris_1_p43, tetris_1_p44, tetris_1_p45, tetris_1_p46, tetris_1_p47, tetris_1_p48,
       tetris_1_p49, tetris_1_p50, tetris_1_p51, tetris_1_p52, tetris_1_p53, tetris_1_p54;

  Clock clock_1 (.out(clock_1_out));
  DotMatrix #(.inputtype("row"), .matrixcols(32), .matrixrows(24)) dotmatrix_1 (
    .row0(tetris_1_p8), .row1(tetris_1_p9), .row2(tetris_1_p10), .row3(tetris_1_p11), .row4(tetris_1_p12),
    .row5(tetris_1_p13), .row6(tetris_1_p14), .row7(tetris_1_p15), .row8(tetris_1_p16), .row9(tetris_1_p17),
    .row10(tetris_1_p18), .row11(tetris_1_p19), .row12(tetris_1_p20), .row13(tetris_1_p21),
    .row14(tetris_1_p22), .row15(tetris_1_p23), .row16(tetris_1_p24), .row17(tetris_1_p25),
    .row18(tetris_1_p26), .row19(tetris_1_p27), .row20(tetris_1_p28), .row21(tetris_1_p29),
    .row22(tetris_1_p30), .row23(tetris_1_p31));
  // tetris tetris_1: pin names not known; wires that end beside it: tetris_1_p1, tetris_1_p2, tetris_1_p3, tetris_1_p4, tetris_1_p5, clock_1_out, tetris_1_p7, tetris_1_p8, tetris_1_p9, tetris_1_p10, tetris_1_p11, tetris_1_p12, tetris_1_p13, tetris_1_p14, tetris_1_p15, tetris_1_p16, tetris_1_p17, tetris_1_p18, tetris_1_p19, tetris_1_p20, tetris_1_p21, tetris_1_p22, tetris_1_p23, tetris_1_p24, tetris_1_p25, tetris_1_p26, tetris_1_p27, tetris_1_p28, tetris_1_p29, tetris_1_p30, tetris_1_p31, tetris_1_p32, tetris_1_p33, tetris_1_p34, tetris_1_p35, tetris_1_p36, tetris_1_p37, tetris_1_p38, tetris_1_p39, tetris_1_p40, tetris_1_p41, tetris_1_p42, tetris_1_p43, tetris_1_p44, tetris_1_p45, tetris_1_p46, tetris_1_p47, tetris_1_p48, tetris_1_p49, tetris_1_p50, tetris_1_p51, tetris_1_p52, tetris_1_p53, tetris_1_p54
  Button button_1 (.out(tetris_1_p1));
  Button button_2 (.out(tetris_1_p2));
  Button button_3 (.out(tetris_1_p3));
  Button button_4 (.out(tetris_1_p4));
  Button button_5 (.out(tetris_1_p5));
  DotMatrix #(.inputtype("row"), .matrixcols(32), .matrixrows(24)) dotmatrix_2 (
    .row0(tetris_1_p32), .row1(tetris_1_p33), .row2(tetris_1_p34), .row3(tetris_1_p35), .row4(tetris_1_p36),
    .row5(tetris_1_p37), .row6(tetris_1_p38), .row7(tetris_1_p39), .row8(tetris_1_p40), .row9(tetris_1_p41),
    .row10(tetris_1_p42), .row11(tetris_1_p43), .row12(tetris_1_p44), .row13(tetris_1_p45),
    .row14(tetris_1_p46), .row15(tetris_1_p47), .row16(tetris_1_p48), .row17(tetris_1_p49),
    .row18(tetris_1_p50), .row19(tetris_1_p51), .row20(tetris_1_p52), .row21(tetris_1_p53),
    .row22(tetris_1_p54), .row23(tetris_1_p7));
endmodule

module _32bit_DMX_6sel (
  input  [31:0] in_1,
  input  [5:0] in_2,
  output [31:0] out_3,
  output [31:0] out_4,
  output [31:0] out_5,
  output [31:0] out_6,
  output [31:0] out_7,
  output [31:0] out_8,
  output [31:0] out_9,
  output [31:0] out_10,
  output [31:0] out_11,
  output [31:0] out_12,
  output [31:0] out_13,
  output [31:0] out_14,
  output [31:0] out_15,
  output [31:0] out_16,
  output [31:0] out_17,
  output [31:0] out_18,
  output [31:0] out_19,
  output [31:0] out_20,
  output [31:0] out_21,
  output [31:0] out_22,
  output [31:0] out_23,
  output [31:0] out_24,
  output [31:0] out_25,
  output [31:0] out_26,
  output [31:0] out_27,
  output [31:0] out_28,
  output [31:0] out_29,
  output [31:0] out_30,
  output [31:0] out_31,
  output [31:0] out_32,
  output [31:0] out_33,
  output [31:0] out_34,
  output [31:0] out_35,
  output [31:0] out_36,
  output [31:0] out_37,
  output [31:0] out_38,
  output [31:0] out_39,
  output [31:0] out_40,
  output [31:0] out_41,
  output [31:0] out_42,
  output [31:0] out_43,
  output [31:0] out_44,
  output [31:0] out_45,
  output [31:0] out_46,
  output [31:0] out_47,
  output [31:0] out_48,
  output [31:0] out_49,
  output [31:0] out_50,
  output [31:0] out_51,
  output [31:0] out_52,
  output [31:0] out_53,
  output [31:0] out_54,
  output [31:0] out_55,
  output [31:0] out_56,
  output [31:0] out_57,
  output [31:0] out_58,
  output [31:0] out_59,
  output [31:0] out_60,
  output [31:0] out_61,
  output [31:0] out_62,
  output [31:0] out_63,
  output [31:0] out_64,
  output [31:0] out_65,
  output [31:0] out_66
);

  wire [31:0] demultiplexer_2_out0, demultiplexer_2_out1;

  Demultiplexer #(.select(5), .width(32), .enable("false")) demultiplexer_1 (
    .out0(out_3), .out1(out_4), .out2(out_5), .out3(out_6), .out4(out_7), .out5(out_8), .out6(out_9),
    .out7(out_10), .out8(out_11), .out9(out_12), .out10(out_13), .out11(out_14), .out12(out_15),
    .out13(out_16), .out14(out_17), .out15(out_18), .out16(out_19), .out17(out_20), .out18(out_21),
    .out19(out_22), .out20(out_23), .out21(out_24), .out22(out_25), .out23(out_26), .out24(out_27),
    .out25(out_28), .out26(out_29), .out27(out_30), .out28(out_31), .out29(out_32), .out30(out_33),
    .out31(out_34), .in(demultiplexer_2_out0), .sel(in_2[4:0]));
  Demultiplexer #(.width(32), .enable("false")) demultiplexer_2 (
    .out0(demultiplexer_2_out0), .out1(demultiplexer_2_out1), .in(in_1), .sel(in_2[5]));
  Demultiplexer #(.select(5), .width(32), .enable("false")) demultiplexer_3 (
    .out0(out_35), .out1(out_36), .out2(out_37), .out3(out_38), .out4(out_39), .out5(out_40), .out6(out_41),
    .out7(out_42), .out8(out_43), .out9(out_44), .out10(out_45), .out11(out_46), .out12(out_47),
    .out13(out_48), .out14(out_49), .out15(out_50), .out16(out_51), .out17(out_52), .out18(out_53),
    .out19(out_54), .out20(out_55), .out21(out_56), .out22(out_57), .out23(out_58), .out24(out_59),
    .out25(out_60), .out26(out_61), .out27(out_62), .out28(out_63), .out29(out_64), .out30(out_65),
    .out31(out_66), .in(demultiplexer_2_out1), .sel(in_2[4:0]));
endmodule

module block_output (
  input  [7:0] X1,
  input  [7:0] Y1,
  input  [7:0] X2,
  input  [7:0] Y2,
  input  [7:0] X3,
  input  [7:0] Y3,
  input  [7:0] X4,
  input  [7:0] Y4,
  output [31:0] out_9,
  output [31:0] out_10,
  output [31:0] out_11,
  output [31:0] out_12,
  output [31:0] out_13,
  output [31:0] out_14,
  output [31:0] out_15,
  output [31:0] out_16,
  output [31:0] out_17,
  output [31:0] out_18,
  output [31:0] out_19,
  output [31:0] out_20,
  output [31:0] out_21,
  output [31:0] out_22,
  output [31:0] out_23,
  output [31:0] out_24,
  output [31:0] out_25,
  output [31:0] out_26,
  output [31:0] out_27,
  output [31:0] out_28,
  output [31:0] out_29,
  output [31:0] out_30,
  output [31:0] out_31,
  output [31:0] out_32,
  output [31:0] out_33,
  output [31:0] out_34,
  output [31:0] out_35,
  output [31:0] out_36,
  output [31:0] out_37,
  output [31:0] out_38,
  output [31:0] out_39,
  output [31:0] out_40,
  output [31:0] out_41,
  output [31:0] out_42,
  output [31:0] out_43,
  output [31:0] out_44,
  output [31:0] out_45,
  output [31:0] out_46,
  output [31:0] out_47,
  output [31:0] out_48,
  output [31:0] out_49,
  output [31:0] out_50,
  output [31:0] out_51,
  output [31:0] out_52,
  output [31:0] out_53,
  output [31:0] out_54,
  output [31:0] out_55,
  output [31:0] out_56
);

  wire [31:0] n8bit_to_32str_1_out_2, n8bit_to_32str_2_out_2, n8bit_to_32str_3_out_2, n8bit_to_32str_4_out_2,
       n32bit_dmx_6sel_1_out_3, n32bit_dmx_6sel_1_out_4, n32bit_dmx_6sel_1_out_5, n32bit_dmx_6sel_1_out_6,
       n32bit_dmx_6sel_1_out_7, n32bit_dmx_6sel_1_out_8, n32bit_dmx_6sel_1_out_9, n32bit_dmx_6sel_1_out_10,
       n32bit_dmx_6sel_1_out_11, n32bit_dmx_6sel_1_out_12, n32bit_dmx_6sel_1_out_13,
       n32bit_dmx_6sel_1_out_14, n32bit_dmx_6sel_1_out_15, n32bit_dmx_6sel_1_out_16,
       n32bit_dmx_6sel_1_out_17, n32bit_dmx_6sel_1_out_18, n32bit_dmx_6sel_1_out_19,
       n32bit_dmx_6sel_1_out_20, n32bit_dmx_6sel_1_out_21, n32bit_dmx_6sel_1_out_22,
       n32bit_dmx_6sel_1_out_23, n32bit_dmx_6sel_1_out_24, n32bit_dmx_6sel_1_out_25,
       n32bit_dmx_6sel_1_out_26, n32bit_dmx_6sel_1_out_27, n32bit_dmx_6sel_1_out_28,
       n32bit_dmx_6sel_1_out_29, n32bit_dmx_6sel_1_out_30, n32bit_dmx_6sel_1_out_31,
       n32bit_dmx_6sel_1_out_32, n32bit_dmx_6sel_1_out_33, n32bit_dmx_6sel_1_out_34,
       n32bit_dmx_6sel_1_out_35, n32bit_dmx_6sel_1_out_36, n32bit_dmx_6sel_1_out_37,
       n32bit_dmx_6sel_1_out_38, n32bit_dmx_6sel_1_out_39, n32bit_dmx_6sel_1_out_40,
       n32bit_dmx_6sel_1_out_41, n32bit_dmx_6sel_1_out_42, n32bit_dmx_6sel_1_out_43,
       n32bit_dmx_6sel_1_out_44, n32bit_dmx_6sel_1_out_45, n32bit_dmx_6sel_1_out_46,
       n32bit_dmx_6sel_1_out_47, n32bit_dmx_6sel_1_out_48, n32bit_dmx_6sel_1_out_49,
       n32bit_dmx_6sel_1_out_50, n32bit_dmx_6sel_2_out_3, n32bit_dmx_6sel_2_out_4, n32bit_dmx_6sel_2_out_5,
       n32bit_dmx_6sel_2_out_6, n32bit_dmx_6sel_2_out_7, n32bit_dmx_6sel_2_out_8, n32bit_dmx_6sel_2_out_9,
       n32bit_dmx_6sel_2_out_10, n32bit_dmx_6sel_2_out_11, n32bit_dmx_6sel_2_out_12,
       n32bit_dmx_6sel_2_out_13, n32bit_dmx_6sel_2_out_14, n32bit_dmx_6sel_2_out_15,
       n32bit_dmx_6sel_2_out_16, n32bit_dmx_6sel_2_out_17, n32bit_dmx_6sel_2_out_18,
       n32bit_dmx_6sel_2_out_19, n32bit_dmx_6sel_2_out_20, n32bit_dmx_6sel_2_out_21,
       n32bit_dmx_6sel_2_out_22, n32bit_dmx_6sel_2_out_23, n32bit_dmx_6sel_2_out_24,
       n32bit_dmx_6sel_2_out_25, n32bit_dmx_6sel_2_out_26, n32bit_dmx_6sel_2_out_27,
       n32bit_dmx_6sel_2_out_28, n32bit_dmx_6sel_2_out_29, n32bit_dmx_6sel_2_out_30,
       n32bit_dmx_6sel_2_out_31, n32bit_dmx_6sel_2_out_32, n32bit_dmx_6sel_2_out_33,
       n32bit_dmx_6sel_2_out_34, n32bit_dmx_6sel_2_out_35, n32bit_dmx_6sel_2_out_36,
       n32bit_dmx_6sel_2_out_37, n32bit_dmx_6sel_2_out_38, n32bit_dmx_6sel_2_out_39,
       n32bit_dmx_6sel_2_out_40, n32bit_dmx_6sel_2_out_41, n32bit_dmx_6sel_2_out_42,
       n32bit_dmx_6sel_2_out_43, n32bit_dmx_6sel_2_out_44, n32bit_dmx_6sel_2_out_45,
       n32bit_dmx_6sel_2_out_46, n32bit_dmx_6sel_2_out_47, n32bit_dmx_6sel_2_out_48,
       n32bit_dmx_6sel_2_out_49, n32bit_dmx_6sel_2_out_50, n32bit_dmx_6sel_3_out_3, n32bit_dmx_6sel_3_out_4,
       n32bit_dmx_6sel_3_out_5, n32bit_dmx_6sel_3_out_6, n32bit_dmx_6sel_3_out_7, n32bit_dmx_6sel_3_out_8,
       n32bit_dmx_6sel_3_out_9, n32bit_dmx_6sel_3_out_10, n32bit_dmx_6sel_3_out_11, n32bit_dmx_6sel_3_out_12,
       n32bit_dmx_6sel_3_out_13, n32bit_dmx_6sel_3_out_14, n32bit_dmx_6sel_3_out_15,
       n32bit_dmx_6sel_3_out_16, n32bit_dmx_6sel_3_out_17, n32bit_dmx_6sel_3_out_18,
       n32bit_dmx_6sel_3_out_19, n32bit_dmx_6sel_3_out_20, n32bit_dmx_6sel_3_out_21,
       n32bit_dmx_6sel_3_out_22, n32bit_dmx_6sel_3_out_23, n32bit_dmx_6sel_3_out_24,
       n32bit_dmx_6sel_3_out_25, n32bit_dmx_6sel_3_out_26, n32bit_dmx_6sel_3_out_27,
       n32bit_dmx_6sel_3_out_28, n32bit_dmx_6sel_3_out_29, n32bit_dmx_6sel_3_out_30,
       n32bit_dmx_6sel_3_out_31, n32bit_dmx_6sel_3_out_32, n32bit_dmx_6sel_3_out_33,
       n32bit_dmx_6sel_3_out_34, n32bit_dmx_6sel_3_out_35, n32bit_dmx_6sel_3_out_36,
       n32bit_dmx_6sel_3_out_37, n32bit_dmx_6sel_3_out_38, n32bit_dmx_6sel_3_out_39,
       n32bit_dmx_6sel_3_out_40, n32bit_dmx_6sel_3_out_41, n32bit_dmx_6sel_3_out_42,
       n32bit_dmx_6sel_3_out_43, n32bit_dmx_6sel_3_out_44, n32bit_dmx_6sel_3_out_45,
       n32bit_dmx_6sel_3_out_46, n32bit_dmx_6sel_3_out_47, n32bit_dmx_6sel_3_out_48,
       n32bit_dmx_6sel_3_out_49, n32bit_dmx_6sel_3_out_50, n32bit_dmx_6sel_4_out_3, n32bit_dmx_6sel_4_out_4,
       n32bit_dmx_6sel_4_out_5, n32bit_dmx_6sel_4_out_6, n32bit_dmx_6sel_4_out_7, n32bit_dmx_6sel_4_out_8,
       n32bit_dmx_6sel_4_out_9, n32bit_dmx_6sel_4_out_10, n32bit_dmx_6sel_4_out_11, n32bit_dmx_6sel_4_out_12,
       n32bit_dmx_6sel_4_out_13, n32bit_dmx_6sel_4_out_14, n32bit_dmx_6sel_4_out_15,
       n32bit_dmx_6sel_4_out_16, n32bit_dmx_6sel_4_out_17, n32bit_dmx_6sel_4_out_18,
       n32bit_dmx_6sel_4_out_19, n32bit_dmx_6sel_4_out_20, n32bit_dmx_6sel_4_out_21,
       n32bit_dmx_6sel_4_out_22, n32bit_dmx_6sel_4_out_23, n32bit_dmx_6sel_4_out_24,
       n32bit_dmx_6sel_4_out_25, n32bit_dmx_6sel_4_out_26, n32bit_dmx_6sel_4_out_27,
       n32bit_dmx_6sel_4_out_28, n32bit_dmx_6sel_4_out_29, n32bit_dmx_6sel_4_out_30,
       n32bit_dmx_6sel_4_out_31, n32bit_dmx_6sel_4_out_32, n32bit_dmx_6sel_4_out_33,
       n32bit_dmx_6sel_4_out_34, n32bit_dmx_6sel_4_out_35, n32bit_dmx_6sel_4_out_36,
       n32bit_dmx_6sel_4_out_37, n32bit_dmx_6sel_4_out_38, n32bit_dmx_6sel_4_out_39,
       n32bit_dmx_6sel_4_out_40, n32bit_dmx_6sel_4_out_41, n32bit_dmx_6sel_4_out_42,
       n32bit_dmx_6sel_4_out_43, n32bit_dmx_6sel_4_out_44, n32bit_dmx_6sel_4_out_45,
       n32bit_dmx_6sel_4_out_46, n32bit_dmx_6sel_4_out_47, n32bit_dmx_6sel_4_out_48,
       n32bit_dmx_6sel_4_out_49, n32bit_dmx_6sel_4_out_50, or_1_out, or_2_out, or_3_out, or_4_out, or_5_out,
       or_6_out, or_7_out, or_8_out, or_9_out, or_10_out, or_11_out, or_12_out, or_13_out, or_14_out,
       or_15_out, or_16_out, or_17_out, or_18_out, or_19_out, or_20_out, or_21_out, or_22_out, or_23_out,
       or_24_out, or_25_out, or_26_out, or_27_out, or_28_out, or_29_out, or_30_out, or_31_out, or_32_out,
       or_33_out, or_34_out, or_35_out, or_36_out, or_37_out, or_38_out, or_39_out, or_40_out, or_41_out,
       or_42_out, or_43_out, or_44_out, or_45_out, or_46_out, or_47_out, or_48_out, or_49_out, or_50_out,
       or_51_out, or_52_out, or_53_out, or_54_out, or_55_out, or_56_out, or_57_out, or_58_out, or_59_out,
       or_60_out, or_61_out, or_62_out, or_63_out, or_64_out, or_65_out, or_66_out, or_67_out, or_68_out,
       or_69_out, or_70_out, or_71_out, or_72_out, or_73_out, or_74_out, or_75_out, or_76_out, or_77_out,
       or_78_out, or_79_out, or_80_out, or_81_out, or_82_out, or_83_out, or_84_out, or_85_out, or_86_out,
       or_87_out, or_88_out, or_89_out, or_90_out, or_91_out, or_92_out, or_93_out, or_94_out, or_95_out;

  _8bit_to_32str u_8bit_to_32str_1 (.in_1(X1), .out_2(n8bit_to_32str_1_out_2));
  _32bit_DMX_6sel u_32bit_dmx_6sel_1 (
    .in_1(n8bit_to_32str_1_out_2), .in_2(Y1[5:0]), .out_3(n32bit_dmx_6sel_1_out_3),
    .out_4(n32bit_dmx_6sel_1_out_4), .out_5(n32bit_dmx_6sel_1_out_5), .out_6(n32bit_dmx_6sel_1_out_6),
    .out_7(n32bit_dmx_6sel_1_out_7), .out_8(n32bit_dmx_6sel_1_out_8), .out_9(n32bit_dmx_6sel_1_out_9),
    .out_10(n32bit_dmx_6sel_1_out_10), .out_11(n32bit_dmx_6sel_1_out_11), .out_12(n32bit_dmx_6sel_1_out_12),
    .out_13(n32bit_dmx_6sel_1_out_13), .out_14(n32bit_dmx_6sel_1_out_14), .out_15(n32bit_dmx_6sel_1_out_15),
    .out_16(n32bit_dmx_6sel_1_out_16), .out_17(n32bit_dmx_6sel_1_out_17), .out_18(n32bit_dmx_6sel_1_out_18),
    .out_19(n32bit_dmx_6sel_1_out_19), .out_20(n32bit_dmx_6sel_1_out_20), .out_21(n32bit_dmx_6sel_1_out_21),
    .out_22(n32bit_dmx_6sel_1_out_22), .out_23(n32bit_dmx_6sel_1_out_23), .out_24(n32bit_dmx_6sel_1_out_24),
    .out_25(n32bit_dmx_6sel_1_out_25), .out_26(n32bit_dmx_6sel_1_out_26), .out_27(n32bit_dmx_6sel_1_out_27),
    .out_28(n32bit_dmx_6sel_1_out_28), .out_29(n32bit_dmx_6sel_1_out_29), .out_30(n32bit_dmx_6sel_1_out_30),
    .out_31(n32bit_dmx_6sel_1_out_31), .out_32(n32bit_dmx_6sel_1_out_32), .out_33(n32bit_dmx_6sel_1_out_33),
    .out_34(n32bit_dmx_6sel_1_out_34), .out_35(n32bit_dmx_6sel_1_out_35), .out_36(n32bit_dmx_6sel_1_out_36),
    .out_37(n32bit_dmx_6sel_1_out_37), .out_38(n32bit_dmx_6sel_1_out_38), .out_39(n32bit_dmx_6sel_1_out_39),
    .out_40(n32bit_dmx_6sel_1_out_40), .out_41(n32bit_dmx_6sel_1_out_41), .out_42(n32bit_dmx_6sel_1_out_42),
    .out_43(n32bit_dmx_6sel_1_out_43), .out_44(n32bit_dmx_6sel_1_out_44), .out_45(n32bit_dmx_6sel_1_out_45),
    .out_46(n32bit_dmx_6sel_1_out_46), .out_47(n32bit_dmx_6sel_1_out_47), .out_48(n32bit_dmx_6sel_1_out_48),
    .out_49(n32bit_dmx_6sel_1_out_49), .out_50(n32bit_dmx_6sel_1_out_50));  // open: out_51, out_52, out_53, out_54, out_55, out_56, out_57, out_58, out_59, out_60, out_61, out_62, out_63, out_64, out_65, out_66
  _32bit_DMX_6sel u_32bit_dmx_6sel_2 (
    .in_1(n8bit_to_32str_2_out_2), .in_2(Y2[5:0]), .out_3(n32bit_dmx_6sel_2_out_3),
    .out_4(n32bit_dmx_6sel_2_out_4), .out_5(n32bit_dmx_6sel_2_out_5), .out_6(n32bit_dmx_6sel_2_out_6),
    .out_7(n32bit_dmx_6sel_2_out_7), .out_8(n32bit_dmx_6sel_2_out_8), .out_9(n32bit_dmx_6sel_2_out_9),
    .out_10(n32bit_dmx_6sel_2_out_10), .out_11(n32bit_dmx_6sel_2_out_11), .out_12(n32bit_dmx_6sel_2_out_12),
    .out_13(n32bit_dmx_6sel_2_out_13), .out_14(n32bit_dmx_6sel_2_out_14), .out_15(n32bit_dmx_6sel_2_out_15),
    .out_16(n32bit_dmx_6sel_2_out_16), .out_17(n32bit_dmx_6sel_2_out_17), .out_18(n32bit_dmx_6sel_2_out_18),
    .out_19(n32bit_dmx_6sel_2_out_19), .out_20(n32bit_dmx_6sel_2_out_20), .out_21(n32bit_dmx_6sel_2_out_21),
    .out_22(n32bit_dmx_6sel_2_out_22), .out_23(n32bit_dmx_6sel_2_out_23), .out_24(n32bit_dmx_6sel_2_out_24),
    .out_25(n32bit_dmx_6sel_2_out_25), .out_26(n32bit_dmx_6sel_2_out_26), .out_27(n32bit_dmx_6sel_2_out_27),
    .out_28(n32bit_dmx_6sel_2_out_28), .out_29(n32bit_dmx_6sel_2_out_29), .out_30(n32bit_dmx_6sel_2_out_30),
    .out_31(n32bit_dmx_6sel_2_out_31), .out_32(n32bit_dmx_6sel_2_out_32), .out_33(n32bit_dmx_6sel_2_out_33),
    .out_34(n32bit_dmx_6sel_2_out_34), .out_35(n32bit_dmx_6sel_2_out_35), .out_36(n32bit_dmx_6sel_2_out_36),
    .out_37(n32bit_dmx_6sel_2_out_37), .out_38(n32bit_dmx_6sel_2_out_38), .out_39(n32bit_dmx_6sel_2_out_39),
    .out_40(n32bit_dmx_6sel_2_out_40), .out_41(n32bit_dmx_6sel_2_out_41), .out_42(n32bit_dmx_6sel_2_out_42),
    .out_43(n32bit_dmx_6sel_2_out_43), .out_44(n32bit_dmx_6sel_2_out_44), .out_45(n32bit_dmx_6sel_2_out_45),
    .out_46(n32bit_dmx_6sel_2_out_46), .out_47(n32bit_dmx_6sel_2_out_47), .out_48(n32bit_dmx_6sel_2_out_48),
    .out_49(n32bit_dmx_6sel_2_out_49), .out_50(n32bit_dmx_6sel_2_out_50));  // open: out_51, out_52, out_53, out_54, out_55, out_56, out_57, out_58, out_59, out_60, out_61, out_62, out_63, out_64, out_65, out_66
  _8bit_to_32str u_8bit_to_32str_2 (.in_1(X2), .out_2(n8bit_to_32str_2_out_2));
  _32bit_DMX_6sel u_32bit_dmx_6sel_3 (
    .in_1(n8bit_to_32str_3_out_2), .in_2(Y3[5:0]), .out_3(n32bit_dmx_6sel_3_out_3),
    .out_4(n32bit_dmx_6sel_3_out_4), .out_5(n32bit_dmx_6sel_3_out_5), .out_6(n32bit_dmx_6sel_3_out_6),
    .out_7(n32bit_dmx_6sel_3_out_7), .out_8(n32bit_dmx_6sel_3_out_8), .out_9(n32bit_dmx_6sel_3_out_9),
    .out_10(n32bit_dmx_6sel_3_out_10), .out_11(n32bit_dmx_6sel_3_out_11), .out_12(n32bit_dmx_6sel_3_out_12),
    .out_13(n32bit_dmx_6sel_3_out_13), .out_14(n32bit_dmx_6sel_3_out_14), .out_15(n32bit_dmx_6sel_3_out_15),
    .out_16(n32bit_dmx_6sel_3_out_16), .out_17(n32bit_dmx_6sel_3_out_17), .out_18(n32bit_dmx_6sel_3_out_18),
    .out_19(n32bit_dmx_6sel_3_out_19), .out_20(n32bit_dmx_6sel_3_out_20), .out_21(n32bit_dmx_6sel_3_out_21),
    .out_22(n32bit_dmx_6sel_3_out_22), .out_23(n32bit_dmx_6sel_3_out_23), .out_24(n32bit_dmx_6sel_3_out_24),
    .out_25(n32bit_dmx_6sel_3_out_25), .out_26(n32bit_dmx_6sel_3_out_26), .out_27(n32bit_dmx_6sel_3_out_27),
    .out_28(n32bit_dmx_6sel_3_out_28), .out_29(n32bit_dmx_6sel_3_out_29), .out_30(n32bit_dmx_6sel_3_out_30),
    .out_31(n32bit_dmx_6sel_3_out_31), .out_32(n32bit_dmx_6sel_3_out_32), .out_33(n32bit_dmx_6sel_3_out_33),
    .out_34(n32bit_dmx_6sel_3_out_34), .out_35(n32bit_dmx_6sel_3_out_35), .out_36(n32bit_dmx_6sel_3_out_36),
    .out_37(n32bit_dmx_6sel_3_out_37), .out_38(n32bit_dmx_6sel_3_out_38), .out_39(n32bit_dmx_6sel_3_out_39),
    .out_40(n32bit_dmx_6sel_3_out_40), .out_41(n32bit_dmx_6sel_3_out_41), .out_42(n32bit_dmx_6sel_3_out_42),
    .out_43(n32bit_dmx_6sel_3_out_43), .out_44(n32bit_dmx_6sel_3_out_44), .out_45(n32bit_dmx_6sel_3_out_45),
    .out_46(n32bit_dmx_6sel_3_out_46), .out_47(n32bit_dmx_6sel_3_out_47), .out_48(n32bit_dmx_6sel_3_out_48),
    .out_49(n32bit_dmx_6sel_3_out_49), .out_50(n32bit_dmx_6sel_3_out_50));  // open: out_51, out_52, out_53, out_54, out_55, out_56, out_57, out_58, out_59, out_60, out_61, out_62, out_63, out_64, out_65, out_66
  _8bit_to_32str u_8bit_to_32str_3 (.in_1(X3), .out_2(n8bit_to_32str_3_out_2));
  _32bit_DMX_6sel u_32bit_dmx_6sel_4 (
    .in_1(n8bit_to_32str_4_out_2), .in_2(Y4[5:0]), .out_3(n32bit_dmx_6sel_4_out_3),
    .out_4(n32bit_dmx_6sel_4_out_4), .out_5(n32bit_dmx_6sel_4_out_5), .out_6(n32bit_dmx_6sel_4_out_6),
    .out_7(n32bit_dmx_6sel_4_out_7), .out_8(n32bit_dmx_6sel_4_out_8), .out_9(n32bit_dmx_6sel_4_out_9),
    .out_10(n32bit_dmx_6sel_4_out_10), .out_11(n32bit_dmx_6sel_4_out_11), .out_12(n32bit_dmx_6sel_4_out_12),
    .out_13(n32bit_dmx_6sel_4_out_13), .out_14(n32bit_dmx_6sel_4_out_14), .out_15(n32bit_dmx_6sel_4_out_15),
    .out_16(n32bit_dmx_6sel_4_out_16), .out_17(n32bit_dmx_6sel_4_out_17), .out_18(n32bit_dmx_6sel_4_out_18),
    .out_19(n32bit_dmx_6sel_4_out_19), .out_20(n32bit_dmx_6sel_4_out_20), .out_21(n32bit_dmx_6sel_4_out_21),
    .out_22(n32bit_dmx_6sel_4_out_22), .out_23(n32bit_dmx_6sel_4_out_23), .out_24(n32bit_dmx_6sel_4_out_24),
    .out_25(n32bit_dmx_6sel_4_out_25), .out_26(n32bit_dmx_6sel_4_out_26), .out_27(n32bit_dmx_6sel_4_out_27),
    .out_28(n32bit_dmx_6sel_4_out_28), .out_29(n32bit_dmx_6sel_4_out_29), .out_30(n32bit_dmx_6sel_4_out_30),
    .out_31(n32bit_dmx_6sel_4_out_31), .out_32(n32bit_dmx_6sel_4_out_32), .out_33(n32bit_dmx_6sel_4_out_33),
    .out_34(n32bit_dmx_6sel_4_out_34), .out_35(n32bit_dmx_6sel_4_out_35), .out_36(n32bit_dmx_6sel_4_out_36),
    .out_37(n32bit_dmx_6sel_4_out_37), .out_38(n32bit_dmx_6sel_4_out_38), .out_39(n32bit_dmx_6sel_4_out_39),
    .out_40(n32bit_dmx_6sel_4_out_40), .out_41(n32bit_dmx_6sel_4_out_41), .out_42(n32bit_dmx_6sel_4_out_42),
    .out_43(n32bit_dmx_6sel_4_out_43), .out_44(n32bit_dmx_6sel_4_out_44), .out_45(n32bit_dmx_6sel_4_out_45),
    .out_46(n32bit_dmx_6sel_4_out_46), .out_47(n32bit_dmx_6sel_4_out_47), .out_48(n32bit_dmx_6sel_4_out_48),
    .out_49(n32bit_dmx_6sel_4_out_49), .out_50(n32bit_dmx_6sel_4_out_50));  // open: out_51, out_52, out_53, out_54, out_55, out_56, out_57, out_58, out_59, out_60, out_61, out_62, out_63, out_64, out_65, out_66
  _8bit_to_32str u_8bit_to_32str_4 (.in_1(X4), .out_2(n8bit_to_32str_4_out_2));
  assign or_1_out = n32bit_dmx_6sel_4_out_3 | n32bit_dmx_6sel_3_out_3 | n32bit_dmx_6sel_2_out_3 | n32bit_dmx_6sel_1_out_3;  // OR_Gate or_1, 32 bits wide
  assign or_2_out = or_1_out | or_3_out;  // OR_Gate or_2, 32 bits wide
  _32bit_extension u_32bit_extension_1 (.in_1(or_1_out), .out_2(out_9));
  _32bit_extension u_32bit_extension_2 (.in_1(or_2_out), .out_2(out_10));
  assign or_3_out = n32bit_dmx_6sel_4_out_4 | n32bit_dmx_6sel_3_out_4 | n32bit_dmx_6sel_2_out_4 | n32bit_dmx_6sel_1_out_4;  // OR_Gate or_3, 32 bits wide
  assign or_4_out = n32bit_dmx_6sel_4_out_5 | n32bit_dmx_6sel_3_out_5 | n32bit_dmx_6sel_2_out_5 | n32bit_dmx_6sel_1_out_5;  // OR_Gate or_4, 32 bits wide
  assign or_5_out = or_3_out | or_4_out;  // OR_Gate or_5, 32 bits wide
  _32bit_extension u_32bit_extension_3 (.in_1(or_5_out), .out_2(out_11));
  assign or_6_out = n32bit_dmx_6sel_4_out_6 | n32bit_dmx_6sel_3_out_6 | n32bit_dmx_6sel_2_out_6 | n32bit_dmx_6sel_1_out_6;  // OR_Gate or_6, 32 bits wide
  assign or_7_out = or_4_out | or_6_out;  // OR_Gate or_7, 32 bits wide
  _32bit_extension u_32bit_extension_4 (.in_1(or_7_out), .out_2(out_12));
  assign or_8_out = n32bit_dmx_6sel_4_out_7 | n32bit_dmx_6sel_3_out_7 | n32bit_dmx_6sel_2_out_7 | n32bit_dmx_6sel_1_out_7;  // OR_Gate or_8, 32 bits wide
  assign or_9_out = or_6_out | or_8_out;  // OR_Gate or_9, 32 bits wide
  assign or_10_out = or_8_out | or_11_out;  // OR_Gate or_10, 32 bits wide
  _32bit_extension u_32bit_extension_5 (.in_1(or_9_out), .out_2(out_13));
  _32bit_extension u_32bit_extension_6 (.in_1(or_10_out), .out_2(out_14));
  assign or_11_out = n32bit_dmx_6sel_4_out_8 | n32bit_dmx_6sel_3_out_8 | n32bit_dmx_6sel_2_out_8 | n32bit_dmx_6sel_1_out_8;  // OR_Gate or_11, 32 bits wide
  assign or_12_out = n32bit_dmx_6sel_4_out_9 | n32bit_dmx_6sel_3_out_9 | n32bit_dmx_6sel_2_out_9 | n32bit_dmx_6sel_1_out_9;  // OR_Gate or_12, 32 bits wide
  assign or_13_out = or_11_out | or_12_out;  // OR_Gate or_13, 32 bits wide
  _32bit_extension u_32bit_extension_7 (.in_1(or_13_out), .out_2(out_15));
  assign or_14_out = n32bit_dmx_6sel_4_out_10 | n32bit_dmx_6sel_3_out_10 | n32bit_dmx_6sel_2_out_10 | n32bit_dmx_6sel_1_out_10;  // OR_Gate or_14, 32 bits wide
  assign or_15_out = or_12_out | or_14_out;  // OR_Gate or_15, 32 bits wide
  _32bit_extension u_32bit_extension_8 (.in_1(or_15_out), .out_2(out_16));
  assign or_16_out = n32bit_dmx_6sel_4_out_11 | n32bit_dmx_6sel_3_out_11 | n32bit_dmx_6sel_2_out_11 | n32bit_dmx_6sel_1_out_11;  // OR_Gate or_16, 32 bits wide
  assign or_17_out = or_14_out | or_16_out;  // OR_Gate or_17, 32 bits wide
  assign or_18_out = or_16_out | or_19_out;  // OR_Gate or_18, 32 bits wide
  _32bit_extension u_32bit_extension_9 (.in_1(or_17_out), .out_2(out_17));
  _32bit_extension u_32bit_extension_10 (.in_1(or_18_out), .out_2(out_18));
  assign or_19_out = n32bit_dmx_6sel_4_out_12 | n32bit_dmx_6sel_3_out_12 | n32bit_dmx_6sel_2_out_12 | n32bit_dmx_6sel_1_out_12;  // OR_Gate or_19, 32 bits wide
  assign or_20_out = n32bit_dmx_6sel_4_out_13 | n32bit_dmx_6sel_3_out_13 | n32bit_dmx_6sel_2_out_13 | n32bit_dmx_6sel_1_out_13;  // OR_Gate or_20, 32 bits wide
  assign or_21_out = or_19_out | or_20_out;  // OR_Gate or_21, 32 bits wide
  _32bit_extension u_32bit_extension_11 (.in_1(or_21_out), .out_2(out_19));
  assign or_22_out = n32bit_dmx_6sel_4_out_14 | n32bit_dmx_6sel_3_out_14 | n32bit_dmx_6sel_2_out_14 | n32bit_dmx_6sel_1_out_14;  // OR_Gate or_22, 32 bits wide
  assign or_23_out = or_20_out | or_22_out;  // OR_Gate or_23, 32 bits wide
  _32bit_extension u_32bit_extension_12 (.in_1(or_23_out), .out_2(out_20));
  assign or_24_out = n32bit_dmx_6sel_4_out_15 | n32bit_dmx_6sel_3_out_15 | n32bit_dmx_6sel_2_out_15 | n32bit_dmx_6sel_1_out_15;  // OR_Gate or_24, 32 bits wide
  assign or_25_out = or_22_out | or_24_out;  // OR_Gate or_25, 32 bits wide
  assign or_26_out = or_24_out | or_27_out;  // OR_Gate or_26, 32 bits wide
  _32bit_extension u_32bit_extension_13 (.in_1(or_25_out), .out_2(out_21));
  _32bit_extension u_32bit_extension_14 (.in_1(or_26_out), .out_2(out_22));
  assign or_27_out = n32bit_dmx_6sel_4_out_16 | n32bit_dmx_6sel_3_out_16 | n32bit_dmx_6sel_2_out_16 | n32bit_dmx_6sel_1_out_16;  // OR_Gate or_27, 32 bits wide
  assign or_28_out = n32bit_dmx_6sel_4_out_17 | n32bit_dmx_6sel_3_out_17 | n32bit_dmx_6sel_2_out_17 | n32bit_dmx_6sel_1_out_17;  // OR_Gate or_28, 32 bits wide
  assign or_29_out = or_27_out | or_28_out;  // OR_Gate or_29, 32 bits wide
  _32bit_extension u_32bit_extension_15 (.in_1(or_29_out), .out_2(out_23));
  assign or_30_out = n32bit_dmx_6sel_4_out_18 | n32bit_dmx_6sel_3_out_18 | n32bit_dmx_6sel_2_out_18 | n32bit_dmx_6sel_1_out_18;  // OR_Gate or_30, 32 bits wide
  assign or_31_out = or_28_out | or_30_out;  // OR_Gate or_31, 32 bits wide
  _32bit_extension u_32bit_extension_16 (.in_1(or_31_out), .out_2(out_24));
  assign or_32_out = n32bit_dmx_6sel_4_out_19 | n32bit_dmx_6sel_3_out_19 | n32bit_dmx_6sel_2_out_19 | n32bit_dmx_6sel_1_out_19;  // OR_Gate or_32, 32 bits wide
  assign or_33_out = or_30_out | or_32_out;  // OR_Gate or_33, 32 bits wide
  assign or_34_out = or_32_out | or_35_out;  // OR_Gate or_34, 32 bits wide
  _32bit_extension u_32bit_extension_17 (.in_1(or_33_out), .out_2(out_25));
  _32bit_extension u_32bit_extension_18 (.in_1(or_34_out), .out_2(out_26));
  assign or_35_out = n32bit_dmx_6sel_4_out_20 | n32bit_dmx_6sel_3_out_20 | n32bit_dmx_6sel_2_out_20 | n32bit_dmx_6sel_1_out_20;  // OR_Gate or_35, 32 bits wide
  assign or_36_out = n32bit_dmx_6sel_4_out_21 | n32bit_dmx_6sel_3_out_21 | n32bit_dmx_6sel_2_out_21 | n32bit_dmx_6sel_1_out_21;  // OR_Gate or_36, 32 bits wide
  assign or_37_out = or_35_out | or_36_out;  // OR_Gate or_37, 32 bits wide
  _32bit_extension u_32bit_extension_19 (.in_1(or_37_out), .out_2(out_27));
  assign or_38_out = n32bit_dmx_6sel_4_out_22 | n32bit_dmx_6sel_3_out_22 | n32bit_dmx_6sel_2_out_22 | n32bit_dmx_6sel_1_out_22;  // OR_Gate or_38, 32 bits wide
  assign or_39_out = or_36_out | or_38_out;  // OR_Gate or_39, 32 bits wide
  _32bit_extension u_32bit_extension_20 (.in_1(or_39_out), .out_2(out_28));
  assign or_40_out = n32bit_dmx_6sel_4_out_23 | n32bit_dmx_6sel_3_out_23 | n32bit_dmx_6sel_2_out_23 | n32bit_dmx_6sel_1_out_23;  // OR_Gate or_40, 32 bits wide
  assign or_41_out = or_38_out | or_40_out;  // OR_Gate or_41, 32 bits wide
  assign or_42_out = or_40_out | or_43_out;  // OR_Gate or_42, 32 bits wide
  _32bit_extension u_32bit_extension_21 (.in_1(or_41_out), .out_2(out_29));
  _32bit_extension u_32bit_extension_22 (.in_1(or_42_out), .out_2(out_30));
  assign or_43_out = n32bit_dmx_6sel_4_out_24 | n32bit_dmx_6sel_3_out_24 | n32bit_dmx_6sel_2_out_24 | n32bit_dmx_6sel_1_out_24;  // OR_Gate or_43, 32 bits wide
  assign or_44_out = n32bit_dmx_6sel_4_out_25 | n32bit_dmx_6sel_3_out_25 | n32bit_dmx_6sel_2_out_25 | n32bit_dmx_6sel_1_out_25;  // OR_Gate or_44, 32 bits wide
  assign or_45_out = or_43_out | or_44_out;  // OR_Gate or_45, 32 bits wide
  _32bit_extension u_32bit_extension_23 (.in_1(or_45_out), .out_2(out_31));
  assign or_46_out = n32bit_dmx_6sel_4_out_26 | n32bit_dmx_6sel_3_out_26 | n32bit_dmx_6sel_2_out_26 | n32bit_dmx_6sel_1_out_26;  // OR_Gate or_46, 32 bits wide
  assign or_47_out = or_44_out | or_46_out;  // OR_Gate or_47, 32 bits wide
  _32bit_extension u_32bit_extension_24 (.in_1(or_47_out), .out_2(out_32));
  assign or_48_out = n32bit_dmx_6sel_4_out_27 | n32bit_dmx_6sel_3_out_27 | n32bit_dmx_6sel_2_out_27 | n32bit_dmx_6sel_1_out_27;  // OR_Gate or_48, 32 bits wide
  assign or_49_out = or_46_out | or_48_out;  // OR_Gate or_49, 32 bits wide
  assign or_50_out = or_48_out | or_51_out;  // OR_Gate or_50, 32 bits wide
  _32bit_extension u_32bit_extension_25 (.in_1(or_49_out), .out_2(out_33));
  _32bit_extension u_32bit_extension_26 (.in_1(or_50_out), .out_2(out_34));
  assign or_51_out = n32bit_dmx_6sel_4_out_28 | n32bit_dmx_6sel_3_out_28 | n32bit_dmx_6sel_2_out_28 | n32bit_dmx_6sel_1_out_28;  // OR_Gate or_51, 32 bits wide
  assign or_52_out = n32bit_dmx_6sel_4_out_29 | n32bit_dmx_6sel_3_out_29 | n32bit_dmx_6sel_2_out_29 | n32bit_dmx_6sel_1_out_29;  // OR_Gate or_52, 32 bits wide
  assign or_53_out = or_51_out | or_52_out;  // OR_Gate or_53, 32 bits wide
  _32bit_extension u_32bit_extension_27 (.in_1(or_53_out), .out_2(out_35));
  assign or_54_out = n32bit_dmx_6sel_4_out_30 | n32bit_dmx_6sel_3_out_30 | n32bit_dmx_6sel_2_out_30 | n32bit_dmx_6sel_1_out_30;  // OR_Gate or_54, 32 bits wide
  assign or_55_out = or_52_out | or_54_out;  // OR_Gate or_55, 32 bits wide
  _32bit_extension u_32bit_extension_28 (.in_1(or_55_out), .out_2(out_36));
  assign or_56_out = n32bit_dmx_6sel_4_out_31 | n32bit_dmx_6sel_3_out_31 | n32bit_dmx_6sel_2_out_31 | n32bit_dmx_6sel_1_out_31;  // OR_Gate or_56, 32 bits wide
  assign or_57_out = or_54_out | or_56_out;  // OR_Gate or_57, 32 bits wide
  assign or_58_out = or_56_out | or_59_out;  // OR_Gate or_58, 32 bits wide
  _32bit_extension u_32bit_extension_29 (.in_1(or_57_out), .out_2(out_37));
  _32bit_extension u_32bit_extension_30 (.in_1(or_58_out), .out_2(out_38));
  assign or_59_out = n32bit_dmx_6sel_4_out_32 | n32bit_dmx_6sel_3_out_32 | n32bit_dmx_6sel_2_out_32 | n32bit_dmx_6sel_1_out_32;  // OR_Gate or_59, 32 bits wide
  assign or_60_out = n32bit_dmx_6sel_4_out_33 | n32bit_dmx_6sel_3_out_33 | n32bit_dmx_6sel_2_out_33 | n32bit_dmx_6sel_1_out_33;  // OR_Gate or_60, 32 bits wide
  assign or_61_out = or_59_out | or_60_out;  // OR_Gate or_61, 32 bits wide
  _32bit_extension u_32bit_extension_31 (.in_1(or_61_out), .out_2(out_39));
  assign or_62_out = n32bit_dmx_6sel_4_out_34 | n32bit_dmx_6sel_3_out_34 | n32bit_dmx_6sel_2_out_34 | n32bit_dmx_6sel_1_out_34;  // OR_Gate or_62, 32 bits wide
  assign or_63_out = or_60_out | or_62_out;  // OR_Gate or_63, 32 bits wide
  _32bit_extension u_32bit_extension_32 (.in_1(or_63_out), .out_2(out_40));
  assign or_64_out = n32bit_dmx_6sel_4_out_35 | n32bit_dmx_6sel_3_out_35 | n32bit_dmx_6sel_2_out_35 | n32bit_dmx_6sel_1_out_35;  // OR_Gate or_64, 32 bits wide
  assign or_65_out = or_62_out | or_64_out;  // OR_Gate or_65, 32 bits wide
  assign or_66_out = or_64_out | or_67_out;  // OR_Gate or_66, 32 bits wide
  _32bit_extension u_32bit_extension_33 (.in_1(or_65_out), .out_2(out_41));
  _32bit_extension u_32bit_extension_34 (.in_1(or_66_out), .out_2(out_42));
  assign or_67_out = n32bit_dmx_6sel_4_out_36 | n32bit_dmx_6sel_3_out_36 | n32bit_dmx_6sel_2_out_36 | n32bit_dmx_6sel_1_out_36;  // OR_Gate or_67, 32 bits wide
  assign or_68_out = n32bit_dmx_6sel_4_out_37 | n32bit_dmx_6sel_3_out_37 | n32bit_dmx_6sel_2_out_37 | n32bit_dmx_6sel_1_out_37;  // OR_Gate or_68, 32 bits wide
  assign or_69_out = or_67_out | or_68_out;  // OR_Gate or_69, 32 bits wide
  _32bit_extension u_32bit_extension_35 (.in_1(or_69_out), .out_2(out_43));
  assign or_70_out = n32bit_dmx_6sel_4_out_38 | n32bit_dmx_6sel_3_out_38 | n32bit_dmx_6sel_2_out_38 | n32bit_dmx_6sel_1_out_38;  // OR_Gate or_70, 32 bits wide
  assign or_71_out = or_68_out | or_70_out;  // OR_Gate or_71, 32 bits wide
  _32bit_extension u_32bit_extension_36 (.in_1(or_71_out), .out_2(out_44));
  assign or_72_out = n32bit_dmx_6sel_4_out_39 | n32bit_dmx_6sel_3_out_39 | n32bit_dmx_6sel_2_out_39 | n32bit_dmx_6sel_1_out_39;  // OR_Gate or_72, 32 bits wide
  assign or_73_out = or_70_out | or_72_out;  // OR_Gate or_73, 32 bits wide
  assign or_74_out = or_72_out | or_75_out;  // OR_Gate or_74, 32 bits wide
  _32bit_extension u_32bit_extension_37 (.in_1(or_73_out), .out_2(out_45));
  _32bit_extension u_32bit_extension_38 (.in_1(or_74_out), .out_2(out_46));
  assign or_75_out = n32bit_dmx_6sel_4_out_40 | n32bit_dmx_6sel_3_out_40 | n32bit_dmx_6sel_2_out_40 | n32bit_dmx_6sel_1_out_40;  // OR_Gate or_75, 32 bits wide
  assign or_76_out = n32bit_dmx_6sel_4_out_41 | n32bit_dmx_6sel_3_out_41 | n32bit_dmx_6sel_2_out_41 | n32bit_dmx_6sel_1_out_41;  // OR_Gate or_76, 32 bits wide
  assign or_77_out = or_75_out | or_76_out;  // OR_Gate or_77, 32 bits wide
  _32bit_extension u_32bit_extension_39 (.in_1(or_77_out), .out_2(out_47));
  assign or_78_out = n32bit_dmx_6sel_4_out_42 | n32bit_dmx_6sel_3_out_42 | n32bit_dmx_6sel_2_out_42 | n32bit_dmx_6sel_1_out_42;  // OR_Gate or_78, 32 bits wide
  assign or_79_out = or_76_out | or_78_out;  // OR_Gate or_79, 32 bits wide
  _32bit_extension u_32bit_extension_40 (.in_1(or_79_out), .out_2(out_48));
  assign or_80_out = n32bit_dmx_6sel_4_out_43 | n32bit_dmx_6sel_3_out_43 | n32bit_dmx_6sel_2_out_43 | n32bit_dmx_6sel_1_out_43;  // OR_Gate or_80, 32 bits wide
  assign or_81_out = or_78_out | or_80_out;  // OR_Gate or_81, 32 bits wide
  assign or_82_out = or_80_out | or_83_out;  // OR_Gate or_82, 32 bits wide
  _32bit_extension u_32bit_extension_41 (.in_1(or_81_out), .out_2(out_49));
  _32bit_extension u_32bit_extension_42 (.in_1(or_82_out), .out_2(out_50));
  assign or_83_out = n32bit_dmx_6sel_4_out_44 | n32bit_dmx_6sel_3_out_44 | n32bit_dmx_6sel_2_out_44 | n32bit_dmx_6sel_1_out_44;  // OR_Gate or_83, 32 bits wide
  assign or_84_out = n32bit_dmx_6sel_4_out_45 | n32bit_dmx_6sel_3_out_45 | n32bit_dmx_6sel_2_out_45 | n32bit_dmx_6sel_1_out_45;  // OR_Gate or_84, 32 bits wide
  assign or_85_out = or_83_out | or_84_out;  // OR_Gate or_85, 32 bits wide
  _32bit_extension u_32bit_extension_43 (.in_1(or_85_out), .out_2(out_51));
  assign or_86_out = n32bit_dmx_6sel_4_out_46 | n32bit_dmx_6sel_3_out_46 | n32bit_dmx_6sel_2_out_46 | n32bit_dmx_6sel_1_out_46;  // OR_Gate or_86, 32 bits wide
  assign or_87_out = or_84_out | or_86_out;  // OR_Gate or_87, 32 bits wide
  _32bit_extension u_32bit_extension_44 (.in_1(or_87_out), .out_2(out_52));
  assign or_88_out = n32bit_dmx_6sel_4_out_47 | n32bit_dmx_6sel_3_out_47 | n32bit_dmx_6sel_2_out_47 | n32bit_dmx_6sel_1_out_47;  // OR_Gate or_88, 32 bits wide
  assign or_89_out = or_86_out | or_88_out;  // OR_Gate or_89, 32 bits wide
  assign or_90_out = or_88_out | or_91_out;  // OR_Gate or_90, 32 bits wide
  _32bit_extension u_32bit_extension_45 (.in_1(or_89_out), .out_2(out_53));
  _32bit_extension u_32bit_extension_46 (.in_1(or_90_out), .out_2(out_54));
  assign or_91_out = n32bit_dmx_6sel_4_out_48 | n32bit_dmx_6sel_3_out_48 | n32bit_dmx_6sel_2_out_48 | n32bit_dmx_6sel_1_out_48;  // OR_Gate or_91, 32 bits wide
  assign or_92_out = n32bit_dmx_6sel_4_out_49 | n32bit_dmx_6sel_3_out_49 | n32bit_dmx_6sel_2_out_49 | n32bit_dmx_6sel_1_out_49;  // OR_Gate or_92, 32 bits wide
  assign or_93_out = or_91_out | or_92_out;  // OR_Gate or_93, 32 bits wide
  _32bit_extension u_32bit_extension_47 (.in_1(or_93_out), .out_2(out_55));
  assign or_94_out = n32bit_dmx_6sel_4_out_50 | n32bit_dmx_6sel_3_out_50 | n32bit_dmx_6sel_2_out_50 | n32bit_dmx_6sel_1_out_50;  // OR_Gate or_94, 32 bits wide
  assign or_95_out = or_92_out | or_94_out;  // OR_Gate or_95, 32 bits wide
  _32bit_extension u_32bit_extension_48 (.in_1(or_95_out), .out_2(out_56));
endmodule

module _32bit_extension (
  input  [31:0] in_1,
  output [31:0] out_2
);

  wire [31:0] shifter_1_out;

  Shifter #(.width(32), .shift("lr")) shifter_1 (.in(in_1), .\dist (5'b00001), .out(shifter_1_out));
  Adder #(.width(32)) adder_1 (.a(in_1), .b(shifter_1_out), .out(out_2));  // open: cin, cout
endmodule

module tetris (
  input  Clock,
  input  Start,
  input  ML,
  input  MR,
  input  TL,
  input  TR,
  output [31:0] R1,
  output [31:0] R2,
  output [31:0] R3,
  output [31:0] R4,
  output [31:0] R5,
  output [31:0] R6,
  output [31:0] R7,
  output [31:0] R8,
  output [31:0] R9,
  output [31:0] R10,
  output [31:0] R11,
  output [31:0] R12,
  output [31:0] R13,
  output [31:0] R14,
  output [31:0] R15,
  output [31:0] R16,
  output [31:0] R17,
  output [31:0] R18,
  output [31:0] R19,
  output [31:0] R20,
  output [31:0] R21,
  output [31:0] R22,
  output [31:0] R23,
  output [31:0] R24,
  output [31:0] R25,
  output [31:0] R26,
  output [31:0] R27,
  output [31:0] R28,
  output [31:0] R29,
  output [31:0] R30,
  output [31:0] R31,
  output [31:0] R32,
  output [31:0] R33,
  output [31:0] R34,
  output [31:0] R35,
  output [31:0] R36,
  output [31:0] R37,
  output [31:0] R38,
  output [31:0] R39,
  output [31:0] R40,
  output [31:0] R41,
  output [31:0] R42,
  output [31:0] R43,
  output [31:0] R44,
  output [31:0] R45,
  output [31:0] R46,
  output [31:0] R47,
  output [31:0] R48
);

  wire block_and_field_1_fail, d_ff_1_q;
  wire [31:0] R1_t, R2_t, R3_t, R4_t, R5_t, R6_t, R7_t, R8_t, R9_t, R10_t, R11_t, R12_t, R13_t, R14_t, R15_t,
       R16_t, R17_t, R18_t, R19_t, R20_t, R21_t, R22_t, R23_t, R24_t, R25_t, R26_t, R27_t, R28_t, R29_t,
       R30_t, R31_t, R32_t, R33_t, R34_t, R35_t, R36_t, R37_t, R38_t, R39_t, R40_t, R41_t, R42_t, R43_t,
       R44_t, R45_t, R46_t, R47_t, R48_t;

  D_Flip_Flop d_ff_1 (.clk(Clock), .D(Start), .Q(d_ff_1_q));  // open: Qn, preset, en, reset
  block_and_field block_and_field_1 (
    .in_1(Clock), .ML(ML), .MR(MR), .TL(TL), .set(d_ff_1_q), .TR(TR), .out_7(R1_t), .out_31(R2_t),
    .out_8(R3_t), .out_32(R4_t), .out_9(R5_t), .out_33(R6_t), .out_10(R7_t), .out_34(R8_t), .out_11(R9_t),
    .out_35(R10_t), .out_12(R11_t), .out_36(R12_t), .out_13(R13_t), .out_37(R14_t), .out_14(R15_t),
    .out_38(R16_t), .out_15(R17_t), .out_39(R18_t), .out_16(R19_t), .out_40(R20_t), .out_17(R21_t),
    .out_41(R22_t), .out_18(R23_t), .out_42(R24_t), .out_19(R25_t), .out_43(R26_t), .out_20(R27_t),
    .out_44(R28_t), .out_21(R29_t), .out_45(R30_t), .out_22(R31_t), .out_46(R32_t), .out_23(R33_t),
    .out_47(R34_t), .out_24(R35_t), .out_48(R36_t), .out_25(R37_t), .out_49(R38_t), .out_26(R39_t),
    .out_50(R40_t), .out_27(R41_t), .out_51(R42_t), .out_28(R43_t), .out_52(R44_t), .out_29(R45_t),
    .out_53(R46_t), .out_30(R47_t), .out_54(R48_t), .fail(block_and_field_1_fail));
  Multiplexer #(.width(32), .enable("false")) multiplexer_1 (
    .in0(R1_t), .in1({32{1'b0}}), .out(R1), .sel(block_and_field_1_fail));
  Multiplexer #(.width(32), .enable("false")) multiplexer_2 (
    .in0(R2_t), .in1({32{1'b0}}), .out(R2), .sel(block_and_field_1_fail));
  Multiplexer #(.width(32), .enable("false")) multiplexer_3 (
    .in0(R3_t), .in1({32{1'b0}}), .out(R3), .sel(block_and_field_1_fail));
  Multiplexer #(.width(32), .enable("false")) multiplexer_4 (
    .in0(R4_t), .in1({32{1'b0}}), .out(R4), .sel(block_and_field_1_fail));
  Multiplexer #(.width(32), .enable("false")) multiplexer_5 (
    .in0(R5_t), .in1({32{1'b0}}), .out(R5), .sel(block_and_field_1_fail));
  Multiplexer #(.width(32), .enable("false")) multiplexer_6 (
    .in0(R6_t), .in1(32'h1139100), .out(R6), .sel(block_and_field_1_fail));
  Multiplexer #(.width(32), .enable("false")) multiplexer_7 (
    .in0(R7_t), .in1(32'h1145100), .out(R7), .sel(block_and_field_1_fail));
  Multiplexer #(.width(32), .enable("false")) multiplexer_8 (
    .in0(R8_t), .in1(32'ha45100), .out(R8), .sel(block_and_field_1_fail));
  Multiplexer #(.width(32), .enable("false")) multiplexer_9 (
    .in0(R9_t), .in1(32'h445100), .out(R9), .sel(block_and_field_1_fail));
  Multiplexer #(.width(32), .enable("false")) multiplexer_10 (
    .in0(R10_t), .in1(32'h445100), .out(R10), .sel(block_and_field_1_fail));
  Multiplexer #(.width(32), .enable("false")) multiplexer_11 (
    .in0(R11_t), .in1(32'h438e00), .out(R11), .sel(block_and_field_1_fail));
  Multiplexer #(.width(32), .enable("false")) multiplexer_12 (
    .in0(R12_t), .in1({32{1'b0}}), .out(R12), .sel(block_and_field_1_fail));
  Multiplexer #(.width(32), .enable("false")) multiplexer_13 (
    .in0(R13_t), .in1({32{1'b0}}), .out(R13), .sel(block_and_field_1_fail));
  Multiplexer #(.width(32), .enable("false")) multiplexer_14 (
    .in0(R14_t), .in1(32'h81c7be0), .out(R14), .sel(block_and_field_1_fail));
  Multiplexer #(.width(32), .enable("false")) multiplexer_15 (
    .in0(R15_t), .in1(32'h8228080), .out(R15), .sel(block_and_field_1_fail));
  Multiplexer #(.width(32), .enable("false")) multiplexer_16 (
    .in0(R16_t), .in1(32'h8228080), .out(R16), .sel(block_and_field_1_fail));
  Multiplexer #(.width(32), .enable("false")) multiplexer_17 (
    .in0(R17_t), .in1(32'h8227880), .out(R17), .sel(block_and_field_1_fail));
  Multiplexer #(.width(32), .enable("false")) multiplexer_18 (
    .in0(R18_t), .in1(32'h8220880), .out(R18), .sel(block_and_field_1_fail));
  Multiplexer #(.width(32), .enable("false")) multiplexer_19 (
    .in0(R19_t), .in1(32'hf9cf080), .out(R19), .sel(block_and_field_1_fail));
  Multiplexer #(.width(32), .enable("false")) multiplexer_20 (
    .in0(R20_t), .in1({32{1'b0}}), .out(R20), .sel(block_and_field_1_fail));
  Multiplexer #(.width(32), .enable("false")) multiplexer_21 (
    .in0(R21_t), .in1({32{1'b0}}), .out(R21), .sel(block_and_field_1_fail));
  Multiplexer #(.width(32), .enable("false")) multiplexer_22 (
    .in0(R22_t), .in1({32{1'b0}}), .out(R22), .sel(block_and_field_1_fail));
  Multiplexer #(.width(32), .enable("false")) multiplexer_23 (
    .in0(R23_t), .in1({32{1'b0}}), .out(R23), .sel(block_and_field_1_fail));
  Multiplexer #(.width(32), .enable("false")) multiplexer_24 (
    .in0(R24_t), .in1({32{1'b0}}), .out(R24), .sel(block_and_field_1_fail));
  Multiplexer #(.width(32), .enable("false")) multiplexer_25 (
    .in0(R25_t), .in1({32{1'b0}}), .out(R25), .sel(block_and_field_1_fail));
  Multiplexer #(.width(32), .enable("false")) multiplexer_26 (
    .in0(R26_t), .in1({32{1'b0}}), .out(R26), .sel(block_and_field_1_fail));
  Multiplexer #(.width(32), .enable("false")) multiplexer_27 (
    .in0(R27_t), .in1({32{1'b0}}), .out(R27), .sel(block_and_field_1_fail));
  Multiplexer #(.width(32), .enable("false")) multiplexer_28 (
    .in0(R28_t), .in1({32{1'b0}}), .out(R28), .sel(block_and_field_1_fail));
  Multiplexer #(.width(32), .enable("false")) multiplexer_29 (
    .in0(R29_t), .in1({32{1'b0}}), .out(R29), .sel(block_and_field_1_fail));
  Multiplexer #(.width(32), .enable("false")) multiplexer_30 (
    .in0(R30_t), .in1(32'h79e7cf3c), .out(R30), .sel(block_and_field_1_fail));
  Multiplexer #(.width(32), .enable("false")) multiplexer_31 (
    .in0(R31_t), .in1(32'h45141040), .out(R31), .sel(block_and_field_1_fail));
  Multiplexer #(.width(32), .enable("false")) multiplexer_32 (
    .in0(R32_t), .in1(32'h45171040), .out(R32), .sel(block_and_field_1_fail));
  Multiplexer #(.width(32), .enable("false")) multiplexer_33 (
    .in0(R33_t), .in1(32'h79e40f3c), .out(R33), .sel(block_and_field_1_fail));
  Multiplexer #(.width(32), .enable("false")) multiplexer_34 (
    .in0(R34_t), .in1(32'h41240104), .out(R34), .sel(block_and_field_1_fail));
  Multiplexer #(.width(32), .enable("false")) multiplexer_35 (
    .in0(R35_t), .in1(32'h4117de78), .out(R35), .sel(block_and_field_1_fail));
  Multiplexer #(.width(32), .enable("false")) multiplexer_36 (
    .in0(R36_t), .in1({32{1'b0}}), .out(R36), .sel(block_and_field_1_fail));
  Multiplexer #(.width(32), .enable("false")) multiplexer_37 (
    .in0(R37_t), .in1({32{1'b0}}), .out(R37), .sel(block_and_field_1_fail));
  Multiplexer #(.width(32), .enable("false")) multiplexer_38 (
    .in0(R38_t), .in1(32'h3df3de7c), .out(R38), .sel(block_and_field_1_fail));
  Multiplexer #(.width(32), .enable("false")) multiplexer_39 (
    .in0(R39_t), .in1(32'h40445110), .out(R39), .sel(block_and_field_1_fail));
  Multiplexer #(.width(32), .enable("false")) multiplexer_40 (
    .in0(R40_t), .in1(32'h40445110), .out(R40), .sel(block_and_field_1_fail));
  Multiplexer #(.width(32), .enable("false")) multiplexer_41 (
    .in0(R41_t), .in1(32'h3c47de10), .out(R41), .sel(block_and_field_1_fail));
  Multiplexer #(.width(32), .enable("false")) multiplexer_42 (
    .in0(R42_t), .in1(32'h4445210), .out(R42), .sel(block_and_field_1_fail));
  Multiplexer #(.width(32), .enable("false")) multiplexer_43 (
    .in0(R43_t), .in1(32'h78445110), .out(R43), .sel(block_and_field_1_fail));
  Multiplexer #(.width(32), .enable("false")) multiplexer_44 (
    .in0(R44_t), .in1({32{1'b0}}), .out(R44), .sel(block_and_field_1_fail));
  Multiplexer #(.width(32), .enable("false")) multiplexer_45 (
    .in0(R45_t), .in1({32{1'b0}}), .out(R45), .sel(block_and_field_1_fail));
  Multiplexer #(.width(32), .enable("false")) multiplexer_46 (
    .in0(R46_t), .in1({32{1'b0}}), .out(R46), .sel(block_and_field_1_fail));
  Multiplexer #(.width(32), .enable("false")) multiplexer_47 (
    .in0(R47_t), .in1({32{1'b0}}), .out(R47), .sel(block_and_field_1_fail));
  Multiplexer #(.width(32), .enable("false")) multiplexer_48 (
    .in0(R48_t), .in1({32{1'b0}}), .out(R48), .sel(block_and_field_1_fail));
endmodule
module collision (
  input  [7:0] X1,
  input  [7:0] Y1,
  input  [7:0] X2,
  input  [7:0] Y2,
  input  [7:0] X3,
  input  [7:0] Y3,
  input  [7:0] X4,
  input  [7:0] Y4,
  input  [31:0] R1,
  input  [31:0] R2,
  input  [31:0] R3,
  input  [31:0] R4,
  input  [31:0] R5,
  input  [31:0] R6,
  input  [31:0] R7,
  input  [31:0] R8,
  input  [31:0] R9,
  input  [31:0] R10,
  input  [31:0] R11,
  input  [31:0] R12,
  input  [31:0] R13,
  input  [31:0] R14,
  input  [31:0] R15,
  input  [31:0] R16,
  input  [31:0] R17,
  input  [31:0] R18,
  input  [31:0] R19,
  input  [31:0] R20,
  input  [31:0] R21,
  input  [31:0] R22,
  input  [31:0] R23,
  input  [31:0] R24,
  input  [31:0] R25,
  input  [31:0] R26,
  input  [31:0] R27,
  input  [31:0] R28,
  input  [31:0] R29,
  input  [31:0] R30,
  input  [31:0] R31,
  input  [31:0] R32,
  input  [31:0] R33,
  input  [31:0] R34,
  input  [31:0] R35,
  input  [31:0] R36,
  input  [31:0] R37,
  input  [31:0] R38,
  input  [31:0] R39,
  input  [31:0] R40,
  input  [31:0] R41,
  input  [31:0] R42,
  input  [31:0] R43,
  input  [31:0] R44,
  input  [31:0] R45,
  input  [31:0] R46,
  input  [31:0] R47,
  input  [31:0] R48,
  output collision
);

  wire comparator_1_eq, comparator_2_eq, comparator_3_eq, comparator_4_eq, comparator_5_eq, comparator_6_eq,
       comparator_7_eq, comparator_8_eq, comparator_9_eq, comparator_10_eq, comparator_11_eq,
       comparator_12_eq, comparator_13_eq, comparator_14_eq, comparator_15_eq, comparator_16_eq,
       comparator_17_eq, comparator_18_eq, comparator_19_eq, comparator_20_eq, comparator_21_eq,
       comparator_22_eq, comparator_23_eq, comparator_24_eq, comparator_25_eq, comparator_26_eq,
       comparator_27_eq, comparator_28_eq, comparator_29_eq, comparator_30_eq, comparator_31_eq,
       comparator_32_eq, comparator_33_eq, comparator_34_eq, comparator_35_eq, comparator_36_eq,
       comparator_37_eq, comparator_38_eq, comparator_39_eq, comparator_40_eq, comparator_41_eq,
       comparator_42_eq, comparator_43_eq, comparator_44_eq, comparator_45_eq, comparator_46_eq,
       comparator_47_eq, comparator_48_eq, not_1_out, not_2_out, not_3_out, not_4_out, not_5_out, not_6_out,
       not_7_out, not_8_out, not_9_out, not_10_out, not_11_out, not_12_out, not_13_out, not_14_out,
       not_15_out, not_16_out, not_17_out, not_18_out, not_19_out, not_20_out, not_21_out, not_22_out,
       not_23_out, not_24_out, not_25_out, not_26_out, not_27_out, not_28_out, not_29_out, not_30_out,
       not_31_out, not_32_out, not_33_out, not_34_out, not_35_out, not_36_out, not_37_out, not_38_out,
       not_39_out, not_40_out, not_41_out, not_42_out, not_43_out, not_44_out, not_45_out, not_46_out,
       not_47_out, not_48_out, or_1_out, or_2_out;
  wire [7:0] adder_1_out, adder_2_out, adder_3_out, adder_4_out;
  wire [31:0] and_1_out, and_2_out, and_3_out, and_4_out, and_5_out, and_6_out, and_7_out, and_8_out,
       and_9_out, and_10_out, and_11_out, and_12_out, and_13_out, and_14_out, and_15_out, and_16_out,
       and_17_out, and_18_out, and_19_out, and_20_out, and_21_out, and_22_out, and_23_out, and_24_out,
       and_25_out, and_26_out, and_27_out, and_28_out, and_29_out, and_30_out, and_31_out, and_32_out,
       and_33_out, and_34_out, and_35_out, and_36_out, and_37_out, and_38_out, and_39_out, and_40_out,
       and_41_out, and_42_out, and_43_out, and_44_out, and_45_out, and_46_out, and_47_out, and_48_out, R1_t,
       R2_t, R3_t, R4_t, R5_t, R6_t, R7_t, R8_t, R9_t, R10_t, R11_t, R12_t, R13_t, R14_t, R15_t, R16_t,
       R17_t, R18_t, R19_t, R20_t, R21_t, R22_t, R23_t, R24_t, R25_t, R26_t, R27_t, R28_t, R29_t, R30_t,
       R31_t, R32_t, R33_t, R34_t, R35_t, R36_t, R37_t, R38_t, R39_t, R40_t, R41_t, R42_t, R43_t, R44_t,
       R45_t, R46_t, R47_t, R48_t;

  Adder adder_1 (.a(Y1), .b(8'h1), .out(adder_1_out));  // open: cin, cout
  Adder adder_2 (.a(Y2), .b(8'h1), .out(adder_2_out));  // open: cin, cout
  Adder adder_3 (.a(Y3), .b(8'h1), .out(adder_3_out));  // open: cin, cout
  Adder adder_4 (.a(Y4), .b(8'h1), .out(adder_4_out));  // open: cin, cout
  block_output block_output_1 (
    .X1(X1), .Y1(adder_1_out), .X2(X2), .Y2(adder_2_out), .X3(X3), .Y3(adder_3_out), .X4(X4),
    .Y4(adder_4_out), .out_9(R1_t), .out_11(R3_t), .out_12(R4_t), .out_13(R5_t), .out_14(R6_t),
    .out_15(R7_t), .out_16(R8_t), .out_17(R9_t), .out_18(R10_t), .out_19(R11_t), .out_20(R12_t),
    .out_21(R13_t), .out_22(R14_t), .out_23(R15_t), .out_24(R16_t), .out_25(R17_t), .out_26(R18_t),
    .out_27(R19_t), .out_28(R20_t), .out_29(R21_t), .out_30(R22_t), .out_31(R23_t), .out_32(R24_t),
    .out_33(R25_t), .out_34(R26_t), .out_35(R27_t), .out_36(R28_t), .out_37(R29_t), .out_38(R30_t),
    .out_39(R31_t), .out_40(R32_t), .out_41(R33_t), .out_42(R34_t), .out_43(R35_t), .out_44(R36_t),
    .out_45(R37_t), .out_46(R38_t), .out_47(R39_t), .out_48(R40_t), .out_49(R41_t), .out_50(R42_t),
    .out_51(R43_t), .out_52(R44_t), .out_53(R45_t), .out_54(R46_t), .out_55(R47_t), .out_56(R48_t),
    .out_10(R2_t));
  Comparator #(.width(32)) comparator_1 (.a({32{1'b0}}), .b(and_1_out), .eq(comparator_1_eq));  // open: gt, lt
  assign and_1_out = R1 & R1_t;  // AND_Gate and_1, 32 bits wide
  Comparator #(.width(32)) comparator_2 (.a({32{1'b0}}), .b(and_2_out), .eq(comparator_2_eq));  // open: gt, lt
  assign and_2_out = R2 & R2_t;  // AND_Gate and_2, 32 bits wide
  Comparator #(.width(32)) comparator_3 (.a({32{1'b0}}), .b(and_3_out), .eq(comparator_3_eq));  // open: gt, lt
  assign and_3_out = R3 & R3_t;  // AND_Gate and_3, 32 bits wide
  Comparator #(.width(32)) comparator_4 (.a({32{1'b0}}), .b(and_4_out), .eq(comparator_4_eq));  // open: gt, lt
  assign and_4_out = R4 & R4_t;  // AND_Gate and_4, 32 bits wide
  Comparator #(.width(32)) comparator_5 (.a({32{1'b0}}), .b(and_5_out), .eq(comparator_5_eq));  // open: gt, lt
  assign and_5_out = R5 & R5_t;  // AND_Gate and_5, 32 bits wide
  Comparator #(.width(32)) comparator_6 (.a({32{1'b0}}), .b(and_6_out), .eq(comparator_6_eq));  // open: gt, lt
  assign and_6_out = R6 & R6_t;  // AND_Gate and_6, 32 bits wide
  Comparator #(.width(32)) comparator_7 (.a({32{1'b0}}), .b(and_7_out), .eq(comparator_7_eq));  // open: gt, lt
  assign and_7_out = R7 & R7_t;  // AND_Gate and_7, 32 bits wide
  Comparator #(.width(32)) comparator_8 (.a({32{1'b0}}), .b(and_8_out), .eq(comparator_8_eq));  // open: gt, lt
  assign and_8_out = R8 & R8_t;  // AND_Gate and_8, 32 bits wide
  Comparator #(.width(32)) comparator_9 (.a({32{1'b0}}), .b(and_9_out), .eq(comparator_9_eq));  // open: gt, lt
  assign and_9_out = R9 & R9_t;  // AND_Gate and_9, 32 bits wide
  Comparator #(.width(32)) comparator_10 (.a({32{1'b0}}), .b(and_10_out), .eq(comparator_10_eq));  // open: gt, lt
  assign and_10_out = R10 & R10_t;  // AND_Gate and_10, 32 bits wide
  Comparator #(.width(32)) comparator_11 (.a({32{1'b0}}), .b(and_11_out), .eq(comparator_11_eq));  // open: gt, lt
  assign and_11_out = R11 & R11_t;  // AND_Gate and_11, 32 bits wide
  Comparator #(.width(32)) comparator_12 (.a({32{1'b0}}), .b(and_12_out), .eq(comparator_12_eq));  // open: gt, lt
  assign and_12_out = R12 & R12_t;  // AND_Gate and_12, 32 bits wide
  Comparator #(.width(32)) comparator_13 (.a({32{1'b0}}), .b(and_13_out), .eq(comparator_13_eq));  // open: gt, lt
  assign and_13_out = R13 & R13_t;  // AND_Gate and_13, 32 bits wide
  Comparator #(.width(32)) comparator_14 (.a({32{1'b0}}), .b(and_14_out), .eq(comparator_14_eq));  // open: gt, lt
  assign and_14_out = R14 & R14_t;  // AND_Gate and_14, 32 bits wide
  Comparator #(.width(32)) comparator_15 (.a({32{1'b0}}), .b(and_15_out), .eq(comparator_15_eq));  // open: gt, lt
  assign and_15_out = R15 & R15_t;  // AND_Gate and_15, 32 bits wide
  Comparator #(.width(32)) comparator_16 (.a({32{1'b0}}), .b(and_16_out), .eq(comparator_16_eq));  // open: gt, lt
  assign and_16_out = R16 & R16_t;  // AND_Gate and_16, 32 bits wide
  Comparator #(.width(32)) comparator_17 (.a({32{1'b0}}), .b(and_17_out), .eq(comparator_17_eq));  // open: gt, lt
  assign and_17_out = R17 & R17_t;  // AND_Gate and_17, 32 bits wide
  Comparator #(.width(32)) comparator_18 (.a({32{1'b0}}), .b(and_18_out), .eq(comparator_18_eq));  // open: gt, lt
  assign and_18_out = R18 & R18_t;  // AND_Gate and_18, 32 bits wide
  Comparator #(.width(32)) comparator_19 (.a({32{1'b0}}), .b(and_19_out), .eq(comparator_19_eq));  // open: gt, lt
  assign and_19_out = R19 & R19_t;  // AND_Gate and_19, 32 bits wide
  Comparator #(.width(32)) comparator_20 (.a({32{1'b0}}), .b(and_20_out), .eq(comparator_20_eq));  // open: gt, lt
  assign and_20_out = R20 & R20_t;  // AND_Gate and_20, 32 bits wide
  Comparator #(.width(32)) comparator_21 (.a({32{1'b0}}), .b(and_21_out), .eq(comparator_21_eq));  // open: gt, lt
  assign and_21_out = R21 & R21_t;  // AND_Gate and_21, 32 bits wide
  Comparator #(.width(32)) comparator_22 (.a({32{1'b0}}), .b(and_22_out), .eq(comparator_22_eq));  // open: gt, lt
  assign and_22_out = R22 & R22_t;  // AND_Gate and_22, 32 bits wide
  Comparator #(.width(32)) comparator_23 (.a({32{1'b0}}), .b(and_23_out), .eq(comparator_23_eq));  // open: gt, lt
  assign and_23_out = R23 & R23_t;  // AND_Gate and_23, 32 bits wide
  Comparator #(.width(32)) comparator_24 (.a({32{1'b0}}), .b(and_24_out), .eq(comparator_24_eq));  // open: gt, lt
  assign and_24_out = R24 & R24_t;  // AND_Gate and_24, 32 bits wide
  Comparator #(.width(32)) comparator_25 (.a({32{1'b0}}), .b(and_25_out), .eq(comparator_25_eq));  // open: gt, lt
  assign and_25_out = R25 & R25_t;  // AND_Gate and_25, 32 bits wide
  Comparator #(.width(32)) comparator_26 (.a({32{1'b0}}), .b(and_26_out), .eq(comparator_26_eq));  // open: gt, lt
  assign and_26_out = R26 & R26_t;  // AND_Gate and_26, 32 bits wide
  Comparator #(.width(32)) comparator_27 (.a({32{1'b0}}), .b(and_27_out), .eq(comparator_27_eq));  // open: gt, lt
  assign and_27_out = R27 & R27_t;  // AND_Gate and_27, 32 bits wide
  Comparator #(.width(32)) comparator_28 (.a({32{1'b0}}), .b(and_28_out), .eq(comparator_28_eq));  // open: gt, lt
  assign and_28_out = R28 & R28_t;  // AND_Gate and_28, 32 bits wide
  Comparator #(.width(32)) comparator_29 (.a({32{1'b0}}), .b(and_29_out), .eq(comparator_29_eq));  // open: gt, lt
  assign and_29_out = R29 & R29_t;  // AND_Gate and_29, 32 bits wide
  Comparator #(.width(32)) comparator_30 (.a({32{1'b0}}), .b(and_30_out), .eq(comparator_30_eq));  // open: gt, lt
  assign and_30_out = R30 & R30_t;  // AND_Gate and_30, 32 bits wide
  Comparator #(.width(32)) comparator_31 (.a({32{1'b0}}), .b(and_31_out), .eq(comparator_31_eq));  // open: gt, lt
  assign and_31_out = R31 & R31_t;  // AND_Gate and_31, 32 bits wide
  Comparator #(.width(32)) comparator_32 (.a({32{1'b0}}), .b(and_32_out), .eq(comparator_32_eq));  // open: gt, lt
  assign and_32_out = R32 & R32_t;  // AND_Gate and_32, 32 bits wide
  Comparator #(.width(32)) comparator_33 (.a({32{1'b0}}), .b(and_33_out), .eq(comparator_33_eq));  // open: gt, lt
  assign and_33_out = R33 & R33_t;  // AND_Gate and_33, 32 bits wide
  Comparator #(.width(32)) comparator_34 (.a({32{1'b0}}), .b(and_34_out), .eq(comparator_34_eq));  // open: gt, lt
  assign and_34_out = R34 & R34_t;  // AND_Gate and_34, 32 bits wide
  Comparator #(.width(32)) comparator_35 (.a({32{1'b0}}), .b(and_35_out), .eq(comparator_35_eq));  // open: gt, lt
  assign and_35_out = R35 & R35_t;  // AND_Gate and_35, 32 bits wide
  Comparator #(.width(32)) comparator_36 (.a({32{1'b0}}), .b(and_36_out), .eq(comparator_36_eq));  // open: gt, lt
  assign and_36_out = R36 & R36_t;  // AND_Gate and_36, 32 bits wide
  Comparator #(.width(32)) comparator_37 (.a({32{1'b0}}), .b(and_37_out), .eq(comparator_37_eq));  // open: gt, lt
  assign and_37_out = R37 & R37_t;  // AND_Gate and_37, 32 bits wide
  Comparator #(.width(32)) comparator_38 (.a({32{1'b0}}), .b(and_38_out), .eq(comparator_38_eq));  // open: gt, lt
  assign and_38_out = R38 & R38_t;  // AND_Gate and_38, 32 bits wide
  Comparator #(.width(32)) comparator_39 (.a({32{1'b0}}), .b(and_39_out), .eq(comparator_39_eq));  // open: gt, lt
  assign and_39_out = R39 & R39_t;  // AND_Gate and_39, 32 bits wide
  Comparator #(.width(32)) comparator_40 (.a({32{1'b0}}), .b(and_40_out), .eq(comparator_40_eq));  // open: gt, lt
  assign and_40_out = R40 & R40_t;  // AND_Gate and_40, 32 bits wide
  Comparator #(.width(32)) comparator_41 (.a({32{1'b0}}), .b(and_41_out), .eq(comparator_41_eq));  // open: gt, lt
  assign and_41_out = R41 & R41_t;  // AND_Gate and_41, 32 bits wide
  Comparator #(.width(32)) comparator_42 (.a({32{1'b0}}), .b(and_42_out), .eq(comparator_42_eq));  // open: gt, lt
  assign and_42_out = R42 & R42_t;  // AND_Gate and_42, 32 bits wide
  Comparator #(.width(32)) comparator_43 (.a({32{1'b0}}), .b(and_43_out), .eq(comparator_43_eq));  // open: gt, lt
  assign and_43_out = R43 & R43_t;  // AND_Gate and_43, 32 bits wide
  Comparator #(.width(32)) comparator_44 (.a({32{1'b0}}), .b(and_44_out), .eq(comparator_44_eq));  // open: gt, lt
  assign and_44_out = R44 & R44_t;  // AND_Gate and_44, 32 bits wide
  Comparator #(.width(32)) comparator_45 (.a({32{1'b0}}), .b(and_45_out), .eq(comparator_45_eq));  // open: gt, lt
  assign and_45_out = R45 & R45_t;  // AND_Gate and_45, 32 bits wide
  Comparator #(.width(32)) comparator_46 (.a({32{1'b0}}), .b(and_46_out), .eq(comparator_46_eq));  // open: gt, lt
  assign and_46_out = R46 & R46_t;  // AND_Gate and_46, 32 bits wide
  Comparator #(.width(32)) comparator_47 (.a({32{1'b0}}), .b(and_47_out), .eq(comparator_47_eq));  // open: gt, lt
  assign and_47_out = R47 & R47_t;  // AND_Gate and_47, 32 bits wide
  Comparator #(.width(32)) comparator_48 (.a({32{1'b0}}), .b(and_48_out), .eq(comparator_48_eq));  // open: gt, lt
  assign and_48_out = R48 & R48_t;  // AND_Gate and_48, 32 bits wide
  not not_1 (not_1_out, comparator_1_eq);
  not not_2 (not_2_out, comparator_2_eq);
  not not_3 (not_3_out, comparator_3_eq);
  not not_4 (not_4_out, comparator_4_eq);
  not not_5 (not_5_out, comparator_5_eq);
  not not_6 (not_6_out, comparator_6_eq);
  not not_7 (not_7_out, comparator_7_eq);
  not not_8 (not_8_out, comparator_8_eq);
  not not_9 (not_9_out, comparator_9_eq);
  not not_10 (not_10_out, comparator_10_eq);
  not not_11 (not_11_out, comparator_11_eq);
  not not_12 (not_12_out, comparator_12_eq);
  not not_13 (not_13_out, comparator_13_eq);
  not not_14 (not_14_out, comparator_14_eq);
  not not_15 (not_15_out, comparator_15_eq);
  not not_16 (not_16_out, comparator_16_eq);
  not not_17 (not_17_out, comparator_17_eq);
  not not_18 (not_18_out, comparator_18_eq);
  not not_19 (not_19_out, comparator_19_eq);
  not not_20 (not_20_out, comparator_20_eq);
  not not_21 (not_21_out, comparator_21_eq);
  not not_22 (not_22_out, comparator_22_eq);
  not not_23 (not_23_out, comparator_23_eq);
  not not_24 (not_24_out, comparator_24_eq);
  not not_25 (not_25_out, comparator_25_eq);
  not not_26 (not_26_out, comparator_26_eq);
  not not_27 (not_27_out, comparator_27_eq);
  not not_28 (not_28_out, comparator_28_eq);
  not not_29 (not_29_out, comparator_29_eq);
  not not_30 (not_30_out, comparator_30_eq);
  not not_31 (not_31_out, comparator_31_eq);
  not not_32 (not_32_out, comparator_32_eq);
  not not_33 (not_33_out, comparator_33_eq);
  not not_34 (not_34_out, comparator_34_eq);
  not not_35 (not_35_out, comparator_35_eq);
  not not_36 (not_36_out, comparator_36_eq);
  not not_37 (not_37_out, comparator_37_eq);
  not not_38 (not_38_out, comparator_38_eq);
  not not_39 (not_39_out, comparator_39_eq);
  not not_40 (not_40_out, comparator_40_eq);
  not not_41 (not_41_out, comparator_41_eq);
  not not_42 (not_42_out, comparator_42_eq);
  not not_43 (not_43_out, comparator_43_eq);
  not not_44 (not_44_out, comparator_44_eq);
  not not_45 (not_45_out, comparator_45_eq);
  not not_46 (not_46_out, comparator_46_eq);
  not not_47 (not_47_out, comparator_47_eq);
  not not_48 (not_48_out, comparator_48_eq);
  or or_1 (or_1_out, not_1_out, not_2_out, not_3_out, not_4_out, not_5_out, not_6_out, not_7_out, not_8_out, not_9_out, not_10_out, not_11_out, not_12_out, not_13_out, not_14_out, not_15_out, not_16_out, not_17_out, not_18_out, not_19_out, not_20_out, not_21_out, not_22_out, not_23_out, not_24_out);
  or or_2 (or_2_out, not_25_out, not_26_out, not_27_out, not_28_out, not_29_out, not_30_out, not_31_out, not_32_out, not_33_out, not_34_out, not_35_out, not_36_out, not_37_out, not_38_out, not_39_out, not_40_out, not_41_out, not_42_out, not_43_out, not_44_out, not_45_out, not_46_out, not_47_out, not_48_out);
  or or_3 (collision, or_1_out, or_2_out);
endmodule

module field (
  input  [31:0] R1,
  input  [31:0] R2,
  input  [31:0] R3,
  input  [31:0] R4,
  input  [31:0] R5,
  input  [31:0] R6,
  input  [31:0] R7,
  input  [31:0] R8,
  input  [31:0] R9,
  input  [31:0] R10,
  input  [31:0] R11,
  input  [31:0] R12,
  input  [31:0] R13,
  input  [31:0] R14,
  input  [31:0] R15,
  input  [31:0] R16,
  input  [31:0] R17,
  input  [31:0] R18,
  input  [31:0] R19,
  input  [31:0] R20,
  input  [31:0] R21,
  input  [31:0] R22,
  input  [31:0] R23,
  input  [31:0] R24,
  input  [31:0] R25,
  input  [31:0] R26,
  input  [31:0] R27,
  input  [31:0] R28,
  input  [31:0] R29,
  input  [31:0] R30,
  input  [31:0] R31,
  input  [31:0] R32,
  input  [31:0] R33,
  input  [31:0] R34,
  input  [31:0] R35,
  input  [31:0] R36,
  input  [31:0] R37,
  input  [31:0] R38,
  input  [31:0] R39,
  input  [31:0] R40,
  input  [31:0] R41,
  input  [31:0] R42,
  input  [31:0] R43,
  input  [31:0] R44,
  input  [31:0] R45,
  input  [31:0] R46,
  input  [31:0] R47,
  input  [31:0] R48,
  input  save,
  input  clr,
  output [31:0] R1_2,
  output [31:0] R2_2,
  output [31:0] R3_2,
  output [31:0] R4_2,
  output [31:0] R5_2,
  output [31:0] R6_2,
  output [31:0] R7_2,
  output [31:0] R8_2,
  output [31:0] R9_2,
  output [31:0] R10_2,
  output [31:0] R11_2,
  output [31:0] R12_2,
  output [31:0] R13_2,
  output [31:0] R14_2,
  output [31:0] R15_2,
  output [31:0] R16_2,
  output [31:0] R17_2,
  output [31:0] R18_2,
  output [31:0] R19_2,
  output [31:0] R20_2,
  output [31:0] R21_2,
  output [31:0] R22_2,
  output [31:0] R23_2,
  output [31:0] R24_2,
  output [31:0] R25_2,
  output [31:0] R26_2,
  output [31:0] R27_2,
  output [31:0] R28_2,
  output [31:0] R29_2,
  output [31:0] R30_2,
  output [31:0] R31_2,
  output [31:0] R32_2,
  output [31:0] R33_2,
  output [31:0] R34_2,
  output [31:0] R35_2,
  output [31:0] R36_2,
  output [31:0] R37_2,
  output [31:0] R38_2,
  output [31:0] R39_2,
  output [31:0] R40_2,
  output [31:0] R41_2,
  output [31:0] R42_2,
  output [31:0] R43_2,
  output [31:0] R44_2,
  output [31:0] R45_2,
  output [31:0] R46_2,
  output [31:0] R47_2,
  output [31:0] R48_2
);

  wire comparator_1_eq, comparator_2_eq, comparator_3_eq, comparator_4_eq, comparator_5_eq, comparator_6_eq,
       comparator_7_eq, comparator_8_eq, comparator_9_eq, comparator_10_eq, comparator_11_eq,
       comparator_12_eq, comparator_13_eq, comparator_14_eq, comparator_15_eq, comparator_16_eq,
       comparator_17_eq, comparator_18_eq, comparator_19_eq, comparator_20_eq, comparator_21_eq,
       comparator_22_eq, comparator_23_eq, comparator_24_eq, comparator_25_eq, comparator_26_eq,
       comparator_27_eq, comparator_28_eq, comparator_29_eq, comparator_30_eq, comparator_31_eq,
       comparator_32_eq, comparator_33_eq, comparator_34_eq, comparator_35_eq, comparator_36_eq,
       comparator_37_eq, comparator_38_eq, comparator_39_eq, comparator_40_eq, comparator_41_eq,
       comparator_42_eq, comparator_43_eq, comparator_44_eq, comparator_45_eq, comparator_46_eq,
       comparator_47_eq, comparator_48_eq, comparator_49_eq, comparator_50_eq, comparator_51_eq,
       comparator_52_eq, comparator_53_eq, comparator_54_eq, comparator_55_eq, comparator_56_eq,
       comparator_57_eq, comparator_58_eq, comparator_59_eq, comparator_60_eq, comparator_61_eq,
       comparator_62_eq, comparator_63_eq, comparator_64_eq, comparator_65_eq, comparator_66_eq,
       comparator_67_eq, comparator_68_eq, comparator_69_eq, comparator_70_eq, comparator_71_eq,
       comparator_72_eq, comparator_73_eq, comparator_74_eq, comparator_75_eq, comparator_76_eq,
       comparator_77_eq, comparator_78_eq, comparator_79_eq, comparator_80_eq, comparator_81_eq,
       comparator_82_eq, comparator_83_eq, comparator_84_eq, comparator_85_eq, comparator_86_eq,
       comparator_87_eq, comparator_88_eq, comparator_89_eq, comparator_90_eq, comparator_91_eq,
       comparator_92_eq, comparator_93_eq, comparator_94_eq, comparator_95_eq, comparator_96_eq,
       comparator_97_eq, comparator_98_eq, comparator_99_eq, comparator_100_eq, comparator_101_eq,
       comparator_102_eq, comparator_103_eq, comparator_104_eq, comparator_105_eq, comparator_106_eq,
       comparator_107_eq, comparator_108_eq, comparator_109_eq, comparator_110_eq, comparator_111_eq,
       comparator_112_eq, comparator_113_eq, comparator_114_eq, comparator_115_eq, comparator_116_eq,
       comparator_117_eq, comparator_118_eq, comparator_119_eq, comparator_120_eq, comparator_121_eq,
       comparator_122_eq, comparator_123_eq, comparator_124_eq, comparator_125_eq, comparator_126_eq,
       comparator_127_eq, comparator_128_eq, comparator_129_eq, comparator_130_eq, comparator_131_eq,
       comparator_132_eq, comparator_133_eq, comparator_134_eq, comparator_135_eq, comparator_136_eq,
       comparator_137_eq, comparator_138_eq, comparator_139_eq, comparator_140_eq, comparator_141_eq,
       comparator_142_eq, comparator_143_eq, comparator_144_eq, comparator_145_eq, comparator_146_eq,
       comparator_147_eq, comparator_148_eq, comparator_149_eq, comparator_150_eq, comparator_151_eq,
       comparator_152_eq, comparator_153_eq, comparator_154_eq, comparator_155_eq, comparator_156_eq,
       comparator_157_eq, comparator_158_eq, comparator_159_eq, comparator_160_eq, comparator_161_eq,
       comparator_162_eq, comparator_163_eq, comparator_164_eq, comparator_165_eq, comparator_166_eq,
       comparator_167_eq, comparator_168_eq, comparator_169_eq, comparator_170_eq, comparator_171_eq,
       comparator_172_eq, comparator_173_eq, comparator_174_eq, comparator_175_eq, comparator_176_eq,
       comparator_177_eq, comparator_178_eq, comparator_179_eq, comparator_180_eq, comparator_181_eq,
       comparator_182_eq, comparator_183_eq, comparator_184_eq, comparator_185_eq, comparator_186_eq,
       comparator_187_eq, comparator_188_eq, comparator_189_eq, comparator_190_eq, comparator_191_eq,
       comparator_192_eq, or_1_out, or_2_out, or_3_out, or_4_out, or_5_out, or_6_out, or_7_out, or_8_out,
       or_9_out, or_10_out, or_11_out, or_12_out, or_13_out, or_14_out, or_15_out, or_16_out, or_17_out,
       or_18_out, or_19_out, or_20_out, or_21_out, or_22_out, or_23_out, or_24_out, or_25_out, or_26_out,
       or_27_out, or_28_out, or_29_out, or_30_out, or_31_out, or_32_out, or_33_out, or_34_out, or_35_out,
       or_36_out, or_37_out, or_38_out, or_39_out, or_40_out, or_41_out, or_42_out, or_43_out, or_44_out,
       or_45_out, or_46_out, or_47_out, or_48_out, or_49_out, or_50_out, or_51_out, or_52_out, or_53_out,
       or_54_out, or_55_out, or_56_out, or_57_out, or_58_out, or_59_out, or_60_out, or_61_out, or_62_out,
       or_63_out, or_64_out, or_65_out, or_66_out, or_67_out, or_68_out, or_69_out, or_70_out, or_71_out,
       or_72_out, or_73_out, or_74_out, or_75_out, or_76_out, or_77_out, or_78_out, or_79_out, or_80_out,
       or_81_out, or_82_out, or_83_out, or_84_out, or_85_out, or_86_out, or_87_out, or_88_out, or_89_out,
       or_90_out, or_91_out, or_92_out, or_93_out, or_94_out, or_95_out, or_96_out, or_97_out, or_98_out,
       or_99_out, or_100_out, or_101_out, or_102_out, or_103_out, or_104_out, or_105_out, or_106_out,
       or_107_out, or_108_out, or_109_out, or_110_out, or_111_out, or_112_out, or_113_out, or_114_out,
       or_115_out, or_116_out, or_117_out, or_118_out, or_119_out, or_120_out, or_121_out, or_122_out,
       or_123_out, or_124_out, or_125_out, or_126_out, or_127_out, or_128_out, or_129_out, or_130_out,
       or_131_out, or_132_out, or_133_out, or_134_out, or_135_out, or_136_out, or_137_out, or_138_out,
       or_139_out, or_140_out, or_141_out, or_142_out, or_143_out, or_144_out, or_145_out, or_146_out,
       or_147_out, or_148_out, or_149_out, or_150_out, or_151_out, or_152_out, or_153_out, or_154_out,
       or_155_out, or_156_out, or_157_out, or_158_out, or_159_out, or_160_out, or_161_out, or_162_out,
       or_163_out, or_164_out, or_165_out, or_166_out, or_167_out, or_168_out, or_169_out, or_170_out,
       or_171_out, or_172_out, or_173_out, or_174_out, or_175_out, or_176_out, or_177_out, or_178_out,
       or_179_out, or_180_out, or_181_out, or_182_out, or_183_out, or_184_out, or_185_out, or_186_out,
       or_187_out, or_188_out;
  wire [31:0] multiplexer_1_out, multiplexer_2_out, multiplexer_3_out, multiplexer_4_out, multiplexer_5_out,
       multiplexer_6_out, multiplexer_7_out, multiplexer_8_out, multiplexer_9_out, multiplexer_10_out,
       multiplexer_11_out, multiplexer_12_out, multiplexer_13_out, multiplexer_14_out, multiplexer_15_out,
       multiplexer_16_out, multiplexer_17_out, multiplexer_18_out, multiplexer_19_out, multiplexer_20_out,
       multiplexer_21_out, multiplexer_22_out, multiplexer_23_out, multiplexer_24_out, multiplexer_25_out,
       multiplexer_26_out, multiplexer_27_out, multiplexer_28_out, multiplexer_29_out, multiplexer_30_out,
       multiplexer_31_out, multiplexer_32_out, multiplexer_33_out, multiplexer_34_out, multiplexer_35_out,
       multiplexer_36_out, multiplexer_37_out, multiplexer_38_out, multiplexer_39_out, multiplexer_40_out,
       multiplexer_41_out, multiplexer_42_out, multiplexer_43_out, multiplexer_44_out, multiplexer_45_out,
       multiplexer_46_out, multiplexer_47_out, multiplexer_48_out, multiplexer_49_out, multiplexer_50_out,
       multiplexer_51_out, multiplexer_52_out, multiplexer_53_out, multiplexer_54_out, multiplexer_55_out,
       multiplexer_56_out, multiplexer_57_out, multiplexer_58_out, multiplexer_59_out, multiplexer_60_out,
       multiplexer_61_out, multiplexer_62_out, multiplexer_63_out, multiplexer_64_out, multiplexer_65_out,
       multiplexer_66_out, multiplexer_67_out, multiplexer_68_out, multiplexer_69_out, multiplexer_70_out,
       multiplexer_71_out, multiplexer_72_out, multiplexer_73_out, multiplexer_74_out, multiplexer_75_out,
       multiplexer_76_out, multiplexer_77_out, multiplexer_78_out, multiplexer_79_out, multiplexer_80_out,
       multiplexer_81_out, multiplexer_82_out, multiplexer_83_out, multiplexer_84_out, multiplexer_85_out,
       multiplexer_86_out, multiplexer_87_out, multiplexer_88_out, multiplexer_89_out, multiplexer_90_out,
       multiplexer_91_out, multiplexer_92_out, multiplexer_93_out, multiplexer_94_out, multiplexer_95_out,
       multiplexer_96_out, multiplexer_97_out, multiplexer_98_out, multiplexer_99_out, multiplexer_100_out,
       multiplexer_101_out, multiplexer_102_out, multiplexer_103_out, multiplexer_104_out,
       multiplexer_105_out, multiplexer_106_out, multiplexer_107_out, multiplexer_108_out,
       multiplexer_109_out, multiplexer_110_out, multiplexer_111_out, multiplexer_112_out,
       multiplexer_113_out, multiplexer_114_out, multiplexer_115_out, multiplexer_116_out,
       multiplexer_117_out, multiplexer_118_out, multiplexer_119_out, multiplexer_120_out,
       multiplexer_121_out, multiplexer_122_out, multiplexer_123_out, multiplexer_124_out,
       multiplexer_125_out, multiplexer_126_out, multiplexer_127_out, multiplexer_128_out,
       multiplexer_129_out, multiplexer_130_out, multiplexer_131_out, multiplexer_132_out,
       multiplexer_133_out, multiplexer_134_out, multiplexer_135_out, multiplexer_136_out,
       multiplexer_137_out, multiplexer_138_out, multiplexer_139_out, multiplexer_140_out,
       multiplexer_141_out, multiplexer_142_out, multiplexer_143_out, multiplexer_144_out,
       multiplexer_145_out, multiplexer_146_out, multiplexer_147_out, multiplexer_148_out,
       multiplexer_149_out, multiplexer_150_out, multiplexer_151_out, multiplexer_152_out,
       multiplexer_153_out, multiplexer_154_out, multiplexer_155_out, multiplexer_156_out,
       multiplexer_157_out, multiplexer_158_out, multiplexer_159_out, multiplexer_160_out,
       multiplexer_161_out, multiplexer_162_out, multiplexer_163_out, multiplexer_164_out,
       multiplexer_165_out, multiplexer_166_out, multiplexer_167_out, multiplexer_168_out,
       multiplexer_169_out, multiplexer_170_out, multiplexer_171_out, multiplexer_172_out,
       multiplexer_173_out, multiplexer_174_out, multiplexer_175_out, multiplexer_176_out,
       multiplexer_177_out, multiplexer_178_out, multiplexer_179_out, multiplexer_180_out,
       multiplexer_181_out, multiplexer_182_out, multiplexer_183_out, multiplexer_184_out,
       multiplexer_185_out, multiplexer_186_out, multiplexer_187_out, multiplexer_188_out,
       multiplexer_189_out, multiplexer_190_out, multiplexer_191_out, multiplexer_192_out;

  Multiplexer #(.width(32), .enable("false")) multiplexer_1 (
    .in0(multiplexer_4_out), .in1({32{1'b0}}), .out(multiplexer_1_out), .sel(or_3_out));
  Multiplexer #(.width(32), .enable("false")) multiplexer_2 (
    .in0(multiplexer_1_out), .in1({32{1'b0}}), .out(multiplexer_2_out), .sel(or_4_out));
  Comparator #(.width(32)) comparator_1 (.a(R1), .b({32{1'b1}}), .eq(comparator_1_eq));  // open: gt, lt
  or or_1 (or_1_out, comparator_1_eq, or_5_out);
  Multiplexer #(.width(32), .enable("false")) multiplexer_3 (
    .in0(R1), .in1({32{1'b0}}), .out(multiplexer_3_out), .sel(or_1_out));
  Comparator #(.width(32)) comparator_2 (.a(multiplexer_3_out), .b({32{1'b1}}), .eq(comparator_2_eq));  // open: gt, lt
  or or_2 (or_2_out, comparator_2_eq, or_6_out);
  Multiplexer #(.width(32), .enable("false")) multiplexer_4 (
    .in0(multiplexer_3_out), .in1({32{1'b0}}), .out(multiplexer_4_out), .sel(or_2_out));
  Comparator #(.width(32)) comparator_3 (.a(multiplexer_4_out), .b({32{1'b1}}), .eq(comparator_3_eq));  // open: gt, lt
  or or_3 (or_3_out, comparator_3_eq, or_7_out);
  Comparator #(.width(32)) comparator_4 (.a(multiplexer_1_out), .b({32{1'b1}}), .eq(comparator_4_eq));  // open: gt, lt
  or or_4 (or_4_out, comparator_4_eq, or_8_out);
  Register #(.width(32)) register_1 (.D(multiplexer_2_out), .Q(R1_2), .clk(save), .clr(clr));  // open: en
  or or_5 (or_5_out, comparator_7_eq, or_12_out);
  Multiplexer #(.width(32), .enable("false")) multiplexer_5 (
    .in0(R2), .in1(R1), .out(multiplexer_5_out), .sel(or_5_out));
  or or_6 (or_6_out, comparator_8_eq, or_9_out);
  Multiplexer #(.width(32), .enable("false")) multiplexer_6 (
    .in0(multiplexer_5_out), .in1(multiplexer_3_out), .out(multiplexer_6_out), .sel(or_6_out));
  Comparator #(.width(32)) comparator_5 (.a(multiplexer_6_out), .b({32{1'b1}}), .eq(comparator_5_eq));  // open: gt, lt
  or or_7 (or_7_out, comparator_5_eq, or_10_out);
  Multiplexer #(.width(32), .enable("false")) multiplexer_7 (
    .in0(multiplexer_6_out), .in1(multiplexer_4_out), .out(multiplexer_7_out), .sel(or_7_out));
  Comparator #(.width(32)) comparator_6 (.a(multiplexer_7_out), .b({32{1'b1}}), .eq(comparator_6_eq));  // open: gt, lt
  or or_8 (or_8_out, comparator_6_eq, or_11_out);
  Multiplexer #(.width(32), .enable("false")) multiplexer_8 (
    .in0(multiplexer_7_out), .in1(multiplexer_1_out), .out(multiplexer_8_out), .sel(or_8_out));
  Register #(.width(32)) register_2 (.D(multiplexer_8_out), .Q(R2_2), .clk(save), .clr(clr));  // open: en
  Comparator #(.width(32)) comparator_7 (.a(R2), .b({32{1'b1}}), .eq(comparator_7_eq));  // open: gt, lt
  Multiplexer #(.width(32), .enable("false")) multiplexer_9 (
    .in0(R3), .in1(R2), .out(multiplexer_9_out), .sel(or_12_out));
  Comparator #(.width(32)) comparator_8 (.a(multiplexer_5_out), .b({32{1'b1}}), .eq(comparator_8_eq));  // open: gt, lt
  or or_9 (or_9_out, comparator_10_eq, or_15_out);
  Multiplexer #(.width(32), .enable("false")) multiplexer_10 (
    .in0(multiplexer_9_out), .in1(multiplexer_5_out), .out(multiplexer_10_out), .sel(or_9_out));
  or or_10 (or_10_out, comparator_11_eq, or_16_out);
  Multiplexer #(.width(32), .enable("false")) multiplexer_11 (
    .in0(multiplexer_10_out), .in1(multiplexer_6_out), .out(multiplexer_11_out), .sel(or_10_out));
  or or_11 (or_11_out, comparator_12_eq, or_13_out);
  Multiplexer #(.width(32), .enable("false")) multiplexer_12 (
    .in0(multiplexer_11_out), .in1(multiplexer_7_out), .out(multiplexer_12_out), .sel(or_11_out));
  Register #(.width(32)) register_3 (.D(multiplexer_12_out), .Q(R3_2), .clk(save), .clr(clr));  // open: en
  Comparator #(.width(32)) comparator_9 (.a(R3), .b({32{1'b1}}), .eq(comparator_9_eq));  // open: gt, lt
  or or_12 (or_12_out, comparator_9_eq, or_14_out);
  Multiplexer #(.width(32), .enable("false")) multiplexer_13 (
    .in0(R4), .in1(R3), .out(multiplexer_13_out), .sel(or_14_out));
  Comparator #(.width(32)) comparator_10 (
    .a(multiplexer_9_out), .b({32{1'b1}}), .eq(comparator_10_eq));  // open: gt, lt
  Multiplexer #(.width(32), .enable("false")) multiplexer_14 (
    .in0(multiplexer_13_out), .in1(multiplexer_9_out), .out(multiplexer_14_out), .sel(or_15_out));
  Comparator #(.width(32)) comparator_11 (
    .a(multiplexer_10_out), .b({32{1'b1}}), .eq(comparator_11_eq));  // open: gt, lt
  Multiplexer #(.width(32), .enable("false")) multiplexer_15 (
    .in0(multiplexer_14_out), .in1(multiplexer_10_out), .out(multiplexer_15_out), .sel(or_16_out));
  Comparator #(.width(32)) comparator_12 (
    .a(multiplexer_11_out), .b({32{1'b1}}), .eq(comparator_12_eq));  // open: gt, lt
  or or_13 (or_13_out, comparator_16_eq, or_20_out);
  Multiplexer #(.width(32), .enable("false")) multiplexer_16 (
    .in0(multiplexer_15_out), .in1(multiplexer_11_out), .out(multiplexer_16_out), .sel(or_13_out));
  Comparator #(.width(32)) comparator_13 (.a(R4), .b({32{1'b1}}), .eq(comparator_13_eq));  // open: gt, lt
  or or_14 (or_14_out, comparator_13_eq, or_17_out);
  Comparator #(.width(32)) comparator_14 (
    .a(multiplexer_13_out), .b({32{1'b1}}), .eq(comparator_14_eq));  // open: gt, lt
  or or_15 (or_15_out, comparator_14_eq, or_18_out);
  Comparator #(.width(32)) comparator_15 (
    .a(multiplexer_14_out), .b({32{1'b1}}), .eq(comparator_15_eq));  // open: gt, lt
  or or_16 (or_16_out, comparator_15_eq, or_19_out);
  Multiplexer #(.width(32), .enable("false")) multiplexer_17 (
    .in0(multiplexer_20_out), .in1(multiplexer_14_out), .out(multiplexer_17_out), .sel(or_19_out));
  Comparator #(.width(32)) comparator_16 (
    .a(multiplexer_15_out), .b({32{1'b1}}), .eq(comparator_16_eq));  // open: gt, lt
  Multiplexer #(.width(32), .enable("false")) multiplexer_18 (
    .in0(multiplexer_17_out), .in1(multiplexer_15_out), .out(multiplexer_18_out), .sel(or_20_out));
  Register #(.width(32)) register_4 (.D(multiplexer_16_out), .Q(R4_2), .clk(save), .clr(clr));  // open: en
  Comparator #(.width(32)) comparator_17 (.a(R5), .b({32{1'b1}}), .eq(comparator_17_eq));  // open: gt, lt
  or or_17 (or_17_out, comparator_17_eq, or_21_out);
  Multiplexer #(.width(32), .enable("false")) multiplexer_19 (
    .in0(R5), .in1(R4), .out(multiplexer_19_out), .sel(or_17_out));
  Comparator #(.width(32)) comparator_18 (
    .a(multiplexer_19_out), .b({32{1'b1}}), .eq(comparator_18_eq));  // open: gt, lt
  or or_18 (or_18_out, comparator_18_eq, or_22_out);
  Multiplexer #(.width(32), .enable("false")) multiplexer_20 (
    .in0(multiplexer_19_out), .in1(multiplexer_13_out), .out(multiplexer_20_out), .sel(or_18_out));
  Comparator #(.width(32)) comparator_19 (
    .a(multiplexer_20_out), .b({32{1'b1}}), .eq(comparator_19_eq));  // open: gt, lt
  or or_19 (or_19_out, comparator_19_eq, or_23_out);
  Comparator #(.width(32)) comparator_20 (
    .a(multiplexer_17_out), .b({32{1'b1}}), .eq(comparator_20_eq));  // open: gt, lt
  or or_20 (or_20_out, comparator_20_eq, or_24_out);
  Register #(.width(32)) register_5 (.D(multiplexer_18_out), .Q(R5_2), .clk(save), .clr(clr));  // open: en
  or or_21 (or_21_out, comparator_23_eq, or_28_out);
  Multiplexer #(.width(32), .enable("false")) multiplexer_21 (
    .in0(R6), .in1(R5), .out(multiplexer_21_out), .sel(or_21_out));
  or or_22 (or_22_out, comparator_24_eq, or_25_out);
  Multiplexer #(.width(32), .enable("false")) multiplexer_22 (
    .in0(multiplexer_21_out), .in1(multiplexer_19_out), .out(multiplexer_22_out), .sel(or_22_out));
  Comparator #(.width(32)) comparator_21 (
    .a(multiplexer_22_out), .b({32{1'b1}}), .eq(comparator_21_eq));  // open: gt, lt
  or or_23 (or_23_out, comparator_21_eq, or_26_out);
  Multiplexer #(.width(32), .enable("false")) multiplexer_23 (
    .in0(multiplexer_22_out), .in1(multiplexer_20_out), .out(multiplexer_23_out), .sel(or_23_out));
  Comparator #(.width(32)) comparator_22 (
    .a(multiplexer_23_out), .b({32{1'b1}}), .eq(comparator_22_eq));  // open: gt, lt
  or or_24 (or_24_out, comparator_22_eq, or_27_out);
  Multiplexer #(.width(32), .enable("false")) multiplexer_24 (
    .in0(multiplexer_23_out), .in1(multiplexer_17_out), .out(multiplexer_24_out), .sel(or_24_out));
  Register #(.width(32)) register_6 (.D(multiplexer_24_out), .Q(R6_2), .clk(save), .clr(clr));  // open: en
  Comparator #(.width(32)) comparator_23 (.a(R6), .b({32{1'b1}}), .eq(comparator_23_eq));  // open: gt, lt
  Multiplexer #(.width(32), .enable("false")) multiplexer_25 (
    .in0(R7), .in1(R6), .out(multiplexer_25_out), .sel(or_28_out));
  Comparator #(.width(32)) comparator_24 (
    .a(multiplexer_21_out), .b({32{1'b1}}), .eq(comparator_24_eq));  // open: gt, lt
  or or_25 (or_25_out, comparator_26_eq, or_31_out);
  Multiplexer #(.width(32), .enable("false")) multiplexer_26 (
    .in0(multiplexer_25_out), .in1(multiplexer_21_out), .out(multiplexer_26_out), .sel(or_25_out));
  or or_26 (or_26_out, comparator_27_eq, or_32_out);
  Multiplexer #(.width(32), .enable("false")) multiplexer_27 (
    .in0(multiplexer_26_out), .in1(multiplexer_22_out), .out(multiplexer_27_out), .sel(or_26_out));
  or or_27 (or_27_out, comparator_28_eq, or_29_out);
  Multiplexer #(.width(32), .enable("false")) multiplexer_28 (
    .in0(multiplexer_27_out), .in1(multiplexer_23_out), .out(multiplexer_28_out), .sel(or_27_out));
  Register #(.width(32)) register_7 (.D(multiplexer_28_out), .Q(R7_2), .clk(save), .clr(clr));  // open: en
  Comparator #(.width(32)) comparator_25 (.a(R7), .b({32{1'b1}}), .eq(comparator_25_eq));  // open: gt, lt
  or or_28 (or_28_out, comparator_25_eq, or_30_out);
  Multiplexer #(.width(32), .enable("false")) multiplexer_29 (
    .in0(R8), .in1(R7), .out(multiplexer_29_out), .sel(or_30_out));
  Comparator #(.width(32)) comparator_26 (
    .a(multiplexer_25_out), .b({32{1'b1}}), .eq(comparator_26_eq));  // open: gt, lt
  Multiplexer #(.width(32), .enable("false")) multiplexer_30 (
    .in0(multiplexer_29_out), .in1(multiplexer_25_out), .out(multiplexer_30_out), .sel(or_31_out));
  Comparator #(.width(32)) comparator_27 (
    .a(multiplexer_26_out), .b({32{1'b1}}), .eq(comparator_27_eq));  // open: gt, lt
  Multiplexer #(.width(32), .enable("false")) multiplexer_31 (
    .in0(multiplexer_30_out), .in1(multiplexer_26_out), .out(multiplexer_31_out), .sel(or_32_out));
  Comparator #(.width(32)) comparator_28 (
    .a(multiplexer_27_out), .b({32{1'b1}}), .eq(comparator_28_eq));  // open: gt, lt
  or or_29 (or_29_out, comparator_32_eq, or_36_out);
  Multiplexer #(.width(32), .enable("false")) multiplexer_32 (
    .in0(multiplexer_31_out), .in1(multiplexer_27_out), .out(multiplexer_32_out), .sel(or_29_out));
  Comparator #(.width(32)) comparator_29 (.a(R8), .b({32{1'b1}}), .eq(comparator_29_eq));  // open: gt, lt
  or or_30 (or_30_out, comparator_29_eq, or_33_out);
  Comparator #(.width(32)) comparator_30 (
    .a(multiplexer_29_out), .b({32{1'b1}}), .eq(comparator_30_eq));  // open: gt, lt
  or or_31 (or_31_out, comparator_30_eq, or_34_out);
  Comparator #(.width(32)) comparator_31 (
    .a(multiplexer_30_out), .b({32{1'b1}}), .eq(comparator_31_eq));  // open: gt, lt
  or or_32 (or_32_out, comparator_31_eq, or_35_out);
  Multiplexer #(.width(32), .enable("false")) multiplexer_33 (
    .in0(multiplexer_36_out), .in1(multiplexer_30_out), .out(multiplexer_33_out), .sel(or_35_out));
  Comparator #(.width(32)) comparator_32 (
    .a(multiplexer_31_out), .b({32{1'b1}}), .eq(comparator_32_eq));  // open: gt, lt
  Multiplexer #(.width(32), .enable("false")) multiplexer_34 (
    .in0(multiplexer_33_out), .in1(multiplexer_31_out), .out(multiplexer_34_out), .sel(or_36_out));
  Register #(.width(32)) register_8 (.D(multiplexer_32_out), .Q(R8_2), .clk(save), .clr(clr));  // open: en
  Comparator #(.width(32)) comparator_33 (.a(R9), .b({32{1'b1}}), .eq(comparator_33_eq));  // open: gt, lt
  or or_33 (or_33_out, comparator_33_eq, or_37_out);
  Multiplexer #(.width(32), .enable("false")) multiplexer_35 (
    .in0(R9), .in1(R8), .out(multiplexer_35_out), .sel(or_33_out));
  Comparator #(.width(32)) comparator_34 (
    .a(multiplexer_35_out), .b({32{1'b1}}), .eq(comparator_34_eq));  // open: gt, lt
  or or_34 (or_34_out, comparator_34_eq, or_38_out);
  Multiplexer #(.width(32), .enable("false")) multiplexer_36 (
    .in0(multiplexer_35_out), .in1(multiplexer_29_out), .out(multiplexer_36_out), .sel(or_34_out));
  Comparator #(.width(32)) comparator_35 (
    .a(multiplexer_36_out), .b({32{1'b1}}), .eq(comparator_35_eq));  // open: gt, lt
  or or_35 (or_35_out, comparator_35_eq, or_39_out);
  Comparator #(.width(32)) comparator_36 (
    .a(multiplexer_33_out), .b({32{1'b1}}), .eq(comparator_36_eq));  // open: gt, lt
  or or_36 (or_36_out, comparator_36_eq, or_40_out);
  Register #(.width(32)) register_9 (.D(multiplexer_34_out), .Q(R9_2), .clk(save), .clr(clr));  // open: en
  or or_37 (or_37_out, comparator_39_eq, or_44_out);
  Multiplexer #(.width(32), .enable("false")) multiplexer_37 (
    .in0(R10), .in1(R9), .out(multiplexer_37_out), .sel(or_37_out));
  or or_38 (or_38_out, comparator_40_eq, or_41_out);
  Multiplexer #(.width(32), .enable("false")) multiplexer_38 (
    .in0(multiplexer_37_out), .in1(multiplexer_35_out), .out(multiplexer_38_out), .sel(or_38_out));
  Comparator #(.width(32)) comparator_37 (
    .a(multiplexer_38_out), .b({32{1'b1}}), .eq(comparator_37_eq));  // open: gt, lt
  or or_39 (or_39_out, comparator_37_eq, or_42_out);
  Multiplexer #(.width(32), .enable("false")) multiplexer_39 (
    .in0(multiplexer_38_out), .in1(multiplexer_36_out), .out(multiplexer_39_out), .sel(or_39_out));
  Comparator #(.width(32)) comparator_38 (
    .a(multiplexer_39_out), .b({32{1'b1}}), .eq(comparator_38_eq));  // open: gt, lt
  or or_40 (or_40_out, comparator_38_eq, or_43_out);
  Multiplexer #(.width(32), .enable("false")) multiplexer_40 (
    .in0(multiplexer_39_out), .in1(multiplexer_33_out), .out(multiplexer_40_out), .sel(or_40_out));
  Register #(.width(32)) register_10 (.D(multiplexer_40_out), .Q(R10_2), .clk(save), .clr(clr));  // open: en
  Comparator #(.width(32)) comparator_39 (.a(R10), .b({32{1'b1}}), .eq(comparator_39_eq));  // open: gt, lt
  Multiplexer #(.width(32), .enable("false")) multiplexer_41 (
    .in0(R11), .in1(R10), .out(multiplexer_41_out), .sel(or_44_out));
  Comparator #(.width(32)) comparator_40 (
    .a(multiplexer_37_out), .b({32{1'b1}}), .eq(comparator_40_eq));  // open: gt, lt
  or or_41 (or_41_out, comparator_42_eq, or_47_out);
  Multiplexer #(.width(32), .enable("false")) multiplexer_42 (
    .in0(multiplexer_41_out), .in1(multiplexer_37_out), .out(multiplexer_42_out), .sel(or_41_out));
  or or_42 (or_42_out, comparator_43_eq, or_48_out);
  Multiplexer #(.width(32), .enable("false")) multiplexer_43 (
    .in0(multiplexer_42_out), .in1(multiplexer_38_out), .out(multiplexer_43_out), .sel(or_42_out));
  or or_43 (or_43_out, comparator_44_eq, or_45_out);
  Multiplexer #(.width(32), .enable("false")) multiplexer_44 (
    .in0(multiplexer_43_out), .in1(multiplexer_39_out), .out(multiplexer_44_out), .sel(or_43_out));
  Register #(.width(32)) register_11 (.D(multiplexer_44_out), .Q(R11_2), .clk(save), .clr(clr));  // open: en
  Comparator #(.width(32)) comparator_41 (.a(R11), .b({32{1'b1}}), .eq(comparator_41_eq));  // open: gt, lt
  or or_44 (or_44_out, comparator_41_eq, or_46_out);
  Multiplexer #(.width(32), .enable("false")) multiplexer_45 (
    .in0(R12), .in1(R11), .out(multiplexer_45_out), .sel(or_46_out));
  Comparator #(.width(32)) comparator_42 (
    .a(multiplexer_41_out), .b({32{1'b1}}), .eq(comparator_42_eq));  // open: gt, lt
  Multiplexer #(.width(32), .enable("false")) multiplexer_46 (
    .in0(multiplexer_45_out), .in1(multiplexer_41_out), .out(multiplexer_46_out), .sel(or_47_out));
  Comparator #(.width(32)) comparator_43 (
    .a(multiplexer_42_out), .b({32{1'b1}}), .eq(comparator_43_eq));  // open: gt, lt
  Multiplexer #(.width(32), .enable("false")) multiplexer_47 (
    .in0(multiplexer_46_out), .in1(multiplexer_42_out), .out(multiplexer_47_out), .sel(or_48_out));
  Comparator #(.width(32)) comparator_44 (
    .a(multiplexer_43_out), .b({32{1'b1}}), .eq(comparator_44_eq));  // open: gt, lt
  or or_45 (or_45_out, comparator_48_eq, or_52_out);
  Multiplexer #(.width(32), .enable("false")) multiplexer_48 (
    .in0(multiplexer_47_out), .in1(multiplexer_43_out), .out(multiplexer_48_out), .sel(or_45_out));
  Comparator #(.width(32)) comparator_45 (.a(R12), .b({32{1'b1}}), .eq(comparator_45_eq));  // open: gt, lt
  or or_46 (or_46_out, comparator_45_eq, or_49_out);
  Comparator #(.width(32)) comparator_46 (
    .a(multiplexer_45_out), .b({32{1'b1}}), .eq(comparator_46_eq));  // open: gt, lt
  or or_47 (or_47_out, comparator_46_eq, or_50_out);
  Comparator #(.width(32)) comparator_47 (
    .a(multiplexer_46_out), .b({32{1'b1}}), .eq(comparator_47_eq));  // open: gt, lt
  or or_48 (or_48_out, comparator_47_eq, or_51_out);
  Multiplexer #(.width(32), .enable("false")) multiplexer_49 (
    .in0(multiplexer_52_out), .in1(multiplexer_46_out), .out(multiplexer_49_out), .sel(or_51_out));
  Comparator #(.width(32)) comparator_48 (
    .a(multiplexer_47_out), .b({32{1'b1}}), .eq(comparator_48_eq));  // open: gt, lt
  Multiplexer #(.width(32), .enable("false")) multiplexer_50 (
    .in0(multiplexer_49_out), .in1(multiplexer_47_out), .out(multiplexer_50_out), .sel(or_52_out));
  Register #(.width(32)) register_12 (.D(multiplexer_48_out), .Q(R12_2), .clk(save), .clr(clr));  // open: en
  Comparator #(.width(32)) comparator_49 (.a(R13), .b({32{1'b1}}), .eq(comparator_49_eq));  // open: gt, lt
  or or_49 (or_49_out, comparator_49_eq, or_53_out);
  Multiplexer #(.width(32), .enable("false")) multiplexer_51 (
    .in0(R13), .in1(R12), .out(multiplexer_51_out), .sel(or_49_out));
  Comparator #(.width(32)) comparator_50 (
    .a(multiplexer_51_out), .b({32{1'b1}}), .eq(comparator_50_eq));  // open: gt, lt
  or or_50 (or_50_out, comparator_50_eq, or_54_out);
  Multiplexer #(.width(32), .enable("false")) multiplexer_52 (
    .in0(multiplexer_51_out), .in1(multiplexer_45_out), .out(multiplexer_52_out), .sel(or_50_out));
  Comparator #(.width(32)) comparator_51 (
    .a(multiplexer_52_out), .b({32{1'b1}}), .eq(comparator_51_eq));  // open: gt, lt
  or or_51 (or_51_out, comparator_51_eq, or_55_out);
  Comparator #(.width(32)) comparator_52 (
    .a(multiplexer_49_out), .b({32{1'b1}}), .eq(comparator_52_eq));  // open: gt, lt
  or or_52 (or_52_out, comparator_52_eq, or_56_out);
  Register #(.width(32)) register_13 (.D(multiplexer_50_out), .Q(R13_2), .clk(save), .clr(clr));  // open: en
  or or_53 (or_53_out, comparator_55_eq, or_60_out);
  Multiplexer #(.width(32), .enable("false")) multiplexer_53 (
    .in0(R14), .in1(R13), .out(multiplexer_53_out), .sel(or_53_out));
  or or_54 (or_54_out, comparator_56_eq, or_57_out);
  Multiplexer #(.width(32), .enable("false")) multiplexer_54 (
    .in0(multiplexer_53_out), .in1(multiplexer_51_out), .out(multiplexer_54_out), .sel(or_54_out));
  Comparator #(.width(32)) comparator_53 (
    .a(multiplexer_54_out), .b({32{1'b1}}), .eq(comparator_53_eq));  // open: gt, lt
  or or_55 (or_55_out, comparator_53_eq, or_58_out);
  Multiplexer #(.width(32), .enable("false")) multiplexer_55 (
    .in0(multiplexer_54_out), .in1(multiplexer_52_out), .out(multiplexer_55_out), .sel(or_55_out));
  Comparator #(.width(32)) comparator_54 (
    .a(multiplexer_55_out), .b({32{1'b1}}), .eq(comparator_54_eq));  // open: gt, lt
  or or_56 (or_56_out, comparator_54_eq, or_59_out);
  Multiplexer #(.width(32), .enable("false")) multiplexer_56 (
    .in0(multiplexer_55_out), .in1(multiplexer_49_out), .out(multiplexer_56_out), .sel(or_56_out));
  Register #(.width(32)) register_14 (.D(multiplexer_56_out), .Q(R14_2), .clk(save), .clr(clr));  // open: en
  Comparator #(.width(32)) comparator_55 (.a(R14), .b({32{1'b1}}), .eq(comparator_55_eq));  // open: gt, lt
  Multiplexer #(.width(32), .enable("false")) multiplexer_57 (
    .in0(R15), .in1(R14), .out(multiplexer_57_out), .sel(or_60_out));
  Comparator #(.width(32)) comparator_56 (
    .a(multiplexer_53_out), .b({32{1'b1}}), .eq(comparator_56_eq));  // open: gt, lt
  or or_57 (or_57_out, comparator_58_eq, or_63_out);
  Multiplexer #(.width(32), .enable("false")) multiplexer_58 (
    .in0(multiplexer_57_out), .in1(multiplexer_53_out), .out(multiplexer_58_out), .sel(or_57_out));
  or or_58 (or_58_out, comparator_59_eq, or_64_out);
  Multiplexer #(.width(32), .enable("false")) multiplexer_59 (
    .in0(multiplexer_58_out), .in1(multiplexer_54_out), .out(multiplexer_59_out), .sel(or_58_out));
  or or_59 (or_59_out, comparator_60_eq, or_61_out);
  Multiplexer #(.width(32), .enable("false")) multiplexer_60 (
    .in0(multiplexer_59_out), .in1(multiplexer_55_out), .out(multiplexer_60_out), .sel(or_59_out));
  Register #(.width(32)) register_15 (.D(multiplexer_60_out), .Q(R15_2), .clk(save), .clr(clr));  // open: en
  Comparator #(.width(32)) comparator_57 (.a(R15), .b({32{1'b1}}), .eq(comparator_57_eq));  // open: gt, lt
  or or_60 (or_60_out, comparator_57_eq, or_62_out);
  Multiplexer #(.width(32), .enable("false")) multiplexer_61 (
    .in0(R16), .in1(R15), .out(multiplexer_61_out), .sel(or_62_out));
  Comparator #(.width(32)) comparator_58 (
    .a(multiplexer_57_out), .b({32{1'b1}}), .eq(comparator_58_eq));  // open: gt, lt
  Multiplexer #(.width(32), .enable("false")) multiplexer_62 (
    .in0(multiplexer_61_out), .in1(multiplexer_57_out), .out(multiplexer_62_out), .sel(or_63_out));
  Comparator #(.width(32)) comparator_59 (
    .a(multiplexer_58_out), .b({32{1'b1}}), .eq(comparator_59_eq));  // open: gt, lt
  Multiplexer #(.width(32), .enable("false")) multiplexer_63 (
    .in0(multiplexer_62_out), .in1(multiplexer_58_out), .out(multiplexer_63_out), .sel(or_64_out));
  Comparator #(.width(32)) comparator_60 (
    .a(multiplexer_59_out), .b({32{1'b1}}), .eq(comparator_60_eq));  // open: gt, lt
  or or_61 (or_61_out, comparator_64_eq, or_68_out);
  Multiplexer #(.width(32), .enable("false")) multiplexer_64 (
    .in0(multiplexer_63_out), .in1(multiplexer_59_out), .out(multiplexer_64_out), .sel(or_61_out));
  Comparator #(.width(32)) comparator_61 (.a(R16), .b({32{1'b1}}), .eq(comparator_61_eq));  // open: gt, lt
  or or_62 (or_62_out, comparator_61_eq, or_65_out);
  Comparator #(.width(32)) comparator_62 (
    .a(multiplexer_61_out), .b({32{1'b1}}), .eq(comparator_62_eq));  // open: gt, lt
  or or_63 (or_63_out, comparator_62_eq, or_66_out);
  Comparator #(.width(32)) comparator_63 (
    .a(multiplexer_62_out), .b({32{1'b1}}), .eq(comparator_63_eq));  // open: gt, lt
  or or_64 (or_64_out, comparator_63_eq, or_67_out);
  Multiplexer #(.width(32), .enable("false")) multiplexer_65 (
    .in0(multiplexer_68_out), .in1(multiplexer_62_out), .out(multiplexer_65_out), .sel(or_67_out));
  Comparator #(.width(32)) comparator_64 (
    .a(multiplexer_63_out), .b({32{1'b1}}), .eq(comparator_64_eq));  // open: gt, lt
  Multiplexer #(.width(32), .enable("false")) multiplexer_66 (
    .in0(multiplexer_65_out), .in1(multiplexer_63_out), .out(multiplexer_66_out), .sel(or_68_out));
  Register #(.width(32)) register_16 (.D(multiplexer_64_out), .Q(R16_2), .clk(save), .clr(clr));  // open: en
  Comparator #(.width(32)) comparator_65 (.a(R17), .b({32{1'b1}}), .eq(comparator_65_eq));  // open: gt, lt
  or or_65 (or_65_out, comparator_65_eq, or_69_out);
  Multiplexer #(.width(32), .enable("false")) multiplexer_67 (
    .in0(R17), .in1(R16), .out(multiplexer_67_out), .sel(or_65_out));
  Comparator #(.width(32)) comparator_66 (
    .a(multiplexer_67_out), .b({32{1'b1}}), .eq(comparator_66_eq));  // open: gt, lt
  or or_66 (or_66_out, comparator_66_eq, or_70_out);
  Multiplexer #(.width(32), .enable("false")) multiplexer_68 (
    .in0(multiplexer_67_out), .in1(multiplexer_61_out), .out(multiplexer_68_out), .sel(or_66_out));
  Comparator #(.width(32)) comparator_67 (
    .a(multiplexer_68_out), .b({32{1'b1}}), .eq(comparator_67_eq));  // open: gt, lt
  or or_67 (or_67_out, comparator_67_eq, or_71_out);
  Comparator #(.width(32)) comparator_68 (
    .a(multiplexer_65_out), .b({32{1'b1}}), .eq(comparator_68_eq));  // open: gt, lt
  or or_68 (or_68_out, comparator_68_eq, or_72_out);
  Register #(.width(32)) register_17 (.D(multiplexer_66_out), .Q(R17_2), .clk(save), .clr(clr));  // open: en
  or or_69 (or_69_out, comparator_71_eq, or_76_out);
  Multiplexer #(.width(32), .enable("false")) multiplexer_69 (
    .in0(R18), .in1(R17), .out(multiplexer_69_out), .sel(or_69_out));
  or or_70 (or_70_out, comparator_72_eq, or_73_out);
  Multiplexer #(.width(32), .enable("false")) multiplexer_70 (
    .in0(multiplexer_69_out), .in1(multiplexer_67_out), .out(multiplexer_70_out), .sel(or_70_out));
  Comparator #(.width(32)) comparator_69 (
    .a(multiplexer_70_out), .b({32{1'b1}}), .eq(comparator_69_eq));  // open: gt, lt
  or or_71 (or_71_out, comparator_69_eq, or_74_out);
  Multiplexer #(.width(32), .enable("false")) multiplexer_71 (
    .in0(multiplexer_70_out), .in1(multiplexer_68_out), .out(multiplexer_71_out), .sel(or_71_out));
  Comparator #(.width(32)) comparator_70 (
    .a(multiplexer_71_out), .b({32{1'b1}}), .eq(comparator_70_eq));  // open: gt, lt
  or or_72 (or_72_out, comparator_70_eq, or_75_out);
  Multiplexer #(.width(32), .enable("false")) multiplexer_72 (
    .in0(multiplexer_71_out), .in1(multiplexer_65_out), .out(multiplexer_72_out), .sel(or_72_out));
  Register #(.width(32)) register_18 (.D(multiplexer_72_out), .Q(R18_2), .clk(save), .clr(clr));  // open: en
  Comparator #(.width(32)) comparator_71 (.a(R18), .b({32{1'b1}}), .eq(comparator_71_eq));  // open: gt, lt
  Multiplexer #(.width(32), .enable("false")) multiplexer_73 (
    .in0(R19), .in1(R18), .out(multiplexer_73_out), .sel(or_76_out));
  Comparator #(.width(32)) comparator_72 (
    .a(multiplexer_69_out), .b({32{1'b1}}), .eq(comparator_72_eq));  // open: gt, lt
  or or_73 (or_73_out, comparator_74_eq, or_79_out);
  Multiplexer #(.width(32), .enable("false")) multiplexer_74 (
    .in0(multiplexer_73_out), .in1(multiplexer_69_out), .out(multiplexer_74_out), .sel(or_73_out));
  or or_74 (or_74_out, comparator_75_eq, or_80_out);
  Multiplexer #(.width(32), .enable("false")) multiplexer_75 (
    .in0(multiplexer_74_out), .in1(multiplexer_70_out), .out(multiplexer_75_out), .sel(or_74_out));
  or or_75 (or_75_out, comparator_76_eq, or_77_out);
  Multiplexer #(.width(32), .enable("false")) multiplexer_76 (
    .in0(multiplexer_75_out), .in1(multiplexer_71_out), .out(multiplexer_76_out), .sel(or_75_out));
  Register #(.width(32)) register_19 (.D(multiplexer_76_out), .Q(R19_2), .clk(save), .clr(clr));  // open: en
  Comparator #(.width(32)) comparator_73 (.a(R19), .b({32{1'b1}}), .eq(comparator_73_eq));  // open: gt, lt
  or or_76 (or_76_out, comparator_73_eq, or_78_out);
  Multiplexer #(.width(32), .enable("false")) multiplexer_77 (
    .in0(R20), .in1(R19), .out(multiplexer_77_out), .sel(or_78_out));
  Comparator #(.width(32)) comparator_74 (
    .a(multiplexer_73_out), .b({32{1'b1}}), .eq(comparator_74_eq));  // open: gt, lt
  Multiplexer #(.width(32), .enable("false")) multiplexer_78 (
    .in0(multiplexer_77_out), .in1(multiplexer_73_out), .out(multiplexer_78_out), .sel(or_79_out));
  Comparator #(.width(32)) comparator_75 (
    .a(multiplexer_74_out), .b({32{1'b1}}), .eq(comparator_75_eq));  // open: gt, lt
  Multiplexer #(.width(32), .enable("false")) multiplexer_79 (
    .in0(multiplexer_78_out), .in1(multiplexer_74_out), .out(multiplexer_79_out), .sel(or_80_out));
  Comparator #(.width(32)) comparator_76 (
    .a(multiplexer_75_out), .b({32{1'b1}}), .eq(comparator_76_eq));  // open: gt, lt
  or or_77 (or_77_out, comparator_80_eq, or_84_out);
  Multiplexer #(.width(32), .enable("false")) multiplexer_80 (
    .in0(multiplexer_79_out), .in1(multiplexer_75_out), .out(multiplexer_80_out), .sel(or_77_out));
  Comparator #(.width(32)) comparator_77 (.a(R20), .b({32{1'b1}}), .eq(comparator_77_eq));  // open: gt, lt
  or or_78 (or_78_out, comparator_77_eq, or_81_out);
  Comparator #(.width(32)) comparator_78 (
    .a(multiplexer_77_out), .b({32{1'b1}}), .eq(comparator_78_eq));  // open: gt, lt
  or or_79 (or_79_out, comparator_78_eq, or_82_out);
  Comparator #(.width(32)) comparator_79 (
    .a(multiplexer_78_out), .b({32{1'b1}}), .eq(comparator_79_eq));  // open: gt, lt
  or or_80 (or_80_out, comparator_79_eq, or_83_out);
  Multiplexer #(.width(32), .enable("false")) multiplexer_81 (
    .in0(multiplexer_84_out), .in1(multiplexer_78_out), .out(multiplexer_81_out), .sel(or_83_out));
  Comparator #(.width(32)) comparator_80 (
    .a(multiplexer_79_out), .b({32{1'b1}}), .eq(comparator_80_eq));  // open: gt, lt
  Multiplexer #(.width(32), .enable("false")) multiplexer_82 (
    .in0(multiplexer_81_out), .in1(multiplexer_79_out), .out(multiplexer_82_out), .sel(or_84_out));
  Register #(.width(32)) register_20 (.D(multiplexer_80_out), .Q(R20_2), .clk(save), .clr(clr));  // open: en
  Comparator #(.width(32)) comparator_81 (.a(R21), .b({32{1'b1}}), .eq(comparator_81_eq));  // open: gt, lt
  or or_81 (or_81_out, comparator_81_eq, or_85_out);
  Multiplexer #(.width(32), .enable("false")) multiplexer_83 (
    .in0(R21), .in1(R20), .out(multiplexer_83_out), .sel(or_81_out));
  Comparator #(.width(32)) comparator_82 (
    .a(multiplexer_83_out), .b({32{1'b1}}), .eq(comparator_82_eq));  // open: gt, lt
  or or_82 (or_82_out, comparator_82_eq, or_86_out);
  Multiplexer #(.width(32), .enable("false")) multiplexer_84 (
    .in0(multiplexer_83_out), .in1(multiplexer_77_out), .out(multiplexer_84_out), .sel(or_82_out));
  Comparator #(.width(32)) comparator_83 (
    .a(multiplexer_84_out), .b({32{1'b1}}), .eq(comparator_83_eq));  // open: gt, lt
  or or_83 (or_83_out, comparator_83_eq, or_87_out);
  Comparator #(.width(32)) comparator_84 (
    .a(multiplexer_81_out), .b({32{1'b1}}), .eq(comparator_84_eq));  // open: gt, lt
  or or_84 (or_84_out, comparator_84_eq, or_88_out);
  Register #(.width(32)) register_21 (.D(multiplexer_82_out), .Q(R21_2), .clk(save), .clr(clr));  // open: en
  or or_85 (or_85_out, comparator_87_eq, or_92_out);
  Multiplexer #(.width(32), .enable("false")) multiplexer_85 (
    .in0(R22), .in1(R21), .out(multiplexer_85_out), .sel(or_85_out));
  or or_86 (or_86_out, comparator_88_eq, or_89_out);
  Multiplexer #(.width(32), .enable("false")) multiplexer_86 (
    .in0(multiplexer_85_out), .in1(multiplexer_83_out), .out(multiplexer_86_out), .sel(or_86_out));
  Comparator #(.width(32)) comparator_85 (
    .a(multiplexer_86_out), .b({32{1'b1}}), .eq(comparator_85_eq));  // open: gt, lt
  or or_87 (or_87_out, comparator_85_eq, or_90_out);
  Multiplexer #(.width(32), .enable("false")) multiplexer_87 (
    .in0(multiplexer_86_out), .in1(multiplexer_84_out), .out(multiplexer_87_out), .sel(or_87_out));
  Comparator #(.width(32)) comparator_86 (
    .a(multiplexer_87_out), .b({32{1'b1}}), .eq(comparator_86_eq));  // open: gt, lt
  or or_88 (or_88_out, comparator_86_eq, or_91_out);
  Multiplexer #(.width(32), .enable("false")) multiplexer_88 (
    .in0(multiplexer_87_out), .in1(multiplexer_81_out), .out(multiplexer_88_out), .sel(or_88_out));
  Register #(.width(32)) register_22 (.D(multiplexer_88_out), .Q(R22_2), .clk(save), .clr(clr));  // open: en
  Comparator #(.width(32)) comparator_87 (.a(R22), .b({32{1'b1}}), .eq(comparator_87_eq));  // open: gt, lt
  Multiplexer #(.width(32), .enable("false")) multiplexer_89 (
    .in0(R23), .in1(R22), .out(multiplexer_89_out), .sel(or_92_out));
  Comparator #(.width(32)) comparator_88 (
    .a(multiplexer_85_out), .b({32{1'b1}}), .eq(comparator_88_eq));  // open: gt, lt
  or or_89 (or_89_out, comparator_90_eq, or_95_out);
  Multiplexer #(.width(32), .enable("false")) multiplexer_90 (
    .in0(multiplexer_89_out), .in1(multiplexer_85_out), .out(multiplexer_90_out), .sel(or_89_out));
  or or_90 (or_90_out, comparator_91_eq, or_96_out);
  Multiplexer #(.width(32), .enable("false")) multiplexer_91 (
    .in0(multiplexer_90_out), .in1(multiplexer_86_out), .out(multiplexer_91_out), .sel(or_90_out));
  or or_91 (or_91_out, comparator_92_eq, or_93_out);
  Multiplexer #(.width(32), .enable("false")) multiplexer_92 (
    .in0(multiplexer_91_out), .in1(multiplexer_87_out), .out(multiplexer_92_out), .sel(or_91_out));
  Register #(.width(32)) register_23 (.D(multiplexer_92_out), .Q(R23_2), .clk(save), .clr(clr));  // open: en
  Comparator #(.width(32)) comparator_89 (.a(R23), .b({32{1'b1}}), .eq(comparator_89_eq));  // open: gt, lt
  or or_92 (or_92_out, comparator_89_eq, or_94_out);
  Multiplexer #(.width(32), .enable("false")) multiplexer_93 (
    .in0(R24), .in1(R23), .out(multiplexer_93_out), .sel(or_94_out));
  Comparator #(.width(32)) comparator_90 (
    .a(multiplexer_89_out), .b({32{1'b1}}), .eq(comparator_90_eq));  // open: gt, lt
  Multiplexer #(.width(32), .enable("false")) multiplexer_94 (
    .in0(multiplexer_93_out), .in1(multiplexer_89_out), .out(multiplexer_94_out), .sel(or_95_out));
  Comparator #(.width(32)) comparator_91 (
    .a(multiplexer_90_out), .b({32{1'b1}}), .eq(comparator_91_eq));  // open: gt, lt
  Multiplexer #(.width(32), .enable("false")) multiplexer_95 (
    .in0(multiplexer_94_out), .in1(multiplexer_90_out), .out(multiplexer_95_out), .sel(or_96_out));
  Comparator #(.width(32)) comparator_92 (
    .a(multiplexer_91_out), .b({32{1'b1}}), .eq(comparator_92_eq));  // open: gt, lt
  or or_93 (or_93_out, comparator_96_eq, or_100_out);
  Multiplexer #(.width(32), .enable("false")) multiplexer_96 (
    .in0(multiplexer_95_out), .in1(multiplexer_91_out), .out(multiplexer_96_out), .sel(or_93_out));
  Comparator #(.width(32)) comparator_93 (.a(R24), .b({32{1'b1}}), .eq(comparator_93_eq));  // open: gt, lt
  or or_94 (or_94_out, comparator_93_eq, or_97_out);
  Comparator #(.width(32)) comparator_94 (
    .a(multiplexer_93_out), .b({32{1'b1}}), .eq(comparator_94_eq));  // open: gt, lt
  or or_95 (or_95_out, comparator_94_eq, or_98_out);
  Comparator #(.width(32)) comparator_95 (
    .a(multiplexer_94_out), .b({32{1'b1}}), .eq(comparator_95_eq));  // open: gt, lt
  or or_96 (or_96_out, comparator_95_eq, or_99_out);
  Multiplexer #(.width(32), .enable("false")) multiplexer_97 (
    .in0(multiplexer_100_out), .in1(multiplexer_94_out), .out(multiplexer_97_out), .sel(or_99_out));
  Comparator #(.width(32)) comparator_96 (
    .a(multiplexer_95_out), .b({32{1'b1}}), .eq(comparator_96_eq));  // open: gt, lt
  Multiplexer #(.width(32), .enable("false")) multiplexer_98 (
    .in0(multiplexer_97_out), .in1(multiplexer_95_out), .out(multiplexer_98_out), .sel(or_100_out));
  Register #(.width(32)) register_24 (.D(multiplexer_96_out), .Q(R24_2), .clk(save), .clr(clr));  // open: en
  Comparator #(.width(32)) comparator_97 (.a(R25), .b({32{1'b1}}), .eq(comparator_97_eq));  // open: gt, lt
  or or_97 (or_97_out, comparator_97_eq, or_101_out);
  Multiplexer #(.width(32), .enable("false")) multiplexer_99 (
    .in0(R25), .in1(R24), .out(multiplexer_99_out), .sel(or_97_out));
  Comparator #(.width(32)) comparator_98 (
    .a(multiplexer_99_out), .b({32{1'b1}}), .eq(comparator_98_eq));  // open: gt, lt
  or or_98 (or_98_out, comparator_98_eq, or_102_out);
  Multiplexer #(.width(32), .enable("false")) multiplexer_100 (
    .in0(multiplexer_99_out), .in1(multiplexer_93_out), .out(multiplexer_100_out), .sel(or_98_out));
  Comparator #(.width(32)) comparator_99 (
    .a(multiplexer_100_out), .b({32{1'b1}}), .eq(comparator_99_eq));  // open: gt, lt
  or or_99 (or_99_out, comparator_99_eq, or_103_out);
  Comparator #(.width(32)) comparator_100 (
    .a(multiplexer_97_out), .b({32{1'b1}}), .eq(comparator_100_eq));  // open: gt, lt
  or or_100 (or_100_out, comparator_100_eq, or_104_out);
  Register #(.width(32)) register_25 (.D(multiplexer_98_out), .Q(R25_2), .clk(save), .clr(clr));  // open: en
  or or_101 (or_101_out, comparator_103_eq, or_108_out);
  Multiplexer #(.width(32), .enable("false")) multiplexer_101 (
    .in0(R26), .in1(R25), .out(multiplexer_101_out), .sel(or_101_out));
  or or_102 (or_102_out, comparator_104_eq, or_105_out);
  Multiplexer #(.width(32), .enable("false")) multiplexer_102 (
    .in0(multiplexer_101_out), .in1(multiplexer_99_out), .out(multiplexer_102_out), .sel(or_102_out));
  Comparator #(.width(32)) comparator_101 (
    .a(multiplexer_102_out), .b({32{1'b1}}), .eq(comparator_101_eq));  // open: gt, lt
  or or_103 (or_103_out, comparator_101_eq, or_106_out);
  Multiplexer #(.width(32), .enable("false")) multiplexer_103 (
    .in0(multiplexer_102_out), .in1(multiplexer_100_out), .out(multiplexer_103_out), .sel(or_103_out));
  Comparator #(.width(32)) comparator_102 (
    .a(multiplexer_103_out), .b({32{1'b1}}), .eq(comparator_102_eq));  // open: gt, lt
  or or_104 (or_104_out, comparator_102_eq, or_107_out);
  Multiplexer #(.width(32), .enable("false")) multiplexer_104 (
    .in0(multiplexer_103_out), .in1(multiplexer_97_out), .out(multiplexer_104_out), .sel(or_104_out));
  Register #(.width(32)) register_26 (.D(multiplexer_104_out), .Q(R26_2), .clk(save), .clr(clr));  // open: en
  Comparator #(.width(32)) comparator_103 (.a(R26), .b({32{1'b1}}), .eq(comparator_103_eq));  // open: gt, lt
  Multiplexer #(.width(32), .enable("false")) multiplexer_105 (
    .in0(R27), .in1(R26), .out(multiplexer_105_out), .sel(or_108_out));
  Comparator #(.width(32)) comparator_104 (
    .a(multiplexer_101_out), .b({32{1'b1}}), .eq(comparator_104_eq));  // open: gt, lt
  or or_105 (or_105_out, comparator_106_eq, or_111_out);
  Multiplexer #(.width(32), .enable("false")) multiplexer_106 (
    .in0(multiplexer_105_out), .in1(multiplexer_101_out), .out(multiplexer_106_out), .sel(or_105_out));
  or or_106 (or_106_out, comparator_107_eq, or_112_out);
  Multiplexer #(.width(32), .enable("false")) multiplexer_107 (
    .in0(multiplexer_106_out), .in1(multiplexer_102_out), .out(multiplexer_107_out), .sel(or_106_out));
  or or_107 (or_107_out, comparator_108_eq, or_109_out);
  Multiplexer #(.width(32), .enable("false")) multiplexer_108 (
    .in0(multiplexer_107_out), .in1(multiplexer_103_out), .out(multiplexer_108_out), .sel(or_107_out));
  Register #(.width(32)) register_27 (.D(multiplexer_108_out), .Q(R27_2), .clk(save), .clr(clr));  // open: en
  Comparator #(.width(32)) comparator_105 (.a(R27), .b({32{1'b1}}), .eq(comparator_105_eq));  // open: gt, lt
  or or_108 (or_108_out, comparator_105_eq, or_110_out);
  Multiplexer #(.width(32), .enable("false")) multiplexer_109 (
    .in0(R28), .in1(R27), .out(multiplexer_109_out), .sel(or_110_out));
  Comparator #(.width(32)) comparator_106 (
    .a(multiplexer_105_out), .b({32{1'b1}}), .eq(comparator_106_eq));  // open: gt, lt
  Multiplexer #(.width(32), .enable("false")) multiplexer_110 (
    .in0(multiplexer_109_out), .in1(multiplexer_105_out), .out(multiplexer_110_out), .sel(or_111_out));
  Comparator #(.width(32)) comparator_107 (
    .a(multiplexer_106_out), .b({32{1'b1}}), .eq(comparator_107_eq));  // open: gt, lt
  Multiplexer #(.width(32), .enable("false")) multiplexer_111 (
    .in0(multiplexer_110_out), .in1(multiplexer_106_out), .out(multiplexer_111_out), .sel(or_112_out));
  Comparator #(.width(32)) comparator_108 (
    .a(multiplexer_107_out), .b({32{1'b1}}), .eq(comparator_108_eq));  // open: gt, lt
  or or_109 (or_109_out, comparator_112_eq, or_116_out);
  Multiplexer #(.width(32), .enable("false")) multiplexer_112 (
    .in0(multiplexer_111_out), .in1(multiplexer_107_out), .out(multiplexer_112_out), .sel(or_109_out));
  Comparator #(.width(32)) comparator_109 (.a(R28), .b({32{1'b1}}), .eq(comparator_109_eq));  // open: gt, lt
  or or_110 (or_110_out, comparator_109_eq, or_113_out);
  Comparator #(.width(32)) comparator_110 (
    .a(multiplexer_109_out), .b({32{1'b1}}), .eq(comparator_110_eq));  // open: gt, lt
  or or_111 (or_111_out, comparator_110_eq, or_114_out);
  Comparator #(.width(32)) comparator_111 (
    .a(multiplexer_110_out), .b({32{1'b1}}), .eq(comparator_111_eq));  // open: gt, lt
  or or_112 (or_112_out, comparator_111_eq, or_115_out);
  Multiplexer #(.width(32), .enable("false")) multiplexer_113 (
    .in0(multiplexer_116_out), .in1(multiplexer_110_out), .out(multiplexer_113_out), .sel(or_115_out));
  Comparator #(.width(32)) comparator_112 (
    .a(multiplexer_111_out), .b({32{1'b1}}), .eq(comparator_112_eq));  // open: gt, lt
  Multiplexer #(.width(32), .enable("false")) multiplexer_114 (
    .in0(multiplexer_113_out), .in1(multiplexer_111_out), .out(multiplexer_114_out), .sel(or_116_out));
  Register #(.width(32)) register_28 (.D(multiplexer_112_out), .Q(R28_2), .clk(save), .clr(clr));  // open: en
  Comparator #(.width(32)) comparator_113 (.a(R29), .b({32{1'b1}}), .eq(comparator_113_eq));  // open: gt, lt
  or or_113 (or_113_out, comparator_113_eq, or_117_out);
  Multiplexer #(.width(32), .enable("false")) multiplexer_115 (
    .in0(R29), .in1(R28), .out(multiplexer_115_out), .sel(or_113_out));
  Comparator #(.width(32)) comparator_114 (
    .a(multiplexer_115_out), .b({32{1'b1}}), .eq(comparator_114_eq));  // open: gt, lt
  or or_114 (or_114_out, comparator_114_eq, or_118_out);
  Multiplexer #(.width(32), .enable("false")) multiplexer_116 (
    .in0(multiplexer_115_out), .in1(multiplexer_109_out), .out(multiplexer_116_out), .sel(or_114_out));
  Comparator #(.width(32)) comparator_115 (
    .a(multiplexer_116_out), .b({32{1'b1}}), .eq(comparator_115_eq));  // open: gt, lt
  or or_115 (or_115_out, comparator_115_eq, or_119_out);
  Comparator #(.width(32)) comparator_116 (
    .a(multiplexer_113_out), .b({32{1'b1}}), .eq(comparator_116_eq));  // open: gt, lt
  or or_116 (or_116_out, comparator_116_eq, or_120_out);
  Register #(.width(32)) register_29 (.D(multiplexer_114_out), .Q(R29_2), .clk(save), .clr(clr));  // open: en
  or or_117 (or_117_out, comparator_119_eq, or_124_out);
  Multiplexer #(.width(32), .enable("false")) multiplexer_117 (
    .in0(R30), .in1(R29), .out(multiplexer_117_out), .sel(or_117_out));
  or or_118 (or_118_out, comparator_120_eq, or_121_out);
  Multiplexer #(.width(32), .enable("false")) multiplexer_118 (
    .in0(multiplexer_117_out), .in1(multiplexer_115_out), .out(multiplexer_118_out), .sel(or_118_out));
  Comparator #(.width(32)) comparator_117 (
    .a(multiplexer_118_out), .b({32{1'b1}}), .eq(comparator_117_eq));  // open: gt, lt
  or or_119 (or_119_out, comparator_117_eq, or_122_out);
  Multiplexer #(.width(32), .enable("false")) multiplexer_119 (
    .in0(multiplexer_118_out), .in1(multiplexer_116_out), .out(multiplexer_119_out), .sel(or_119_out));
  Comparator #(.width(32)) comparator_118 (
    .a(multiplexer_119_out), .b({32{1'b1}}), .eq(comparator_118_eq));  // open: gt, lt
  or or_120 (or_120_out, comparator_118_eq, or_123_out);
  Multiplexer #(.width(32), .enable("false")) multiplexer_120 (
    .in0(multiplexer_119_out), .in1(multiplexer_113_out), .out(multiplexer_120_out), .sel(or_120_out));
  Register #(.width(32)) register_30 (.D(multiplexer_120_out), .Q(R30_2), .clk(save), .clr(clr));  // open: en
  Comparator #(.width(32)) comparator_119 (.a(R30), .b({32{1'b1}}), .eq(comparator_119_eq));  // open: gt, lt
  Multiplexer #(.width(32), .enable("false")) multiplexer_121 (
    .in0(R31), .in1(R30), .out(multiplexer_121_out), .sel(or_124_out));
  Comparator #(.width(32)) comparator_120 (
    .a(multiplexer_117_out), .b({32{1'b1}}), .eq(comparator_120_eq));  // open: gt, lt
  or or_121 (or_121_out, comparator_122_eq, or_127_out);
  Multiplexer #(.width(32), .enable("false")) multiplexer_122 (
    .in0(multiplexer_121_out), .in1(multiplexer_117_out), .out(multiplexer_122_out), .sel(or_121_out));
  or or_122 (or_122_out, comparator_123_eq, or_128_out);
  Multiplexer #(.width(32), .enable("false")) multiplexer_123 (
    .in0(multiplexer_122_out), .in1(multiplexer_118_out), .out(multiplexer_123_out), .sel(or_122_out));
  or or_123 (or_123_out, comparator_124_eq, or_125_out);
  Multiplexer #(.width(32), .enable("false")) multiplexer_124 (
    .in0(multiplexer_123_out), .in1(multiplexer_119_out), .out(multiplexer_124_out), .sel(or_123_out));
  Register #(.width(32)) register_31 (.D(multiplexer_124_out), .Q(R31_2), .clk(save), .clr(clr));  // open: en
  Comparator #(.width(32)) comparator_121 (.a(R31), .b({32{1'b1}}), .eq(comparator_121_eq));  // open: gt, lt
  or or_124 (or_124_out, comparator_121_eq, or_126_out);
  Multiplexer #(.width(32), .enable("false")) multiplexer_125 (
    .in0(R32), .in1(R31), .out(multiplexer_125_out), .sel(or_126_out));
  Comparator #(.width(32)) comparator_122 (
    .a(multiplexer_121_out), .b({32{1'b1}}), .eq(comparator_122_eq));  // open: gt, lt
  Multiplexer #(.width(32), .enable("false")) multiplexer_126 (
    .in0(multiplexer_125_out), .in1(multiplexer_121_out), .out(multiplexer_126_out), .sel(or_127_out));
  Comparator #(.width(32)) comparator_123 (
    .a(multiplexer_122_out), .b({32{1'b1}}), .eq(comparator_123_eq));  // open: gt, lt
  Multiplexer #(.width(32), .enable("false")) multiplexer_127 (
    .in0(multiplexer_126_out), .in1(multiplexer_122_out), .out(multiplexer_127_out), .sel(or_128_out));
  Comparator #(.width(32)) comparator_124 (
    .a(multiplexer_123_out), .b({32{1'b1}}), .eq(comparator_124_eq));  // open: gt, lt
  or or_125 (or_125_out, comparator_128_eq, or_132_out);
  Multiplexer #(.width(32), .enable("false")) multiplexer_128 (
    .in0(multiplexer_127_out), .in1(multiplexer_123_out), .out(multiplexer_128_out), .sel(or_125_out));
  Comparator #(.width(32)) comparator_125 (.a(R32), .b({32{1'b1}}), .eq(comparator_125_eq));  // open: gt, lt
  or or_126 (or_126_out, comparator_125_eq, or_129_out);
  Comparator #(.width(32)) comparator_126 (
    .a(multiplexer_125_out), .b({32{1'b1}}), .eq(comparator_126_eq));  // open: gt, lt
  or or_127 (or_127_out, comparator_126_eq, or_130_out);
  Comparator #(.width(32)) comparator_127 (
    .a(multiplexer_126_out), .b({32{1'b1}}), .eq(comparator_127_eq));  // open: gt, lt
  or or_128 (or_128_out, comparator_127_eq, or_131_out);
  Multiplexer #(.width(32), .enable("false")) multiplexer_129 (
    .in0(multiplexer_132_out), .in1(multiplexer_126_out), .out(multiplexer_129_out), .sel(or_131_out));
  Comparator #(.width(32)) comparator_128 (
    .a(multiplexer_127_out), .b({32{1'b1}}), .eq(comparator_128_eq));  // open: gt, lt
  Multiplexer #(.width(32), .enable("false")) multiplexer_130 (
    .in0(multiplexer_129_out), .in1(multiplexer_127_out), .out(multiplexer_130_out), .sel(or_132_out));
  Register #(.width(32)) register_32 (.D(multiplexer_128_out), .Q(R32_2), .clk(save), .clr(clr));  // open: en
  Comparator #(.width(32)) comparator_129 (.a(R33), .b({32{1'b1}}), .eq(comparator_129_eq));  // open: gt, lt
  or or_129 (or_129_out, comparator_129_eq, or_133_out);
  Multiplexer #(.width(32), .enable("false")) multiplexer_131 (
    .in0(R33), .in1(R32), .out(multiplexer_131_out), .sel(or_129_out));
  Comparator #(.width(32)) comparator_130 (
    .a(multiplexer_131_out), .b({32{1'b1}}), .eq(comparator_130_eq));  // open: gt, lt
  or or_130 (or_130_out, comparator_130_eq, or_134_out);
  Multiplexer #(.width(32), .enable("false")) multiplexer_132 (
    .in0(multiplexer_131_out), .in1(multiplexer_125_out), .out(multiplexer_132_out), .sel(or_130_out));
  Comparator #(.width(32)) comparator_131 (
    .a(multiplexer_132_out), .b({32{1'b1}}), .eq(comparator_131_eq));  // open: gt, lt
  or or_131 (or_131_out, comparator_131_eq, or_135_out);
  Comparator #(.width(32)) comparator_132 (
    .a(multiplexer_129_out), .b({32{1'b1}}), .eq(comparator_132_eq));  // open: gt, lt
  or or_132 (or_132_out, comparator_132_eq, or_136_out);
  Register #(.width(32)) register_33 (.D(multiplexer_130_out), .Q(R33_2), .clk(save), .clr(clr));  // open: en
  or or_133 (or_133_out, comparator_135_eq, or_140_out);
  Multiplexer #(.width(32), .enable("false")) multiplexer_133 (
    .in0(R34), .in1(R33), .out(multiplexer_133_out), .sel(or_133_out));
  or or_134 (or_134_out, comparator_136_eq, or_137_out);
  Multiplexer #(.width(32), .enable("false")) multiplexer_134 (
    .in0(multiplexer_133_out), .in1(multiplexer_131_out), .out(multiplexer_134_out), .sel(or_134_out));
  Comparator #(.width(32)) comparator_133 (
    .a(multiplexer_134_out), .b({32{1'b1}}), .eq(comparator_133_eq));  // open: gt, lt
  or or_135 (or_135_out, comparator_133_eq, or_138_out);
  Multiplexer #(.width(32), .enable("false")) multiplexer_135 (
    .in0(multiplexer_134_out), .in1(multiplexer_132_out), .out(multiplexer_135_out), .sel(or_135_out));
  Comparator #(.width(32)) comparator_134 (
    .a(multiplexer_135_out), .b({32{1'b1}}), .eq(comparator_134_eq));  // open: gt, lt
  or or_136 (or_136_out, comparator_134_eq, or_139_out);
  Multiplexer #(.width(32), .enable("false")) multiplexer_136 (
    .in0(multiplexer_135_out), .in1(multiplexer_129_out), .out(multiplexer_136_out), .sel(or_136_out));
  Register #(.width(32)) register_34 (.D(multiplexer_136_out), .Q(R34_2), .clk(save), .clr(clr));  // open: en
  Comparator #(.width(32)) comparator_135 (.a(R34), .b({32{1'b1}}), .eq(comparator_135_eq));  // open: gt, lt
  Multiplexer #(.width(32), .enable("false")) multiplexer_137 (
    .in0(R35), .in1(R34), .out(multiplexer_137_out), .sel(or_140_out));
  Comparator #(.width(32)) comparator_136 (
    .a(multiplexer_133_out), .b({32{1'b1}}), .eq(comparator_136_eq));  // open: gt, lt
  or or_137 (or_137_out, comparator_138_eq, or_143_out);
  Multiplexer #(.width(32), .enable("false")) multiplexer_138 (
    .in0(multiplexer_137_out), .in1(multiplexer_133_out), .out(multiplexer_138_out), .sel(or_137_out));
  or or_138 (or_138_out, comparator_139_eq, or_144_out);
  Multiplexer #(.width(32), .enable("false")) multiplexer_139 (
    .in0(multiplexer_138_out), .in1(multiplexer_134_out), .out(multiplexer_139_out), .sel(or_138_out));
  or or_139 (or_139_out, comparator_140_eq, or_141_out);
  Multiplexer #(.width(32), .enable("false")) multiplexer_140 (
    .in0(multiplexer_139_out), .in1(multiplexer_135_out), .out(multiplexer_140_out), .sel(or_139_out));
  Register #(.width(32)) register_35 (.D(multiplexer_140_out), .Q(R35_2), .clk(save), .clr(clr));  // open: en
  Comparator #(.width(32)) comparator_137 (.a(R35), .b({32{1'b1}}), .eq(comparator_137_eq));  // open: gt, lt
  or or_140 (or_140_out, comparator_137_eq, or_142_out);
  Multiplexer #(.width(32), .enable("false")) multiplexer_141 (
    .in0(R36), .in1(R35), .out(multiplexer_141_out), .sel(or_142_out));
  Comparator #(.width(32)) comparator_138 (
    .a(multiplexer_137_out), .b({32{1'b1}}), .eq(comparator_138_eq));  // open: gt, lt
  Multiplexer #(.width(32), .enable("false")) multiplexer_142 (
    .in0(multiplexer_141_out), .in1(multiplexer_137_out), .out(multiplexer_142_out), .sel(or_143_out));
  Comparator #(.width(32)) comparator_139 (
    .a(multiplexer_138_out), .b({32{1'b1}}), .eq(comparator_139_eq));  // open: gt, lt
  Multiplexer #(.width(32), .enable("false")) multiplexer_143 (
    .in0(multiplexer_142_out), .in1(multiplexer_138_out), .out(multiplexer_143_out), .sel(or_144_out));
  Comparator #(.width(32)) comparator_140 (
    .a(multiplexer_139_out), .b({32{1'b1}}), .eq(comparator_140_eq));  // open: gt, lt
  or or_141 (or_141_out, comparator_144_eq, or_148_out);
  Multiplexer #(.width(32), .enable("false")) multiplexer_144 (
    .in0(multiplexer_143_out), .in1(multiplexer_139_out), .out(multiplexer_144_out), .sel(or_141_out));
  Comparator #(.width(32)) comparator_141 (.a(R36), .b({32{1'b1}}), .eq(comparator_141_eq));  // open: gt, lt
  or or_142 (or_142_out, comparator_141_eq, or_145_out);
  Comparator #(.width(32)) comparator_142 (
    .a(multiplexer_141_out), .b({32{1'b1}}), .eq(comparator_142_eq));  // open: gt, lt
  or or_143 (or_143_out, comparator_142_eq, or_146_out);
  Comparator #(.width(32)) comparator_143 (
    .a(multiplexer_142_out), .b({32{1'b1}}), .eq(comparator_143_eq));  // open: gt, lt
  or or_144 (or_144_out, comparator_143_eq, or_147_out);
  Multiplexer #(.width(32), .enable("false")) multiplexer_145 (
    .in0(multiplexer_148_out), .in1(multiplexer_142_out), .out(multiplexer_145_out), .sel(or_147_out));
  Comparator #(.width(32)) comparator_144 (
    .a(multiplexer_143_out), .b({32{1'b1}}), .eq(comparator_144_eq));  // open: gt, lt
  Multiplexer #(.width(32), .enable("false")) multiplexer_146 (
    .in0(multiplexer_145_out), .in1(multiplexer_143_out), .out(multiplexer_146_out), .sel(or_148_out));
  Register #(.width(32)) register_36 (.D(multiplexer_144_out), .Q(R36_2), .clk(save), .clr(clr));  // open: en
  Comparator #(.width(32)) comparator_145 (.a(R37), .b({32{1'b1}}), .eq(comparator_145_eq));  // open: gt, lt
  or or_145 (or_145_out, comparator_145_eq, or_149_out);
  Multiplexer #(.width(32), .enable("false")) multiplexer_147 (
    .in0(R37), .in1(R36), .out(multiplexer_147_out), .sel(or_145_out));
  Comparator #(.width(32)) comparator_146 (
    .a(multiplexer_147_out), .b({32{1'b1}}), .eq(comparator_146_eq));  // open: gt, lt
  or or_146 (or_146_out, comparator_146_eq, or_150_out);
  Multiplexer #(.width(32), .enable("false")) multiplexer_148 (
    .in0(multiplexer_147_out), .in1(multiplexer_141_out), .out(multiplexer_148_out), .sel(or_146_out));
  Comparator #(.width(32)) comparator_147 (
    .a(multiplexer_148_out), .b({32{1'b1}}), .eq(comparator_147_eq));  // open: gt, lt
  or or_147 (or_147_out, comparator_147_eq, or_151_out);
  Comparator #(.width(32)) comparator_148 (
    .a(multiplexer_145_out), .b({32{1'b1}}), .eq(comparator_148_eq));  // open: gt, lt
  or or_148 (or_148_out, comparator_148_eq, or_152_out);
  Register #(.width(32)) register_37 (.D(multiplexer_146_out), .Q(R37_2), .clk(save), .clr(clr));  // open: en
  or or_149 (or_149_out, comparator_151_eq, or_156_out);
  Multiplexer #(.width(32), .enable("false")) multiplexer_149 (
    .in0(R38), .in1(R37), .out(multiplexer_149_out), .sel(or_149_out));
  or or_150 (or_150_out, comparator_152_eq, or_153_out);
  Multiplexer #(.width(32), .enable("false")) multiplexer_150 (
    .in0(multiplexer_149_out), .in1(multiplexer_147_out), .out(multiplexer_150_out), .sel(or_150_out));
  Comparator #(.width(32)) comparator_149 (
    .a(multiplexer_150_out), .b({32{1'b1}}), .eq(comparator_149_eq));  // open: gt, lt
  or or_151 (or_151_out, comparator_149_eq, or_154_out);
  Multiplexer #(.width(32), .enable("false")) multiplexer_151 (
    .in0(multiplexer_150_out), .in1(multiplexer_148_out), .out(multiplexer_151_out), .sel(or_151_out));
  Comparator #(.width(32)) comparator_150 (
    .a(multiplexer_151_out), .b({32{1'b1}}), .eq(comparator_150_eq));  // open: gt, lt
  or or_152 (or_152_out, comparator_150_eq, or_155_out);
  Multiplexer #(.width(32), .enable("false")) multiplexer_152 (
    .in0(multiplexer_151_out), .in1(multiplexer_145_out), .out(multiplexer_152_out), .sel(or_152_out));
  Register #(.width(32)) register_38 (.D(multiplexer_152_out), .Q(R38_2), .clk(save), .clr(clr));  // open: en
  Comparator #(.width(32)) comparator_151 (.a(R38), .b({32{1'b1}}), .eq(comparator_151_eq));  // open: gt, lt
  Multiplexer #(.width(32), .enable("false")) multiplexer_153 (
    .in0(R39), .in1(R38), .out(multiplexer_153_out), .sel(or_156_out));
  Comparator #(.width(32)) comparator_152 (
    .a(multiplexer_149_out), .b({32{1'b1}}), .eq(comparator_152_eq));  // open: gt, lt
  or or_153 (or_153_out, comparator_154_eq, or_159_out);
  Multiplexer #(.width(32), .enable("false")) multiplexer_154 (
    .in0(multiplexer_153_out), .in1(multiplexer_149_out), .out(multiplexer_154_out), .sel(or_153_out));
  or or_154 (or_154_out, comparator_155_eq, or_160_out);
  Multiplexer #(.width(32), .enable("false")) multiplexer_155 (
    .in0(multiplexer_154_out), .in1(multiplexer_150_out), .out(multiplexer_155_out), .sel(or_154_out));
  or or_155 (or_155_out, comparator_156_eq, or_157_out);
  Multiplexer #(.width(32), .enable("false")) multiplexer_156 (
    .in0(multiplexer_155_out), .in1(multiplexer_151_out), .out(multiplexer_156_out), .sel(or_155_out));
  Register #(.width(32)) register_39 (.D(multiplexer_156_out), .Q(R39_2), .clk(save), .clr(clr));  // open: en
  Comparator #(.width(32)) comparator_153 (.a(R39), .b({32{1'b1}}), .eq(comparator_153_eq));  // open: gt, lt
  or or_156 (or_156_out, comparator_153_eq, or_158_out);
  Multiplexer #(.width(32), .enable("false")) multiplexer_157 (
    .in0(R40), .in1(R39), .out(multiplexer_157_out), .sel(or_158_out));
  Comparator #(.width(32)) comparator_154 (
    .a(multiplexer_153_out), .b({32{1'b1}}), .eq(comparator_154_eq));  // open: gt, lt
  Multiplexer #(.width(32), .enable("false")) multiplexer_158 (
    .in0(multiplexer_157_out), .in1(multiplexer_153_out), .out(multiplexer_158_out), .sel(or_159_out));
  Comparator #(.width(32)) comparator_155 (
    .a(multiplexer_154_out), .b({32{1'b1}}), .eq(comparator_155_eq));  // open: gt, lt
  Multiplexer #(.width(32), .enable("false")) multiplexer_159 (
    .in0(multiplexer_158_out), .in1(multiplexer_154_out), .out(multiplexer_159_out), .sel(or_160_out));
  Comparator #(.width(32)) comparator_156 (
    .a(multiplexer_155_out), .b({32{1'b1}}), .eq(comparator_156_eq));  // open: gt, lt
  or or_157 (or_157_out, comparator_160_eq, or_164_out);
  Multiplexer #(.width(32), .enable("false")) multiplexer_160 (
    .in0(multiplexer_159_out), .in1(multiplexer_155_out), .out(multiplexer_160_out), .sel(or_157_out));
  Comparator #(.width(32)) comparator_157 (.a(R40), .b({32{1'b1}}), .eq(comparator_157_eq));  // open: gt, lt
  or or_158 (or_158_out, comparator_157_eq, or_161_out);
  Comparator #(.width(32)) comparator_158 (
    .a(multiplexer_157_out), .b({32{1'b1}}), .eq(comparator_158_eq));  // open: gt, lt
  or or_159 (or_159_out, comparator_158_eq, or_162_out);
  Comparator #(.width(32)) comparator_159 (
    .a(multiplexer_158_out), .b({32{1'b1}}), .eq(comparator_159_eq));  // open: gt, lt
  or or_160 (or_160_out, comparator_159_eq, or_163_out);
  Multiplexer #(.width(32), .enable("false")) multiplexer_161 (
    .in0(multiplexer_164_out), .in1(multiplexer_158_out), .out(multiplexer_161_out), .sel(or_163_out));
  Comparator #(.width(32)) comparator_160 (
    .a(multiplexer_159_out), .b({32{1'b1}}), .eq(comparator_160_eq));  // open: gt, lt
  Multiplexer #(.width(32), .enable("false")) multiplexer_162 (
    .in0(multiplexer_161_out), .in1(multiplexer_159_out), .out(multiplexer_162_out), .sel(or_164_out));
  Register #(.width(32)) register_40 (.D(multiplexer_160_out), .Q(R40_2), .clk(save), .clr(clr));  // open: en
  Comparator #(.width(32)) comparator_161 (.a(R41), .b({32{1'b1}}), .eq(comparator_161_eq));  // open: gt, lt
  or or_161 (or_161_out, comparator_161_eq, or_165_out);
  Multiplexer #(.width(32), .enable("false")) multiplexer_163 (
    .in0(R41), .in1(R40), .out(multiplexer_163_out), .sel(or_161_out));
  Comparator #(.width(32)) comparator_162 (
    .a(multiplexer_163_out), .b({32{1'b1}}), .eq(comparator_162_eq));  // open: gt, lt
  or or_162 (or_162_out, comparator_162_eq, or_166_out);
  Multiplexer #(.width(32), .enable("false")) multiplexer_164 (
    .in0(multiplexer_163_out), .in1(multiplexer_157_out), .out(multiplexer_164_out), .sel(or_162_out));
  Comparator #(.width(32)) comparator_163 (
    .a(multiplexer_164_out), .b({32{1'b1}}), .eq(comparator_163_eq));  // open: gt, lt
  or or_163 (or_163_out, comparator_163_eq, or_167_out);
  Comparator #(.width(32)) comparator_164 (
    .a(multiplexer_161_out), .b({32{1'b1}}), .eq(comparator_164_eq));  // open: gt, lt
  or or_164 (or_164_out, comparator_164_eq, or_168_out);
  Register #(.width(32)) register_41 (.D(multiplexer_162_out), .Q(R41_2), .clk(save), .clr(clr));  // open: en
  or or_165 (or_165_out, comparator_167_eq, or_172_out);
  Multiplexer #(.width(32), .enable("false")) multiplexer_165 (
    .in0(R42), .in1(R41), .out(multiplexer_165_out), .sel(or_165_out));
  or or_166 (or_166_out, comparator_168_eq, or_169_out);
  Multiplexer #(.width(32), .enable("false")) multiplexer_166 (
    .in0(multiplexer_165_out), .in1(multiplexer_163_out), .out(multiplexer_166_out), .sel(or_166_out));
  Comparator #(.width(32)) comparator_165 (
    .a(multiplexer_166_out), .b({32{1'b1}}), .eq(comparator_165_eq));  // open: gt, lt
  or or_167 (or_167_out, comparator_165_eq, or_170_out);
  Multiplexer #(.width(32), .enable("false")) multiplexer_167 (
    .in0(multiplexer_166_out), .in1(multiplexer_164_out), .out(multiplexer_167_out), .sel(or_167_out));
  Comparator #(.width(32)) comparator_166 (
    .a(multiplexer_167_out), .b({32{1'b1}}), .eq(comparator_166_eq));  // open: gt, lt
  or or_168 (or_168_out, comparator_166_eq, or_171_out);
  Multiplexer #(.width(32), .enable("false")) multiplexer_168 (
    .in0(multiplexer_167_out), .in1(multiplexer_161_out), .out(multiplexer_168_out), .sel(or_168_out));
  Register #(.width(32)) register_42 (.D(multiplexer_168_out), .Q(R42_2), .clk(save), .clr(clr));  // open: en
  Comparator #(.width(32)) comparator_167 (.a(R42), .b({32{1'b1}}), .eq(comparator_167_eq));  // open: gt, lt
  Multiplexer #(.width(32), .enable("false")) multiplexer_169 (
    .in0(R43), .in1(R42), .out(multiplexer_169_out), .sel(or_172_out));
  Comparator #(.width(32)) comparator_168 (
    .a(multiplexer_165_out), .b({32{1'b1}}), .eq(comparator_168_eq));  // open: gt, lt
  or or_169 (or_169_out, comparator_170_eq, or_175_out);
  Multiplexer #(.width(32), .enable("false")) multiplexer_170 (
    .in0(multiplexer_169_out), .in1(multiplexer_165_out), .out(multiplexer_170_out), .sel(or_169_out));
  or or_170 (or_170_out, comparator_171_eq, or_176_out);
  Multiplexer #(.width(32), .enable("false")) multiplexer_171 (
    .in0(multiplexer_170_out), .in1(multiplexer_166_out), .out(multiplexer_171_out), .sel(or_170_out));
  or or_171 (or_171_out, comparator_172_eq, or_173_out);
  Multiplexer #(.width(32), .enable("false")) multiplexer_172 (
    .in0(multiplexer_171_out), .in1(multiplexer_167_out), .out(multiplexer_172_out), .sel(or_171_out));
  Register #(.width(32)) register_43 (.D(multiplexer_172_out), .Q(R43_2), .clk(save), .clr(clr));  // open: en
  Comparator #(.width(32)) comparator_169 (.a(R43), .b({32{1'b1}}), .eq(comparator_169_eq));  // open: gt, lt
  or or_172 (or_172_out, comparator_169_eq, or_174_out);
  Multiplexer #(.width(32), .enable("false")) multiplexer_173 (
    .in0(R44), .in1(R43), .out(multiplexer_173_out), .sel(or_174_out));
  Comparator #(.width(32)) comparator_170 (
    .a(multiplexer_169_out), .b({32{1'b1}}), .eq(comparator_170_eq));  // open: gt, lt
  Multiplexer #(.width(32), .enable("false")) multiplexer_174 (
    .in0(multiplexer_173_out), .in1(multiplexer_169_out), .out(multiplexer_174_out), .sel(or_175_out));
  Comparator #(.width(32)) comparator_171 (
    .a(multiplexer_170_out), .b({32{1'b1}}), .eq(comparator_171_eq));  // open: gt, lt
  Multiplexer #(.width(32), .enable("false")) multiplexer_175 (
    .in0(multiplexer_174_out), .in1(multiplexer_170_out), .out(multiplexer_175_out), .sel(or_176_out));
  Comparator #(.width(32)) comparator_172 (
    .a(multiplexer_171_out), .b({32{1'b1}}), .eq(comparator_172_eq));  // open: gt, lt
  or or_173 (or_173_out, comparator_176_eq, or_180_out);
  Multiplexer #(.width(32), .enable("false")) multiplexer_176 (
    .in0(multiplexer_175_out), .in1(multiplexer_171_out), .out(multiplexer_176_out), .sel(or_173_out));
  Comparator #(.width(32)) comparator_173 (.a(R44), .b({32{1'b1}}), .eq(comparator_173_eq));  // open: gt, lt
  or or_174 (or_174_out, comparator_173_eq, or_177_out);
  Comparator #(.width(32)) comparator_174 (
    .a(multiplexer_173_out), .b({32{1'b1}}), .eq(comparator_174_eq));  // open: gt, lt
  or or_175 (or_175_out, comparator_174_eq, or_178_out);
  Comparator #(.width(32)) comparator_175 (
    .a(multiplexer_174_out), .b({32{1'b1}}), .eq(comparator_175_eq));  // open: gt, lt
  or or_176 (or_176_out, comparator_175_eq, or_179_out);
  Multiplexer #(.width(32), .enable("false")) multiplexer_177 (
    .in0(multiplexer_180_out), .in1(multiplexer_174_out), .out(multiplexer_177_out), .sel(or_179_out));
  Comparator #(.width(32)) comparator_176 (
    .a(multiplexer_175_out), .b({32{1'b1}}), .eq(comparator_176_eq));  // open: gt, lt
  Multiplexer #(.width(32), .enable("false")) multiplexer_178 (
    .in0(multiplexer_177_out), .in1(multiplexer_175_out), .out(multiplexer_178_out), .sel(or_180_out));
  Register #(.width(32)) register_44 (.D(multiplexer_176_out), .Q(R44_2), .clk(save), .clr(clr));  // open: en
  Comparator #(.width(32)) comparator_177 (.a(R45), .b({32{1'b1}}), .eq(comparator_177_eq));  // open: gt, lt
  or or_177 (or_177_out, comparator_177_eq, or_181_out);
  Multiplexer #(.width(32), .enable("false")) multiplexer_179 (
    .in0(R45), .in1(R44), .out(multiplexer_179_out), .sel(or_177_out));
  Comparator #(.width(32)) comparator_178 (
    .a(multiplexer_179_out), .b({32{1'b1}}), .eq(comparator_178_eq));  // open: gt, lt
  or or_178 (or_178_out, comparator_178_eq, or_182_out);
  Multiplexer #(.width(32), .enable("false")) multiplexer_180 (
    .in0(multiplexer_179_out), .in1(multiplexer_173_out), .out(multiplexer_180_out), .sel(or_178_out));
  Comparator #(.width(32)) comparator_179 (
    .a(multiplexer_180_out), .b({32{1'b1}}), .eq(comparator_179_eq));  // open: gt, lt
  or or_179 (or_179_out, comparator_179_eq, or_183_out);
  Comparator #(.width(32)) comparator_180 (
    .a(multiplexer_177_out), .b({32{1'b1}}), .eq(comparator_180_eq));  // open: gt, lt
  or or_180 (or_180_out, comparator_180_eq, or_184_out);
  Register #(.width(32)) register_45 (.D(multiplexer_178_out), .Q(R45_2), .clk(save), .clr(clr));  // open: en
  or or_181 (or_181_out, comparator_183_eq, or_188_out);
  Multiplexer #(.width(32), .enable("false")) multiplexer_181 (
    .in0(R46), .in1(R45), .out(multiplexer_181_out), .sel(or_181_out));
  or or_182 (or_182_out, comparator_184_eq, or_185_out);
  Multiplexer #(.width(32), .enable("false")) multiplexer_182 (
    .in0(multiplexer_181_out), .in1(multiplexer_179_out), .out(multiplexer_182_out), .sel(or_182_out));
  Comparator #(.width(32)) comparator_181 (
    .a(multiplexer_182_out), .b({32{1'b1}}), .eq(comparator_181_eq));  // open: gt, lt
  or or_183 (or_183_out, comparator_181_eq, or_186_out);
  Multiplexer #(.width(32), .enable("false")) multiplexer_183 (
    .in0(multiplexer_182_out), .in1(multiplexer_180_out), .out(multiplexer_183_out), .sel(or_183_out));
  Comparator #(.width(32)) comparator_182 (
    .a(multiplexer_183_out), .b({32{1'b1}}), .eq(comparator_182_eq));  // open: gt, lt
  or or_184 (or_184_out, comparator_182_eq, or_187_out);
  Multiplexer #(.width(32), .enable("false")) multiplexer_184 (
    .in0(multiplexer_183_out), .in1(multiplexer_177_out), .out(multiplexer_184_out), .sel(or_184_out));
  Register #(.width(32)) register_46 (.D(multiplexer_184_out), .Q(R46_2), .clk(save), .clr(clr));  // open: en
  Comparator #(.width(32)) comparator_183 (.a(R46), .b({32{1'b1}}), .eq(comparator_183_eq));  // open: gt, lt
  Multiplexer #(.width(32), .enable("false")) multiplexer_185 (
    .in0(R47), .in1(R46), .out(multiplexer_185_out), .sel(or_188_out));
  Comparator #(.width(32)) comparator_184 (
    .a(multiplexer_181_out), .b({32{1'b1}}), .eq(comparator_184_eq));  // open: gt, lt
  or or_185 (or_185_out, comparator_186_eq, comparator_190_eq);
  Multiplexer #(.width(32), .enable("false")) multiplexer_186 (
    .in0(multiplexer_185_out), .in1(multiplexer_181_out), .out(multiplexer_186_out), .sel(or_185_out));
  or or_186 (or_186_out, comparator_187_eq, comparator_191_eq);
  Multiplexer #(.width(32), .enable("false")) multiplexer_187 (
    .in0(multiplexer_186_out), .in1(multiplexer_182_out), .out(multiplexer_187_out), .sel(or_186_out));
  or or_187 (or_187_out, comparator_188_eq, comparator_192_eq);
  Multiplexer #(.width(32), .enable("false")) multiplexer_188 (
    .in0(multiplexer_187_out), .in1(multiplexer_183_out), .out(multiplexer_188_out), .sel(or_187_out));
  Register #(.width(32)) register_47 (.D(multiplexer_188_out), .Q(R47_2), .clk(save), .clr(clr));  // open: en
  Comparator #(.width(32)) comparator_185 (.a(R47), .b({32{1'b1}}), .eq(comparator_185_eq));  // open: gt, lt
  or or_188 (or_188_out, comparator_185_eq, comparator_189_eq);
  Multiplexer #(.width(32), .enable("false")) multiplexer_189 (
    .in0(R48), .in1(R47), .out(multiplexer_189_out), .sel(comparator_189_eq));
  Comparator #(.width(32)) comparator_186 (
    .a(multiplexer_185_out), .b({32{1'b1}}), .eq(comparator_186_eq));  // open: gt, lt
  Multiplexer #(.width(32), .enable("false")) multiplexer_190 (
    .in0(multiplexer_189_out), .in1(multiplexer_185_out), .out(multiplexer_190_out), .sel(comparator_190_eq));
  Comparator #(.width(32)) comparator_187 (
    .a(multiplexer_186_out), .b({32{1'b1}}), .eq(comparator_187_eq));  // open: gt, lt
  Multiplexer #(.width(32), .enable("false")) multiplexer_191 (
    .in0(multiplexer_190_out), .in1(multiplexer_186_out), .out(multiplexer_191_out), .sel(comparator_191_eq));
  Comparator #(.width(32)) comparator_188 (
    .a(multiplexer_187_out), .b({32{1'b1}}), .eq(comparator_188_eq));  // open: gt, lt
  Multiplexer #(.width(32), .enable("false")) multiplexer_192 (
    .in0(multiplexer_191_out), .in1(multiplexer_187_out), .out(multiplexer_192_out), .sel(comparator_192_eq));
  Comparator #(.width(32)) comparator_189 (.a(R48), .b({32{1'b1}}), .eq(comparator_189_eq));  // open: gt, lt
  Comparator #(.width(32)) comparator_190 (
    .a(multiplexer_189_out), .b({32{1'b1}}), .eq(comparator_190_eq));  // open: gt, lt
  Comparator #(.width(32)) comparator_191 (
    .a(multiplexer_190_out), .b({32{1'b1}}), .eq(comparator_191_eq));  // open: gt, lt
  Comparator #(.width(32)) comparator_192 (
    .a(multiplexer_191_out), .b({32{1'b1}}), .eq(comparator_192_eq));  // open: gt, lt
  Register #(.width(32)) register_48 (.D(multiplexer_192_out), .Q(R48_2), .clk(save), .clr(clr));  // open: en
endmodule
